// Logisim project cpu21-riscv-6(多级中断).circ as structural Verilog: 13 circuits, main circuit ◇单周期RISC-V
module \单周期RISC_V  (
);


  // Notes on the sheet:
  //   本文件仅包含多级中断电路
  //   请见cpu21-riscv-1(单周期CCAB).circ的“单周期RISC-V”
endmodule

// 单周期硬布线控制器
module \单周期硬布线控制器  (
  input  [4:0] OP,
  input  [4:0] Funct,
  input  in_3,
  output [3:0] ALU_OP,
  output uret,
  output MemToReg,
  output ecall,
  output MemWrite,
  output ALU_SRC,
  output RegWrite,
  output S_type,
  output Beq,
  output Bne,
  output Jalr,
  output JAL,
  output CSRRSI,
  output CSRRCI
);

  wire \控制信号自动生成_1_ecall ;

  \运算控制器自动生成  \u_运算控制器自动生成_1  (
    .OP2(OP[0]), .OP3(OP[1]), .OP4(OP[2]), .OP5(OP[3]), .OP6(OP[4]), .F12(Funct[0]), .F13(Funct[1]),
    .F14(Funct[2]), .F25(Funct[3]), .F30(Funct[4]), .S0(ALU_OP[0]), .S1(ALU_OP[1]), .S2(ALU_OP[2]),
    .S3(ALU_OP[3]));
  \控制信号自动生成  \u_控制信号自动生成_1  (
    .OP2(OP[0]), .OP3(OP[1]), .OP4(OP[2]), .OP5(OP[3]), .OP6(OP[4]), .MemToReg(MemToReg), .F12(Funct[0]),
    .F13(Funct[1]), .F14(Funct[2]), .F25(Funct[3]), .F30(Funct[4]), .MemWrite(MemWrite), .ALU_SRC(ALU_SRC),
    .RegWrite(RegWrite), .ecall(\控制信号自动生成_1_ecall ), .S_Type(S_type), .BEQ(Beq), .BNE(Bne), .JALR(Jalr),
    .JAL(JAL), .CSRRSI(CSRRSI), .CSRRCI(CSRRCI));  // open: CSRRW
  and and_1 (uret, in_3, \控制信号自动生成_1_ecall );
  and and_2 (ecall, ~in_3, \控制信号自动生成_1_ecall );  // AND_Gate

  // Other names for the same wires on the sheet: IR21 = in_3; OP_CODE[4:0] = OP

  // Notes on the sheet:
  //   运算器控制器，根据指令生成运算器功能选择信号
  //   控制信号生成，产生数据通路需要的其他控制信号
endmodule

// 运算器控制器
module \运算控制器自动生成  (
  input  OP2,
  input  OP3,
  input  OP4,
  input  OP5,
  input  OP6,
  input  F12,
  input  F13,
  input  F14,
  input  F25,
  input  F30,
  output S0,
  output S1,
  output S2,
  output S3
);

  wire and_1_out, and_2_out, and_3_out, and_4_out, and_5_out, and_6_out, and_7_out, and_8_out, and_9_out,
       and_10_out, and_11_out, and_12_out, and_13_out, and_14_out, and_15_out, and_16_out, and_17_out,
       and_18_out, and_19_out, and_20_out, and_21_out, and_22_out, and_23_out, and_24_out, and_25_out,
       and_26_out, and_27_out, and_28_out, and_29_out, and_30_out, and_31_out, and_32_out, and_33_out,
       and_34_out, not_1_out, not_2_out, not_3_out, not_4_out, not_5_out, not_6_out, not_7_out, not_8_out,
       not_9_out, not_10_out, not_11_out, not_12_out, not_13_out, not_14_out, not_15_out, not_16_out,
       not_17_out, not_18_out, not_19_out, not_20_out, not_21_out, not_22_out, not_23_out, not_24_out,
       not_25_out, not_26_out, not_27_out, not_28_out, not_29_out, not_30_out, not_31_out, not_32_out,
       not_33_out, not_34_out, not_35_out, not_36_out, not_37_out, not_38_out, not_39_out, not_40_out,
       not_41_out, not_42_out, not_43_out, not_44_out, not_45_out, not_46_out, not_47_out, not_48_out,
       not_49_out, not_50_out, not_51_out, not_52_out, not_53_out, not_54_out, not_55_out, not_56_out,
       not_57_out, not_58_out, not_59_out, not_60_out, not_61_out, not_62_out, not_63_out, not_64_out,
       not_65_out, not_66_out, not_67_out, not_68_out, not_69_out, not_70_out, not_71_out, not_72_out,
       not_73_out, not_74_out, not_75_out, not_76_out, not_77_out, not_78_out, not_79_out, not_80_out,
       not_81_out, not_82_out, not_83_out, not_84_out, not_85_out, not_86_out, not_87_out, not_88_out,
       not_89_out, not_90_out, not_91_out, not_92_out, not_93_out, not_94_out, not_95_out, not_96_out,
       not_97_out, not_98_out, not_99_out, not_100_out, not_101_out, not_102_out, not_103_out, not_104_out,
       not_105_out, not_106_out, not_107_out, not_108_out, not_109_out, not_110_out, not_111_out,
       not_112_out, not_113_out, not_114_out, not_115_out, not_116_out, not_117_out, not_118_out,
       not_119_out, not_120_out, not_121_out, not_122_out, not_123_out, not_124_out, not_125_out,
       not_126_out, not_127_out, not_128_out, not_129_out, not_130_out, not_131_out, not_132_out,
       not_133_out, not_134_out, not_135_out, not_136_out, not_137_out, not_138_out, not_139_out,
       not_140_out, not_141_out, not_142_out, not_143_out, not_144_out, not_145_out, not_146_out,
       not_147_out, not_148_out, not_149_out, not_150_out, not_151_out, not_152_out, not_153_out,
       not_154_out, not_155_out, not_156_out, not_157_out, not_158_out, not_159_out, not_160_out,
       not_161_out, not_162_out, not_163_out, not_164_out, not_165_out, not_166_out, not_167_out,
       not_168_out, not_169_out, not_170_out, not_171_out, not_172_out, not_173_out, not_174_out,
       not_175_out, not_176_out, not_177_out, not_178_out, not_179_out, not_180_out, not_181_out,
       not_182_out, not_183_out, not_184_out, not_185_out, not_186_out, not_187_out, not_188_out, not_189_out;

  not not_1 (not_1_out, F30);
  not not_2 (not_2_out, F25);
  not not_3 (not_3_out, F14);
  not not_4 (not_4_out, F13);
  not not_5 (not_5_out, F12);
  not not_6 (not_6_out, OP6);
  not not_7 (not_7_out, OP3);
  not not_8 (not_8_out, OP2);
  not not_9 (not_9_out, F30);
  not not_10 (not_10_out, F25);
  not not_11 (not_11_out, OP6);
  not not_12 (not_12_out, OP3);
  not not_13 (not_13_out, OP2);
  not not_14 (not_14_out, F30);
  not not_15 (not_15_out, F25);
  not not_16 (not_16_out, F14);
  not not_17 (not_17_out, F12);
  not not_18 (not_18_out, OP6);
  not not_19 (not_19_out, OP3);
  not not_20 (not_20_out, OP2);
  not not_21 (not_21_out, F14);
  not not_22 (not_22_out, F13);
  not not_23 (not_23_out, F12);
  not not_24 (not_24_out, OP6);
  not not_25 (not_25_out, OP5);
  not not_26 (not_26_out, OP3);
  not not_27 (not_27_out, OP2);
  not not_28 (not_28_out, OP6);
  not not_29 (not_29_out, OP5);
  not not_30 (not_30_out, OP3);
  not not_31 (not_31_out, OP2);
  not not_32 (not_32_out, F13);
  not not_33 (not_33_out, F12);
  not not_34 (not_34_out, OP6);
  not not_35 (not_35_out, OP5);
  not not_36 (not_36_out, OP3);
  not not_37 (not_37_out, OP2);
  not not_38 (not_38_out, F14);
  not not_39 (not_39_out, F12);
  not not_40 (not_40_out, OP6);
  not not_41 (not_41_out, OP5);
  not not_42 (not_42_out, OP3);
  not not_43 (not_43_out, OP2);
  not not_44 (not_44_out, F25);
  not not_45 (not_45_out, F13);
  not not_46 (not_46_out, OP6);
  not not_47 (not_47_out, OP5);
  not not_48 (not_48_out, OP3);
  not not_49 (not_49_out, OP2);
  not not_50 (not_50_out, OP3);
  not not_51 (not_51_out, OP2);
  not not_52 (not_52_out, F25);
  not not_53 (not_53_out, F14);
  not not_54 (not_54_out, F13);
  not not_55 (not_55_out, F12);
  not not_56 (not_56_out, OP6);
  not not_57 (not_57_out, OP3);
  not not_58 (not_58_out, OP2);
  not not_59 (not_59_out, F30);
  not not_60 (not_60_out, F25);
  not not_61 (not_61_out, OP6);
  not not_62 (not_62_out, OP3);
  not not_63 (not_63_out, OP2);
  not not_64 (not_64_out, F30);
  not not_65 (not_65_out, F25);
  not not_66 (not_66_out, F14);
  not not_67 (not_67_out, F12);
  not not_68 (not_68_out, OP6);
  not not_69 (not_69_out, OP3);
  not not_70 (not_70_out, OP2);
  not not_71 (not_71_out, OP6);
  not not_72 (not_72_out, OP5);
  not not_73 (not_73_out, OP3);
  not not_74 (not_74_out, OP2);
  not not_75 (not_75_out, F14);
  not not_76 (not_76_out, F12);
  not not_77 (not_77_out, OP6);
  not not_78 (not_78_out, OP5);
  not not_79 (not_79_out, OP3);
  not not_80 (not_80_out, OP2);
  not not_81 (not_81_out, F30);
  not not_82 (not_82_out, F25);
  not not_83 (not_83_out, F13);
  not not_84 (not_84_out, OP6);
  not not_85 (not_85_out, OP5);
  not not_86 (not_86_out, OP3);
  not not_87 (not_87_out, OP2);
  not not_88 (not_88_out, F14);
  not not_89 (not_89_out, F13);
  not not_90 (not_90_out, F12);
  not not_91 (not_91_out, OP4);
  not not_92 (not_92_out, OP3);
  not not_93 (not_93_out, OP2);
  not not_94 (not_94_out, F14);
  not not_95 (not_95_out, F13);
  not not_96 (not_96_out, OP4);
  not not_97 (not_97_out, OP3);
  not not_98 (not_98_out, OP2);
  not not_99 (not_99_out, OP3);
  not not_100 (not_100_out, OP2);
  not not_101 (not_101_out, F30);
  not not_102 (not_102_out, F25);
  not not_103 (not_103_out, F14);
  not not_104 (not_104_out, F13);
  not not_105 (not_105_out, F12);
  not not_106 (not_106_out, OP6);
  not not_107 (not_107_out, OP3);
  not not_108 (not_108_out, OP2);
  not not_109 (not_109_out, F25);
  not not_110 (not_110_out, F14);
  not not_111 (not_111_out, F13);
  not not_112 (not_112_out, F12);
  not not_113 (not_113_out, OP6);
  not not_114 (not_114_out, OP3);
  not not_115 (not_115_out, OP2);
  not not_116 (not_116_out, F30);
  not not_117 (not_117_out, F25);
  not not_118 (not_118_out, OP6);
  not not_119 (not_119_out, OP3);
  not not_120 (not_120_out, OP2);
  not not_121 (not_121_out, F30);
  not not_122 (not_122_out, F25);
  not not_123 (not_123_out, F14);
  not not_124 (not_124_out, OP6);
  not not_125 (not_125_out, OP3);
  not not_126 (not_126_out, OP2);
  not not_127 (not_127_out, F14);
  not not_128 (not_128_out, F13);
  not not_129 (not_129_out, F12);
  not not_130 (not_130_out, OP6);
  not not_131 (not_131_out, OP5);
  not not_132 (not_132_out, OP3);
  not not_133 (not_133_out, OP2);
  not not_134 (not_134_out, OP6);
  not not_135 (not_135_out, OP5);
  not not_136 (not_136_out, OP3);
  not not_137 (not_137_out, OP2);
  not not_138 (not_138_out, F14);
  not not_139 (not_139_out, F13);
  not not_140 (not_140_out, F12);
  not not_141 (not_141_out, OP4);
  not not_142 (not_142_out, OP3);
  not not_143 (not_143_out, OP2);
  not not_144 (not_144_out, F14);
  not not_145 (not_145_out, F13);
  not not_146 (not_146_out, OP4);
  not not_147 (not_147_out, OP3);
  not not_148 (not_148_out, OP2);
  not not_149 (not_149_out, OP3);
  not not_150 (not_150_out, OP2);
  not not_151 (not_151_out, F30);
  not not_152 (not_152_out, F25);
  not not_153 (not_153_out, F12);
  not not_154 (not_154_out, OP6);
  not not_155 (not_155_out, OP3);
  not not_156 (not_156_out, OP2);
  not not_157 (not_157_out, F30);
  not not_158 (not_158_out, F25);
  not not_159 (not_159_out, F14);
  not not_160 (not_160_out, F12);
  not not_161 (not_161_out, OP6);
  not not_162 (not_162_out, OP3);
  not not_163 (not_163_out, OP2);
  not not_164 (not_164_out, F30);
  not not_165 (not_165_out, F25);
  not not_166 (not_166_out, F14);
  not not_167 (not_167_out, OP6);
  not not_168 (not_168_out, OP3);
  not not_169 (not_169_out, OP2);
  not not_170 (not_170_out, F12);
  not not_171 (not_171_out, OP6);
  not not_172 (not_172_out, OP5);
  not not_173 (not_173_out, OP3);
  not not_174 (not_174_out, OP2);
  not not_175 (not_175_out, F13);
  not not_176 (not_176_out, F12);
  not not_177 (not_177_out, OP6);
  not not_178 (not_178_out, OP5);
  not not_179 (not_179_out, OP3);
  not not_180 (not_180_out, OP2);
  not not_181 (not_181_out, F14);
  not not_182 (not_182_out, F12);
  not not_183 (not_183_out, OP6);
  not not_184 (not_184_out, OP5);
  not not_185 (not_185_out, OP3);
  not not_186 (not_186_out, OP2);
  not not_187 (not_187_out, F12);
  not not_188 (not_188_out, OP3);
  not not_189 (not_189_out, OP2);
  and and_1 (and_1_out, not_1_out, not_2_out, not_3_out, not_4_out, not_5_out, not_6_out, OP5, OP4, not_7_out, not_8_out);
  and and_2 (and_2_out, not_9_out, not_10_out, F14, F13, F12, not_11_out, OP5, OP4, not_12_out, not_13_out);
  and and_3 (and_3_out, not_14_out, not_15_out, not_16_out, F13, not_17_out, not_18_out, OP5, OP4, not_19_out, not_20_out);
  and and_4 (and_4_out, not_21_out, not_22_out, not_23_out, not_24_out, not_25_out, OP4, not_26_out, not_27_out);
  and and_5 (and_5_out, F14, F13, F12, not_28_out, not_29_out, OP4, not_30_out, not_31_out);
  and and_6 (and_6_out, F14, not_32_out, not_33_out, not_34_out, not_35_out, OP4, not_36_out, not_37_out);
  and and_7 (and_7_out, not_38_out, F13, not_39_out, not_40_out, not_41_out, OP4, not_42_out, not_43_out);
  and and_8 (and_8_out, F30, not_44_out, F14, not_45_out, F12, not_46_out, not_47_out, OP4, not_48_out, not_49_out);
  and and_9 (and_9_out, F14, F13, F12, OP6, OP5, OP4, not_50_out, not_51_out);
  and and_10 (and_10_out, F30, not_52_out, not_53_out, not_54_out, not_55_out, not_56_out, OP5, OP4, not_57_out, not_58_out);
  and and_11 (and_11_out, not_59_out, not_60_out, F14, F13, F12, not_61_out, OP5, OP4, not_62_out, not_63_out);
  and and_12 (and_12_out, not_64_out, not_65_out, not_66_out, F13, not_67_out, not_68_out, OP5, OP4, not_69_out, not_70_out);
  and and_13 (and_13_out, F14, F13, F12, not_71_out, not_72_out, OP4, not_73_out, not_74_out);
  and and_14 (and_14_out, not_75_out, F13, not_76_out, not_77_out, not_78_out, OP4, not_79_out, not_80_out);
  and and_15 (and_15_out, not_81_out, not_82_out, F14, not_83_out, F12, not_84_out, not_85_out, OP4, not_86_out, not_87_out);
  and and_16 (and_16_out, not_88_out, not_89_out, not_90_out, OP6, OP5, not_91_out, not_92_out, not_93_out);
  and and_17 (and_17_out, not_94_out, not_95_out, F12, OP6, OP5, not_96_out, not_97_out, not_98_out);
  and and_18 (and_18_out, F14, F13, F12, OP6, OP5, OP4, not_99_out, not_100_out);
  and and_19 (and_19_out, not_101_out, not_102_out, not_103_out, not_104_out, not_105_out, not_106_out, OP5, OP4, not_107_out, not_108_out);
  and and_20 (and_20_out, F30, not_109_out, not_110_out, not_111_out, not_112_out, not_113_out, OP5, OP4, not_114_out, not_115_out);
  and and_21 (and_21_out, not_116_out, not_117_out, F14, F13, F12, not_118_out, OP5, OP4, not_119_out, not_120_out);
  and and_22 (and_22_out, not_121_out, not_122_out, not_123_out, F13, F12, not_124_out, OP5, OP4, not_125_out, not_126_out);
  and and_23 (and_23_out, not_127_out, not_128_out, not_129_out, not_130_out, not_131_out, OP4, not_132_out, not_133_out);
  and and_24 (and_24_out, F14, F13, F12, not_134_out, not_135_out, OP4, not_136_out, not_137_out);
  and and_25 (and_25_out, not_138_out, not_139_out, not_140_out, OP6, OP5, not_141_out, not_142_out, not_143_out);
  and and_26 (and_26_out, not_144_out, not_145_out, F12, OP6, OP5, not_146_out, not_147_out, not_148_out);
  and and_27 (and_27_out, F14, F13, F12, OP6, OP5, OP4, not_149_out, not_150_out);
  and and_28 (and_28_out, not_151_out, not_152_out, F14, F13, not_153_out, not_154_out, OP5, OP4, not_155_out, not_156_out);
  and and_29 (and_29_out, not_157_out, not_158_out, not_159_out, F13, not_160_out, not_161_out, OP5, OP4, not_162_out, not_163_out);
  and and_30 (and_30_out, not_164_out, not_165_out, not_166_out, F13, F12, not_167_out, OP5, OP4, not_168_out, not_169_out);
  and and_31 (and_31_out, F14, F13, not_170_out, not_171_out, not_172_out, OP4, not_173_out, not_174_out);
  and and_32 (and_32_out, F14, not_175_out, not_176_out, not_177_out, not_178_out, OP4, not_179_out, not_180_out);
  and and_33 (and_33_out, not_181_out, F13, not_182_out, not_183_out, not_184_out, OP4, not_185_out, not_186_out);
  and and_34 (and_34_out, F14, F13, not_187_out, OP6, OP5, OP4, not_188_out, not_189_out);
  or or_1 (S0, and_1_out, and_2_out, and_3_out, and_4_out, and_5_out, and_6_out, and_7_out, and_8_out, and_9_out);
  or or_2 (S1, and_10_out, and_11_out, and_12_out, and_13_out, and_14_out, and_15_out, and_16_out, and_17_out, and_18_out);
  or or_3 (S2, and_19_out, and_20_out, and_21_out, and_22_out, and_23_out, and_24_out, and_25_out, and_26_out, and_27_out);
  or or_4 (S3, and_28_out, and_29_out, and_30_out, and_31_out, and_32_out, and_33_out, and_34_out);
endmodule

// 控制信号生成
module \控制信号自动生成  (
  input  OP2,
  input  OP3,
  input  OP4,
  input  OP5,
  input  OP6,
  input  F12,
  input  F13,
  input  F14,
  input  F25,
  input  F30,
  output MemToReg,
  output MemWrite,
  output ALU_SRC,
  output RegWrite,
  output ecall,
  output S_Type,
  output BEQ,
  output BNE,
  output JALR,
  output JAL,
  output CSRRSI,
  output CSRRCI,
  output CSRRW
);

  wire and_1_out, and_2_out, and_4_out, and_5_out, and_6_out, and_7_out, and_8_out, and_9_out, and_10_out,
       and_11_out, and_12_out, and_13_out, and_14_out, and_15_out, and_16_out, and_17_out, and_18_out,
       and_19_out, and_20_out, and_21_out, and_22_out, and_23_out, not_1_out, not_2_out, not_3_out,
       not_4_out, not_5_out, not_6_out, not_7_out, not_8_out, not_9_out, not_10_out, not_11_out, not_12_out,
       not_13_out, not_14_out, not_15_out, not_16_out, not_17_out, not_18_out, not_19_out, not_20_out,
       not_21_out, not_22_out, not_23_out, not_24_out, not_25_out, not_26_out, not_27_out, not_28_out,
       not_29_out, not_30_out, not_31_out, not_32_out, not_33_out, not_34_out, not_35_out, not_36_out,
       not_37_out, not_38_out, not_39_out, not_40_out, not_41_out, not_42_out, not_43_out, not_44_out,
       not_45_out, not_46_out, not_47_out, not_48_out, not_49_out, not_50_out, not_51_out, not_52_out,
       not_53_out, not_54_out, not_55_out, not_56_out, not_57_out, not_58_out, not_59_out, not_60_out,
       not_61_out, not_62_out, not_63_out, not_64_out, not_65_out, not_66_out, not_67_out, not_68_out,
       not_69_out, not_70_out, not_71_out, not_72_out, not_73_out, not_74_out, not_75_out, not_76_out,
       not_77_out, not_78_out, not_79_out, not_80_out, not_81_out, not_82_out, not_83_out, not_84_out,
       not_85_out, not_86_out, not_87_out, not_88_out, not_89_out, not_90_out, not_91_out, not_92_out,
       not_93_out, not_94_out, not_95_out, not_96_out, not_97_out, not_98_out, not_99_out, not_100_out,
       not_101_out, not_102_out, not_103_out, not_104_out, not_105_out, not_106_out, not_107_out,
       not_108_out, not_109_out, not_110_out, not_111_out, not_112_out, not_113_out, not_114_out,
       not_115_out, not_116_out, not_117_out, not_118_out, not_119_out, not_120_out, not_121_out,
       not_122_out, not_123_out, not_124_out, not_125_out, not_126_out, not_127_out, not_128_out,
       not_129_out, not_130_out, not_131_out, not_132_out, not_133_out, not_134_out, not_135_out,
       not_136_out, not_137_out, not_138_out, not_139_out, not_140_out, not_141_out, not_142_out,
       not_143_out, not_144_out, not_145_out, not_146_out, not_147_out, not_148_out, not_149_out,
       not_150_out, not_151_out, not_152_out, not_153_out, not_154_out, not_155_out, not_156_out;

  not not_1 (not_1_out, OP2);
  not not_2 (not_2_out, OP3);
  not not_3 (not_3_out, OP4);
  not not_4 (not_4_out, OP5);
  not not_5 (not_5_out, OP6);
  not not_6 (not_6_out, F12);
  not not_7 (not_7_out, F14);
  not not_8 (not_8_out, F25);
  not not_9 (not_9_out, F30);
  not not_10 (not_10_out, OP2);
  not not_11 (not_11_out, OP3);
  not not_12 (not_12_out, OP4);
  not not_13 (not_13_out, OP5);
  not not_14 (not_14_out, OP6);
  not not_15 (not_15_out, F12);
  not not_16 (not_16_out, F14);
  not not_17 (not_17_out, OP2);
  not not_18 (not_18_out, OP3);
  not not_19 (not_19_out, OP4);
  not not_20 (not_20_out, OP6);
  not not_21 (not_21_out, F12);
  not not_22 (not_22_out, F14);
  not not_23 (not_23_out, OP2);
  not not_24 (not_24_out, OP3);
  not not_25 (not_25_out, OP5);
  not not_26 (not_26_out, OP6);
  not not_27 (not_27_out, F12);
  not not_28 (not_28_out, F14);
  not not_29 (not_29_out, F25);
  not not_30 (not_30_out, F30);
  not not_31 (not_31_out, OP2);
  not not_32 (not_32_out, OP3);
  not not_33 (not_33_out, OP4);
  not not_34 (not_34_out, OP6);
  not not_35 (not_35_out, F12);
  not not_36 (not_36_out, F14);
  not not_37 (not_37_out, OP2);
  not not_38 (not_38_out, OP3);
  not not_39 (not_39_out, OP5);
  not not_40 (not_40_out, OP6);
  not not_41 (not_41_out, F12);
  not not_42 (not_42_out, OP2);
  not not_43 (not_43_out, OP3);
  not not_44 (not_44_out, OP5);
  not not_45 (not_45_out, OP6);
  not not_46 (not_46_out, F13);
  not not_47 (not_47_out, F25);
  not not_48 (not_48_out, F30);
  not not_49 (not_49_out, OP2);
  not not_50 (not_50_out, OP3);
  not not_51 (not_51_out, OP5);
  not not_52 (not_52_out, OP6);
  not not_53 (not_53_out, F25);
  not not_54 (not_54_out, OP2);
  not not_55 (not_55_out, OP3);
  not not_56 (not_56_out, OP5);
  not not_57 (not_57_out, OP6);
  not not_58 (not_58_out, OP2);
  not not_59 (not_59_out, OP3);
  not not_60 (not_60_out, OP2);
  not not_61 (not_61_out, OP3);
  not not_62 (not_62_out, F13);
  not not_63 (not_63_out, F14);
  not not_64 (not_64_out, OP3);
  not not_65 (not_65_out, OP4);
  not not_66 (not_66_out, F12);
  not not_67 (not_67_out, F13);
  not not_68 (not_68_out, F14);
  not not_69 (not_69_out, OP2);
  not not_70 (not_70_out, OP3);
  not not_71 (not_71_out, OP5);
  not not_72 (not_72_out, OP6);
  not not_73 (not_73_out, F12);
  not not_74 (not_74_out, F14);
  not not_75 (not_75_out, OP2);
  not not_76 (not_76_out, OP3);
  not not_77 (not_77_out, OP4);
  not not_78 (not_78_out, OP5);
  not not_79 (not_79_out, OP6);
  not not_80 (not_80_out, F13);
  not not_81 (not_81_out, F14);
  not not_82 (not_82_out, OP2);
  not not_83 (not_83_out, OP3);
  not not_84 (not_84_out, OP6);
  not not_85 (not_85_out, F12);
  not not_86 (not_86_out, F13);
  not not_87 (not_87_out, F14);
  not not_88 (not_88_out, F25);
  not not_89 (not_89_out, OP3);
  not not_90 (not_90_out, OP5);
  not not_91 (not_91_out, OP6);
  not not_92 (not_92_out, F12);
  not not_93 (not_93_out, OP3);
  not not_94 (not_94_out, OP5);
  not not_95 (not_95_out, OP6);
  not not_96 (not_96_out, F25);
  not not_97 (not_97_out, F30);
  not not_98 (not_98_out, OP3);
  not not_99 (not_99_out, OP5);
  not not_100 (not_100_out, OP6);
  not not_101 (not_101_out, F25);
  not not_102 (not_102_out, OP2);
  not not_103 (not_103_out, OP3);
  not not_104 (not_104_out, OP6);
  not not_105 (not_105_out, F25);
  not not_106 (not_106_out, F30);
  not not_107 (not_107_out, OP3);
  not not_108 (not_108_out, OP5);
  not not_109 (not_109_out, OP6);
  not not_110 (not_110_out, OP4);
  not not_111 (not_111_out, F12);
  not not_112 (not_112_out, F13);
  not not_113 (not_113_out, F14);
  not not_114 (not_114_out, OP3);
  not not_115 (not_115_out, OP5);
  not not_116 (not_116_out, OP6);
  not not_117 (not_117_out, OP4);
  not not_118 (not_118_out, OP2);
  not not_119 (not_119_out, OP3);
  not not_120 (not_120_out, F12);
  not not_121 (not_121_out, F13);
  not not_122 (not_122_out, F14);
  not not_123 (not_123_out, F25);
  not not_124 (not_124_out, F30);
  not not_125 (not_125_out, OP2);
  not not_126 (not_126_out, OP3);
  not not_127 (not_127_out, OP4);
  not not_128 (not_128_out, OP6);
  not not_129 (not_129_out, F12);
  not not_130 (not_130_out, F14);
  not not_131 (not_131_out, OP2);
  not not_132 (not_132_out, OP3);
  not not_133 (not_133_out, OP4);
  not not_134 (not_134_out, F12);
  not not_135 (not_135_out, F13);
  not not_136 (not_136_out, F14);
  not not_137 (not_137_out, OP2);
  not not_138 (not_138_out, OP3);
  not not_139 (not_139_out, OP4);
  not not_140 (not_140_out, F13);
  not not_141 (not_141_out, F14);
  not not_142 (not_142_out, OP3);
  not not_143 (not_143_out, OP4);
  not not_144 (not_144_out, F12);
  not not_145 (not_145_out, F13);
  not not_146 (not_146_out, F14);
  not not_147 (not_147_out, OP4);
  not not_148 (not_148_out, OP2);
  not not_149 (not_149_out, OP3);
  not not_150 (not_150_out, F12);
  not not_151 (not_151_out, OP2);
  not not_152 (not_152_out, OP3);
  not not_153 (not_153_out, OP2);
  not not_154 (not_154_out, OP3);
  not not_155 (not_155_out, F13);
  not not_156 (not_156_out, F14);
  and and_1 (and_1_out, not_1_out, not_2_out, not_3_out, not_4_out, not_5_out, not_6_out, not_7_out, not_8_out, not_9_out);
  and and_2 (and_2_out, not_10_out, not_11_out, not_12_out, not_13_out, not_14_out, not_15_out, F13, not_16_out);
  and and_3 (MemWrite, not_17_out, not_18_out, not_19_out, OP5, not_20_out, not_21_out, F13, not_22_out);
  and and_4 (and_4_out, not_23_out, not_24_out, not_25_out, not_26_out, not_27_out, not_28_out, not_29_out, not_30_out);
  and and_5 (and_5_out, not_31_out, not_32_out, not_33_out, not_34_out, not_35_out, F13, not_36_out);
  and and_6 (and_6_out, not_37_out, not_38_out, OP4, not_39_out, not_40_out, not_41_out);
  and and_7 (and_7_out, not_42_out, not_43_out, OP4, not_44_out, not_45_out, not_46_out, not_47_out, not_48_out);
  and and_8 (and_8_out, not_49_out, not_50_out, OP4, not_51_out, not_52_out, F14, not_53_out);
  and and_9 (and_9_out, not_54_out, not_55_out, OP4, not_56_out, not_57_out, F13, F14);
  and and_10 (and_10_out, not_58_out, not_59_out, OP4, OP5, OP6, F13, F14);
  and and_11 (and_11_out, not_60_out, not_61_out, OP4, OP5, OP6, F12, not_62_out, not_63_out);
  and and_12 (and_12_out, OP2, not_64_out, not_65_out, OP5, OP6, not_66_out, not_67_out, not_68_out);
  and and_13 (and_13_out, not_69_out, not_70_out, not_71_out, not_72_out, not_73_out, F13, not_74_out);
  and and_14 (and_14_out, not_75_out, not_76_out, not_77_out, not_78_out, not_79_out, F12, not_80_out, not_81_out);
  and and_15 (and_15_out, not_82_out, not_83_out, OP4, not_84_out, not_85_out, not_86_out, not_87_out, not_88_out);
  and and_16 (and_16_out, not_89_out, OP4, not_90_out, not_91_out, not_92_out);
  and and_17 (and_17_out, not_93_out, OP4, not_94_out, not_95_out, not_96_out, not_97_out);
  and and_18 (and_18_out, not_98_out, OP4, not_99_out, not_100_out, F14, not_101_out);
  and and_19 (and_19_out, not_102_out, not_103_out, OP4, not_104_out, F13, not_105_out, not_106_out);
  and and_20 (and_20_out, not_107_out, OP4, not_108_out, not_109_out, F13);
  and and_21 (and_21_out, OP2, not_110_out, OP5, OP6, not_111_out, not_112_out, not_113_out);
  and and_22 (and_22_out, OP2, not_114_out, OP4, not_115_out, not_116_out);
  and and_23 (and_23_out, OP2, OP3, not_117_out, OP5, OP6);
  and and_24 (ecall, not_118_out, not_119_out, OP4, OP5, OP6, not_120_out, not_121_out, not_122_out, not_123_out, not_124_out);
  and and_25 (S_Type, not_125_out, not_126_out, not_127_out, OP5, not_128_out, not_129_out, F13, not_130_out);
  and and_26 (BEQ, not_131_out, not_132_out, not_133_out, OP5, OP6, not_134_out, not_135_out, not_136_out);
  and and_27 (BNE, not_137_out, not_138_out, not_139_out, OP5, OP6, F12, not_140_out, not_141_out);
  and and_28 (JALR, OP2, not_142_out, not_143_out, OP5, OP6, not_144_out, not_145_out, not_146_out);
  and and_29 (JAL, OP2, OP3, not_147_out, OP5, OP6);
  and and_30 (CSRRSI, not_148_out, not_149_out, OP4, OP5, OP6, not_150_out, F13, F14);
  and and_31 (CSRRCI, not_151_out, not_152_out, OP4, OP5, OP6, F12, F13, F14);
  and and_32 (CSRRW, not_153_out, not_154_out, OP4, OP5, OP6, F12, not_155_out, not_156_out);
  or or_1 (MemToReg, and_1_out, and_2_out);
  or or_2 (ALU_SRC, and_4_out, and_5_out, and_6_out, and_7_out, and_8_out, and_9_out, and_10_out, and_11_out, and_12_out);
  or or_3 (RegWrite, and_13_out, and_14_out, and_15_out, and_16_out, and_17_out, and_18_out, and_19_out, and_20_out, and_21_out, and_22_out, and_23_out);
endmodule

// ALU
module ALU (
  input  [31:0] X,
  input  [31:0] Y,
  input  [3:0] AluOP,
  output out_4,
  output Equal,
  output out_6,
  output [31:0] Result,
  output [31:0] Result_2
);

  wire [0:0] comparator_1_lt, comparator_2_lt;
  wire [31:0] adder_1_out, AND_out, divider_1_out, divider_1_rem, multiplier_1_cout, multiplier_1_out,
       NOR_out, OR_out, shifter_1_out, shifter_2_out, shifter_3_out, subtractor_1_out, XOR_out;

  assign AND_out = X & Y;  // AND_Gate AND, 32 bits wide
  assign OR_out = X | Y;  // OR_Gate OR, 32 bits wide
  Shifter #(.width(32), .shift("ll")) shifter_1 (.in(X), .\dist (Y[4:0]), .out(shifter_1_out));
  Shifter #(.width(32), .shift("ar")) shifter_2 (.in(X), .\dist (Y[4:0]), .out(shifter_2_out));
  Shifter #(.width(32), .shift("lr")) shifter_3 (.in(X), .\dist (Y[4:0]), .out(shifter_3_out));
  Multiplier #(.width(32)) multiplier_1 (.a(X), .b(Y), .out(multiplier_1_out), .cout(multiplier_1_cout));  // open: cin
  Divider #(.width(32)) divider_1 (.a(X), .b(Y), .out(divider_1_out), .rem(divider_1_rem));  // open: upper
  Adder #(.width(32)) adder_1 (.a(X), .b(Y), .out(adder_1_out));  // open: cin, cout
  Subtractor #(.width(32)) subtractor_1 (.a(X), .b(Y), .out(subtractor_1_out));  // open: bin, bout
  assign XOR_out = X ^ Y;  // XOR_Gate XOR, 32 bits wide
  assign NOR_out = ~(X | Y);  // NOR_Gate NOR, 32 bits wide
  Comparator #(.width(32), .mode("twosComplement")) comparator_1 (
    .a(X), .b(Y), .eq(Equal), .lt(comparator_1_lt[0]));  // open: gt
  Comparator #(.width(32), .mode("unsigned")) comparator_2 (.a(X), .b(Y), .lt(comparator_2_lt[0]));  // open: gt, eq
  Multiplexer #(.select(4), .width(32), .disabled("Z"), .enable("false")) multiplexer_1 (
    .in0(shifter_1_out), .in1(shifter_2_out), .in2(shifter_3_out), .in3(multiplier_1_out),
    .in4(divider_1_out), .in5(adder_1_out), .in6(subtractor_1_out), .in7(AND_out), .in8(OR_out),
    .in9(XOR_out), .in10(NOR_out), .in11({{31{1'b0}}, comparator_1_lt[0]}),
    .in12({{31{1'b0}}, comparator_2_lt[0]}), .in13({32{1'b0}}), .in14({32{1'b0}}), .in15({32{1'b0}}),
    .out(Result), .sel(AluOP));
  Multiplexer #(.select(4), .width(32), .disabled("Z"), .enable("false")) multiplexer_2 (
    .in0({32{1'b0}}), .in1({32{1'b0}}), .in2({32{1'b0}}), .in3(multiplier_1_cout), .in4(divider_1_rem),
    .in5({32{1'b0}}), .in6({32{1'b0}}), .in7({32{1'b0}}), .in8({32{1'b0}}), .in9({32{1'b0}}),
    .in10({32{1'b0}}), .in11({32{1'b0}}), .in12({32{1'b0}}), .in13({32{1'b0}}), .in14({32{1'b0}}),
    .in15({32{1'b0}}), .out(Result_2), .sel(AluOP));
  Multiplexer #(.select(4), .width(1), .disabled("Z"), .enable("false")) multiplexer_3 (
    .in0(1'b0), .in1(1'b0), .in2(1'b0), .in3(1'b0), .in4(1'b0), .in5(1'b0), .in6(1'b0), .in7(1'b0),
    .in8(1'b0), .in9(1'b0), .in10(1'b0), .in11(comparator_1_lt[0]), .in12(comparator_2_lt[0]), .in13(1'b0),
    .in14(1'b0), .in15(1'b0), .out(out_6), .sel(AluOP));
  not not_1 (out_4, out_6);

  // Other names for the same wires on the sheet: Result2[31:0] = Result_2; S[3:0] = AluOP; tunnel = out_6;
  //   tunnel_t = out_4

  // Notes on the sheet:
  //   不要改变此引脚区域内容，也不要改变ALU封装形式
  //   输入引脚
  //   输出引脚
endmodule

module Regifile (
  input  [31:0] Din,
  input  Clk,
  input  WE,
  input  [4:0] R1_num,
  input  [4:0] W_num,
  input  [4:0] R2_num,
  output [31:0] R1,
  output [31:0] R2
);

  // RegisterFile registerfile_1: pin names not known; wires that end beside it: Din, Clk, WE, W_num, R1_num, R2_num, R1, R2
endmodule

module \理想流水线  (
);


  // Notes on the sheet:
  //   本文件仅包含多级中断电路
  //   请见cpu21-riscv-2(理想流水线).circ的“理想流水线”
endmodule

module \气泡流水线  (
);


  // Notes on the sheet:
  //   本文件仅包含多级中断电路
  //   请见cpu21-riscv-3(气泡流水线).circ的“气泡流水线”
endmodule

module \重定向流水线  (
);


  // Notes on the sheet:
  //   本文件仅包含多级中断电路
  //   请见cpu21-riscv-4(重定向流水线).circ的“重定向流水线”
endmodule

module \中断按键参考电路  (
  input  \同步清零信号 ,
  output \与中断屏蔽位与 
);

  wire \_1号中断_out , and_1_out, clock_1_out, d_ff_1_q, or_1_out, or_2_out;

  Clock #(.highDuration(1), .lowDuration(1)) clock_1 (.out(clock_1_out));
  Button \_1号中断  (.out(\_1号中断_out ));
  LED #(.active("true")) \_1号中断等待指示灯  (.in(or_1_out));
  or or_1 (or_1_out, \与中断屏蔽位与 , d_ff_1_q);
  D_Flip_Flop #(.trigger("rising"), .Pre_Clr_Positions("LEGACY"), .NegatePresetClear("false"), .enable("true"), .NewFFLayout("false")) d_ff_1 (
    .clk(\_1号中断_out ), .D(1'b1), .Q(d_ff_1_q), .reset(\与中断屏蔽位与 ));  // open: Qn, preset, en
  or or_2 (or_2_out, d_ff_1_q, \与中断屏蔽位与 );
  and and_1 (and_1_out, or_2_out, ~\同步清零信号 );  // AND_Gate
  D_Flip_Flop #(.trigger("rising"), .Pre_Clr_Positions("LEGACY"), .NegatePresetClear("false"), .enable("true"), .NewFFLayout("false")) IR1 (
    .clk(clock_1_out), .D(and_1_out), .Q(\与中断屏蔽位与 ));  // open: Qn, preset, en, reset

  // Notes on the sheet:
  //   中断信号采样参考电路
  //   Reset 
endmodule

module \单周期_单级中断  (
);


  // Notes on the sheet:
  //   本文件仅包含多级中断电路
  //   请见cpu21-riscv-5(单级中断).circ的“单周期+单级中断”
endmodule

module \单周期_多级中断  (
  input  IR1,
  input  IR2,
  input  IR3,
  output RegWrite,
  output MemWrite,
  output [31:0] PC,
  output [31:0] IR,
  output [31:0] RDin,
  output [31:0] MDin,
  output [31:0] LedData
);

  wire and_1_out, and_2_out, and_3_out, and_4_out, and_5_out, and_6_out, and_10_out, Beq, Bne, button_2_out,
       clear1, clear2, clear3, CLK, clock_2_out, comparator_1_eq, comparator_2_eq, comparator_3_eq,
       comparator_3_lt, comparator_4_eq, comparator_5_eq, comparator_6_eq, comparator_7_eq, comparator_8_eq,
       CSRRCI, CSRRSI, d_ff_2_q, decoder_1_out0, decoder_1_out1, decoder_1_out2, decoder_2_out1,
       decoder_2_out2, decoder_2_out3, decoder_3_out1, decoder_3_out2, decoder_3_out3, ecall, Equal, FLAG1_q,
       FLAG2_q, FLAG3_q, Go, halt, Has_Run, IE, INT, INT_Level, IR1_t, IR2_t, IR3_t, IRA, IRB, IRC, JAL,
       JALR, multiplexer_3_out, multiplexer_12_out, nand_1_out, NEW_INT, not_1_out, not_2_out, not_3_out,
       not_4_out, not_5_out, not_7_out, not_8_out, not_9_out, not_10_out, not_11_out, or_2_out, or_3_out,
       or_6_out, or_7_out, or_8_out, or_9_out, or_10_out, or_11_out, or_12_out, or_13_out, or_14_out,
       or_18_out, or_19_out, or_20_out, or_21_out, or_22_out, or_23_out, or_24_out, register_1_q,
       register_2_q, register_3_q, register_4_q, register_5_q, register_6_q, register_8_q, register_9_q,
       register_10_q, register_15_q, register_16_q, RST, URET, W1, W2, W3, \中断信号 , \单周期硬布线控制器_1_alu_src ,
       \单周期硬布线控制器_1_memtoreg , \单周期硬布线控制器_1_s_type ;
  wire [1:0] INT_NUM, multiplexer_8_out, priority_encoder_1_out, priority_encoder_3_out, register_14_q,
       subtractor_1_out, TOP;
  wire [3:0] \单周期硬布线控制器_1_alu_op ;
  wire [4:0] multiplexer_6_out, multiplexer_7_out;
  wire [11:0] multiplexer_9_out;
  wire [12:0] CNT_num;
  wire [15:0] \总周期数 ;
  wire [31:0] adder_2_out, adder_3_out, bit_extender_1_out, bit_extender_2_out, bit_extender_3_out,
       multiplexer_1_out, multiplexer_2_out, multiplexer_11_out, NEXT_PC, PC_4, PC_INT, PC_RET, ram_1_data,
       regifile_1_r1, register_11_q, register_12_q, register_13_q, Result, shifter_1_out, shifter_2_out;

  Clock #(.highDuration(1), .lowDuration(1)) clock_1 ();  // open: out
  Button _1 ();  // open: out
  Button _2 ();  // open: out
  Button _3 ();  // open: out
  Button \u_继续运行  (.out(Go));
  LED #(.active("true")) led_1 (.in(W1));
  LED #(.active("true")) led_2 (.in(W2));
  LED #(.active("true")) led_3 (.in(W3));
  Button button_1 (.out(RST));
  Hex_Digit_Display hex_digit_display_1 (.value(LedData[31:28]));  // open: dp
  or or_1 (W1, register_8_q, register_1_q);
  Hex_Digit_Display hex_digit_display_2 (.value(LedData[27:24]));  // open: dp
  Hex_Digit_Display hex_digit_display_3 (.value(LedData[23:20]));  // open: dp
  Multiplexer #(.select(2), .width(32), .disabled("Z"), .enable("false")) multiplexer_1 (
    .in0(PC_4), .in1(adder_2_out), .in2(adder_3_out), .in3(Result), .out(multiplexer_1_out),
    .sel(priority_encoder_1_out));
  Register #(.width(1), .trigger("rising"), .Select("low")) register_1 (
    .D(1'b1), .Q(register_1_q), .clk(IR1_t), .clr(or_2_out));  // open: en
  or or_2 (or_2_out, register_8_q, RST);
  or or_3 (or_3_out, register_9_q, RST);
  or or_4 (W2, register_9_q, register_4_q);
  or or_5 (W3, register_10_q, register_5_q);
  Hex_Digit_Display hex_digit_display_4 (.value(LedData[15:12]));  // open: dp
  Hex_Digit_Display hex_digit_display_5 (.value(LedData[19:16]));  // open: dp
  Priority_Encoder #(.select(2), .disabled("Z")) priority_encoder_1 (
    .in0(1'b1), .in1(or_13_out), .in2(JAL), .in3(JALR), .out(priority_encoder_1_out));  // open: gs, en_out, en_in
  Multiplexer #(.select(1), .width(32), .disabled("Z"), .enable("false")) multiplexer_2 (
    .in0(multiplexer_1_out), .in1(PC_RET), .out(multiplexer_2_out), .sel(URET));
  not not_1 (not_1_out, halt);
  Register #(.width(1), .trigger("rising"), .Select("low")) register_2 (
    .D(1'b1), .Q(register_2_q), .clk(NEW_INT), .clr(or_6_out));  // open: en
  or or_6 (or_6_out, RST, register_3_q);
  Register #(.width(1), .trigger("rising"), .Select("low")) register_3 (
    .D(1'b1), .Q(register_3_q), .clk(multiplexer_3_out), .clr(or_7_out));  // open: en
  or or_7 (or_7_out, register_3_q, RST);
  Multiplexer #(.select(1), .width(1), .disabled("Z"), .enable("false")) multiplexer_3 (
    .in0(1'b1), .in1(CLK), .out(multiplexer_3_out), .sel(register_2_q));
  Register #(.width(1), .trigger("rising"), .Select("low")) register_4 (
    .D(1'b1), .Q(register_4_q), .clk(IR2_t), .clr(or_3_out));  // open: en
  Register #(.width(1), .trigger("rising"), .Select("low")) register_5 (
    .D(1'b1), .Q(register_5_q), .clk(IR3_t), .clr(or_8_out));  // open: en
  or or_8 (or_8_out, register_10_q, RST);
  or or_9 (or_9_out, CSRRCI, INT_Level);
  not not_2 (not_2_out, URET);
  and and_1 (and_1_out, not_2_out, not_3_out);
  not not_3 (not_3_out, CSRRSI);
  Hex_Digit_Display hex_digit_display_6 (.value(LedData[7:4]));  // open: dp
  Hex_Digit_Display hex_digit_display_7 (.value(LedData[11:8]));  // open: dp
  // Probe on \总周期数 
  Register #(.width(32), .trigger("rising"), .Select("low")) u_PC (
    .D(multiplexer_2_out), .en(not_1_out), .Q(NEXT_PC), .clk(CLK), .clr(RST));
  or or_10 (or_10_out, register_1_q, register_8_q);
  not not_4 (not_4_out, clear1);
  or or_11 (or_11_out, register_4_q, register_9_q);
  not not_5 (not_5_out, clear2);
  or or_12 (or_12_out, register_5_q, register_10_q);
  Register #(.width(1), .trigger("rising"), .Select("low")) register_6 (
    .D(1'b0), .Q(register_6_q), .clk(and_1_out), .clr(RST), .preset(or_9_out));  // open: en, cs
  not not_6 (IE, register_6_q);
  Hex_Digit_Display hex_digit_display_8 (.value(LedData[3:0]));  // open: dp
  and and_2 (and_2_out, Bne, not_8_out);
  or or_13 (or_13_out, and_2_out, and_3_out);
  and and_3 (and_3_out, Beq, Equal);
  Multiplexer #(.select(1), .width(32), .disabled("Z"), .enable("false")) multiplexer_4 (
    .in0(NEXT_PC), .in1(PC_INT), .out(PC), .sel(INT_Level));
  Register #(.width(1), .trigger("rising"), .Select("low")) register_7 (
    .D(register_2_q), .Q(INT_Level), .clk(CLK), .clr(RST));  // open: en
  and and_4 (and_4_out, or_10_out, not_4_out);
  and and_5 (and_5_out, or_11_out, not_5_out);
  and and_6 (and_6_out, or_12_out, not_7_out);
  not not_7 (not_7_out, clear3);
  or or_14 (or_14_out, INT_Level, URET);
  not not_8 (not_8_out, Equal);
  // Probe on adder_3_out
  Register #(.width(1), .trigger("rising"), .Select("low")) register_8 (
    .D(and_4_out), .Q(register_8_q), .clk(CLK), .clr(RST));  // open: en
  Register #(.width(1), .trigger("rising"), .Select("low")) register_9 (
    .D(and_5_out), .Q(register_9_q), .clk(CLK), .clr(RST));  // open: en
  Register #(.width(1), .trigger("rising"), .Select("low")) register_10 (
    .D(and_6_out), .Q(register_10_q), .clk(CLK), .clr(RST));  // open: en
  Counter #(.width(2), .max('h3), .ongoal("wrap"), .trigger("rising"), .behavior("new")) counter_1 (
    .count(or_14_out), .Q(TOP), .clk(CLK), .clr(RST), .down(URET));  // open: load, D, carry, preset
  Decoder #(.select(2), .tristate("false"), .disabled("Z"), .enable("false")) decoder_1 (
    .out0(decoder_1_out0), .out1(decoder_1_out1), .out2(decoder_1_out2), .sel(TOP));  // open: out3
  or or_15 (IR1_t, IR1, IRA);
  Priority_Encoder #(.select(2), .disabled("Z")) priority_encoder_2 (
    .in0(1'b1), .in1(register_8_q), .in2(register_9_q), .in3(register_10_q), .out(INT_NUM), .gs(\中断信号 ),
    .en_in(1'b1));  // open: en_out
  or or_16 (IR2_t, IR2, IRB);
  // RiscV_Probe riscv_probe_1: pin names not known; wires that end beside it: IR
  ROM #(.addrWidth(10), .dataWidth(32), .Select("high")) rom_1 (.addr(PC[11:2]), .data(IR));
  Adder #(.width(32)) adder_1 (.a(PC), .b(32'h4), .out(PC_4));  // open: cin, cout
  Multiplexer #(.select(2), .width(32), .disabled("Z"), .enable("false")) multiplexer_5 (
    .in1(32'h30ac), .in2(32'h3158), .in3(32'h3204), .out(PC_INT), .sel(INT_NUM));  // open: in0
  Register #(.width(32), .trigger("rising"), .Select("low")) register_11 (
    .D(NEXT_PC), .en(decoder_1_out0), .Q(register_11_q), .clk(CLK), .clr(RST));
  Register #(.width(32), .trigger("rising"), .Select("low")) register_12 (
    .D(NEXT_PC), .en(decoder_1_out1), .Q(register_12_q), .clk(CLK), .clr(RST));
  Register #(.width(32), .trigger("rising"), .Select("low")) register_13 (
    .D(NEXT_PC), .en(decoder_1_out2), .Q(register_13_q), .clk(CLK), .clr(RST));
  or or_17 (IR3_t, IR3, IRC);
  \单周期硬布线控制器  \u_单周期硬布线控制器_1  (
    .Funct({IR[30], IR[25], IR[14:12]}), .OP(IR[6:2]), .ALU_OP(\单周期硬布线控制器_1_alu_op ),
    .MemToReg(\单周期硬布线控制器_1_memtoreg ), .MemWrite(MemWrite), .ALU_SRC(\单周期硬布线控制器_1_alu_src ),
    .RegWrite(RegWrite), .ecall(ecall), .S_type(\单周期硬布线控制器_1_s_type ), .Jalr(JALR), .Beq(Beq), .JAL(JAL),
    .Bne(Bne), .in_3(IR[21]), .uret(URET), .CSRRSI(CSRRSI), .CSRRCI(CSRRCI));
  Multiplexer #(.select(1), .width(5), .disabled("Z"), .enable("false")) multiplexer_6 (
    .in0(IR[19:15]), .in1(5'b10001), .out(multiplexer_6_out), .sel(ecall));
  Multiplexer #(.select(1), .width(5), .disabled("Z"), .enable("false")) multiplexer_7 (
    .in0(IR[24:20]), .in1(5'b01010), .out(multiplexer_7_out), .sel(ecall));
  Multiplexer #(.select(1), .width(2), .disabled("Z"), .enable("false")) multiplexer_8 (
    .in0(multiplexer_8_out), .in1(INT_NUM), .out(multiplexer_8_out), .sel(IE));
  Subtractor #(.width(2)) subtractor_1 (.a(TOP), .b(2'b01), .out(subtractor_1_out));  // open: bin, bout
  Multiplexer #(.select(1), .width(12), .disabled("Z"), .enable("false")) multiplexer_9 (
    .in0(IR[31:20]), .in1({IR[31:25], IR[11:7]}), .out(multiplexer_9_out), .sel(\单周期硬布线控制器_1_s_type ));
  Multiplexer #(.select(2), .width(32), .disabled("Z"), .enable("false")) multiplexer_10 (
    .in0(register_11_q), .in1(register_12_q), .in2(register_13_q), .out(PC_RET), .sel(subtractor_1_out));  // open: in3
  assign bit_extender_1_out = {{20{multiplexer_9_out[11]}}, multiplexer_9_out};  // Bit_Extender bit_extender_1
  assign bit_extender_2_out = {{20{IR[31]}}, {IR[31], IR[7], IR[30:25], IR[11:8]}};  // Bit_Extender bit_extender_2
  Shifter #(.width(32), .shift("ll")) shifter_1 (.in(bit_extender_2_out), .\dist (5'b00001), .out(shifter_1_out));
  assign bit_extender_3_out = {{12{IR[31]}}, {IR[31], IR[19:12], IR[20], IR[30:21]}};  // Bit_Extender bit_extender_3
  Shifter #(.width(32), .shift("ll")) shifter_2 (.in(bit_extender_3_out), .\dist (5'b00001), .out(shifter_2_out));
  Decoder #(.select(2), .tristate("false"), .disabled("Z"), .enable("false")) decoder_2 (
    .out1(decoder_2_out1), .out2(decoder_2_out2), .out3(decoder_2_out3), .sel(register_14_q));  // open: out0
  Register #(.width(2), .trigger("rising"), .Select("low")) register_14 (
    .D(multiplexer_8_out), .Q(register_14_q), .clk(CLK), .clr(RST));  // open: en
  Register #(.width(1), .trigger("rising"), .Select("low")) register_15 (
    .D(1'b0), .Q(register_15_q), .clk(CLK), .clr(RST), .preset(URET));  // open: en, cs
  Regifile regifile_1 (
    .Din(RDin), .Clk(CLK), .R1(regifile_1_r1), .R2(MDin), .WE(RegWrite), .W_num(IR[11:7]),
    .R1_num(multiplexer_6_out), .R2_num(multiplexer_7_out));
  Adder #(.width(32)) adder_2 (.a(shifter_1_out), .b(PC), .out(adder_2_out));  // open: cin, cout
  Adder #(.width(32)) adder_3 (.a(shifter_2_out), .b(PC), .out(adder_3_out));  // open: cin, cout
  and and_7 (clear1, decoder_2_out1, URET);
  and and_8 (clear2, decoder_2_out2, URET);
  and and_9 (clear3, decoder_2_out3, URET);
  Comparator #(.width(2), .mode("twosComplement")) comparator_1 (
    .a(register_14_q), .b(multiplexer_8_out), .eq(comparator_1_eq));  // open: gt, lt
  not not_9 (not_9_out, comparator_1_eq);
  or or_18 (or_18_out, register_15_q, register_16_q);
  Register #(.width(1), .trigger("rising"), .Select("low")) register_16 (
    .D(register_15_q), .Q(register_16_q), .clk(CLK), .clr(RST));  // open: en
  Multiplexer #(.select(1), .width(32), .disabled("Z"), .enable("false")) multiplexer_11 (
    .in0(MDin), .in1(bit_extender_1_out), .out(multiplexer_11_out), .sel(\单周期硬布线控制器_1_alu_src ));
  Multiplexer #(.select(1), .width(1), .disabled("Z"), .enable("false")) multiplexer_12 (
    .in0(not_9_out), .in1(multiplexer_12_out), .out(multiplexer_12_out), .sel(or_18_out));
  ALU alu_1 (
    .X(regifile_1_r1), .Y(multiplexer_11_out), .AluOP(\单周期硬布线控制器_1_alu_op ), .Equal(Equal), .Result(Result));  // open: Result_2, out_4, out_6
  Comparator #(.width(32), .mode("twosComplement")) comparator_2 (
    .a(regifile_1_r1), .b(32'ha), .eq(comparator_2_eq));  // open: gt, lt
  Multiplexer #(.select(1), .width(1), .disabled("Z"), .enable("false")) multiplexer_13 (
    .in0(not_9_out), .in1(multiplexer_12_out), .out(NEW_INT), .sel(Has_Run));
  not not_10 (not_10_out, comparator_2_eq);
  not not_11 (not_11_out, halt);
  Counter #(.width(16), .max('hffff), .ongoal("wrap"), .trigger("rising"), .behavior("old")) counter_2 (
    .Q(\总周期数 ), .clk(CLK));  // open: load, D, count, carry, clr, preset
  and and_10 (and_10_out, ecall, not_10_out);
  D_Flip_Flop #(.trigger("rising"), .Pre_Clr_Positions("ABOVE_BELOW"), .NegatePresetClear("false"), .enable("true"), .NewFFLayout("true")) d_ff_1 (
    .clk(comparator_2_eq), .D(1'b1), .Q(halt), .en(ecall), .reset(Go));  // open: Qn, preset
  D_Flip_Flop #(.trigger("high"), .Pre_Clr_Positions("LEGACY"), .NegatePresetClear("false"), .enable("true"), .NewFFLayout("false")) d_ff_2 (.Q(d_ff_2_q));  // open: clk, D, Qn, preset, en, reset
  // Probe on 13'hcd
  Button button_2 (.out(button_2_out));
  Register #(.width(32), .trigger("rising"), .Select("low")) register_17 (
    .D(MDin), .en(and_10_out), .Q(LedData), .clk(CLK));  // open: clr
  Comparator #(.width(13), .mode("twosComplement")) comparator_3 (
    .a(CNT_num), .b(13'hcd), .eq(comparator_3_eq), .lt(comparator_3_lt));  // open: gt
  Clock #(.highDuration(1), .lowDuration(1)) clock_2 (.out(clock_2_out));
  Priority_Encoder #(.select(2), .disabled("Z")) priority_encoder_3 (
    .in0(1'b1), .in1(\单周期硬布线控制器_1_memtoreg ), .in2(or_19_out), .out(priority_encoder_3_out));  // open: in3, gs, en_out, en_in
  RAM #(.addrWidth(10), .dataWidth(32), .bus("separate"), .Select("high")) ram_1 (
    .addr(Result[11:2]), .din(MDin), .data(ram_1_data), .str(MemWrite), .sel(1'b1), .clk(CLK), .ld(1'b1),
    .clr(button_2_out));
  Multiplexer #(.select(2), .width(32), .disabled("Z"), .enable("false")) multiplexer_14 (
    .in0(Result), .in1(ram_1_data), .in2(PC_4), .out(RDin), .sel(priority_encoder_3_out));  // open: in3
  Decoder #(.select(2), .tristate("false"), .disabled("Z"), .enable("false")) decoder_3 (
    .out1(decoder_3_out1), .out2(decoder_3_out2), .out3(decoder_3_out3), .sel(INT_NUM));  // open: out0
  nand nand_1 (nand_1_out, d_ff_2_q, comparator_3_eq);
  Counter #(.width(13), .max('h1fff), .ongoal("stay"), .trigger("rising"), .behavior("old")) counter_3 (
    .count(comparator_3_lt), .Q(CNT_num), .clk(clock_2_out));  // open: load, D, carry, clr, preset
  or or_19 (or_19_out, JAL, JALR);
  Comparator #(.width(16), .mode("twosComplement")) comparator_4 (
    .a(\总周期数 ), .b(16'h7), .eq(comparator_4_eq));  // open: gt, lt
  Comparator #(.width(16), .mode("twosComplement")) comparator_5 (
    .a(\总周期数 ), .b(16'h241), .eq(comparator_5_eq));  // open: gt, lt
  Register #(.width(1), .trigger("rising"), .Select("low")) FLAG1 (
    .D(1'b1), .en(decoder_3_out1), .Q(FLAG1_q), .clk(INT_Level), .clr(or_20_out));
  or or_20 (or_20_out, clear1, RST);
  Register #(.width(1), .trigger("rising"), .Select("low")) FLAG2 (
    .D(1'b1), .en(decoder_3_out2), .Q(FLAG2_q), .clk(INT_Level), .clr(or_21_out));
  or or_21 (or_21_out, clear2, RST);
  Register #(.width(1), .trigger("rising"), .Select("low")) FLAG3 (
    .D(1'b1), .en(decoder_3_out3), .Q(FLAG3_q), .clk(INT_Level), .clr(or_22_out));
  or or_22 (or_22_out, clear3, RST);
  Comparator #(.width(16), .mode("twosComplement")) comparator_6 (
    .a(16'h258), .b(\总周期数 ), .eq(comparator_6_eq));  // open: gt, lt
  or or_23 (or_23_out, comparator_6_eq, comparator_7_eq);
  Comparator #(.width(16), .mode("twosComplement")) comparator_7 (
    .a(\总周期数 ), .b(16'h1), .eq(comparator_7_eq));  // open: gt, lt
  Comparator #(.width(16), .mode("twosComplement")) comparator_8 (
    .a(\总周期数 ), .b(16'h4), .eq(comparator_8_eq));  // open: gt, lt
  or or_24 (or_24_out, comparator_4_eq, comparator_5_eq);
  and and_11 (INT, IE, \中断信号 );
  assign CLK = nand_1_out ? clock_2_out : 1'bz;  // Controlled_Buffer controlled_buffer_1
  Pull_Resistor #(.pull(1)) pull_resistor_1 (.node(CLK));
  Pull_Resistor #(.pull(0)) pull_resistor_2 (.node(IRA));
  assign IRA = or_23_out ? ~CLK : 1'bz;  // Controlled_Inverter controlled_inverter_1
  Pull_Resistor #(.pull(0)) pull_resistor_3 (.node(IRB));
  assign IRB = comparator_8_eq ? ~CLK : 1'bz;  // Controlled_Inverter controlled_inverter_2
  Pull_Resistor #(.pull(0)) pull_resistor_4 (.node(IRC));
  assign IRC = or_24_out ? ~CLK : 1'bz;  // Controlled_Inverter controlled_inverter_3
  Multiplexer #(.select(2), .width(1), .disabled("Z"), .enable("false")) multiplexer_15 (
    .in0(1'b1), .in1(FLAG1_q), .in2(FLAG2_q), .in3(FLAG3_q), .out(Has_Run), .sel(INT_NUM));

  // Notes on the sheet:
  //   中断源
  //   中断等待指示
  //   总复位信号应将除ROM以外所有存储组件全部清零
  //   数码管输出
  //   数码管输出应该用寄存器锁存，否则显示数据只能一闪而过
  //   指令探针
  //   指令存储器
  //   contents of rom_1 (hex, n*v repeats v):
  //   7d000113 100413 1f41993 41f9d993 433 c00913 800b13 140413 f47413 800293 100313 499993 89e9b3 1300533
  //   2200893 73 406282b3 fe0294e3 140413 f00f93 1f47433 1c41413 800293 100313 49d993 89e9b3 1300533
  //   2200893 73 406282b3 fe0294e3 1c45413 406b0b33 b0463 f95ff06f 2b3 fff2c293 1029293 fff2e293 500533
  //   2200893 73 f5dff06f 1112023 410113 a12023 410113 812023 410113 1312023 410113 1412023 410113 1512023
  //   410113 1612023 410113 40e073 100b13 300a13 100a93 1600433 441413 14469b3 1300533 2200893 73 fe0416e3
  //   415a0a33 fe0a10e3 40f073 ffc10113 12b03 ffc10113 12a83 ffc10113 12a03 ffc10113 12983 ffc10113 12403
  //   ffc10113 12503 ffc10113 12883 200073 1112023 410113 a12023 410113 812023 410113 1312023 410113
  //   1412023 410113 1512023 410113 1612023 410113 40e073 200b13 300a13 100a93 1600433 441413 14469b3
  //   1300533 2200893 73 fe0416e3 415a0a33 fe0a10e3 40f073 ffc10113 12b03 ffc10113 12a83 ffc10113 12a03
  //   ffc10113 12983 ffc10113 12403 ffc10113 12503 ffc10113 12883 200073 1112023 410113 a12023 410113
  //   812023 410113 1312023 410113 1412023 410113 1512023 410113 1612023 410113 40e073 300b13 300a13
  //   100a93 1600433 441413 14469b3 1300533 2200893 73 fe0416e3 415a0a33 fe0a10e3 40f073 ffc10113 12b03
  //   ffc10113 12a83 ffc10113 12a03 ffc10113 12983 ffc10113 12403 ffc10113 12503 ffc10113 12883 200073
  //   EPC1
  //   EPC2
  //   rs1
  //   rs2
  //   指令字
  //   rd
  //   EPC0
  //   JAL
  //   JALR
  //   URET
  //   I
  //   s
  //   b
  //   j
  //   Beq
  //   Bne
  //   MemToReg
  //   MemWrite
  //   AluOP
  //   AluSrcB
  //   RegWrite
  //   S_type
  //   为方便自动评测，需要输出PC，IR，寄存器堆写如数据RDin
  //   RAM写使能MemWrite、RAM写入数据MDin等信号
  //   控制位
  //   暂停节拍，不能为0
  //   数据存储器
  //   戳工具置1进入计数暂停模式，ctrl+k时钟自动运行到对应节拍暂停
  //   ctrl+k关闭时钟连续运行，将控制位置零，进入单步调试模式调试
  //   用这个时钟源需要去掉电路中的其他时钟源
  //   多级中断测试信号模拟器
  //   可计数暂停的时钟源
endmodule

module \封装正确性测试  (
);

  wire IR1, IR2, IR3, MemW, RegW;
  wire [31:0] IR, LED, MDin, PC, RDin;

  \单周期RISC_V  \u_单周期risc_v_1  ();
  \气泡流水线  \u_气泡流水线_1  ();
  \单周期_单级中断  \u_单周期_单级中断_1  ();
  \理想流水线  \u_理想流水线_1  ();
  \重定向流水线  \u_重定向流水线_1  ();
  \单周期_多级中断  \u_单周期_多级中断_1  (
    .IR1(IR1), .IR2(IR2), .IR3(IR3), .RegWrite(RegW), .MemWrite(MemW), .PC(PC), .IR(IR), .RDin(RDin),
    .MDin(MDin), .LedData(LED));

  // Notes on the sheet:
  //   单周期封装测试
  //   气泡流水封装测试
  //   单周期+单级中断封装测试
  //   请检查上面封装有无位宽不匹配，引脚标签是否和连接的标签相对应，否则无法在educoder平台上正确测试
  //   理想流水封装测试
  //   重定向流水封装测试
  //   单周期+多级中断封装测试
endmodule
