// Logisim project cpu21-riscv-8(动态预测).circ as structural Verilog: 23 circuits, main circuit ◇单周期RISC-V
module \单周期RISC_V  (
);


  // Notes on the sheet:
  //   本文件仅包含动态预测电路
  //   请见cpu21-riscv-1(单周期CCAB).circ的“单周期RISC-V”
endmodule

// 单周期硬布线控制器
module \单周期硬布线控制器  (
  input  [4:0] OP,
  input  [4:0] Funct,
  input  in_3,
  output [3:0] ALU_OP,
  output MemToReg,
  output MemWrite,
  output ALU_SRC,
  output uret,
  output \xor ,
  output Bge,
  output Lh,
  output Auipc,
  output RegWrite,
  output ecall,
  output S_type,
  output Beq,
  output Bne,
  output Jalr,
  output JAL,
  output RsUsed,
  output RtUsed
);

  wire \控制信号自动生成_1_ecall ;

  \运算控制器自动生成  \u_运算控制器自动生成_1  (
    .OP2(OP[0]), .OP3(OP[1]), .OP4(OP[2]), .OP5(OP[3]), .OP6(OP[4]), .F12(Funct[0]), .F13(Funct[1]),
    .F14(Funct[2]), .F25(Funct[3]), .F30(Funct[4]), .S0(ALU_OP[0]), .S1(ALU_OP[1]), .S2(ALU_OP[2]),
    .S3(ALU_OP[3]));
  \控制信号自动生成  \u_控制信号自动生成_1  (
    .OP2(OP[0]), .OP3(OP[1]), .OP4(OP[2]), .OP5(OP[3]), .OP6(OP[4]), .MemToReg(MemToReg), .F12(Funct[0]),
    .F13(Funct[1]), .F14(Funct[2]), .F25(Funct[3]), .F30(Funct[4]), .MemWrite(MemWrite), .ALU_SRC(ALU_SRC),
    .Xor(\xor ), .Bge(Bge), .Lh(Lh), .Auipc(Auipc), .RegWrite(RegWrite), .ecall(\控制信号自动生成_1_ecall ),
    .S_Type(S_type), .BEQ(Beq), .BNE(Bne), .JALR(Jalr), .JAL(JAL), .RsUsed(RsUsed), .RtUsed(RtUsed));
  and and_1 (uret, in_3, \控制信号自动生成_1_ecall );
  and and_2 (ecall, ~in_3, \控制信号自动生成_1_ecall );  // AND_Gate

  // Other names for the same wires on the sheet: IR21 = in_3; OP_CODE[4:0] = OP

  // Notes on the sheet:
  //   运算器控制器，根据指令生成运算器功能选择信号
  //   控制信号生成，产生数据通路需要的其他控制信号
endmodule

// 运算器控制器
module \运算控制器自动生成  (
  input  OP2,
  input  OP3,
  input  OP4,
  input  OP5,
  input  OP6,
  input  F12,
  input  F13,
  input  F14,
  input  F25,
  input  F30,
  output S0,
  output S1,
  output S2,
  output S3
);

  wire and_1_out, and_2_out, and_3_out, and_4_out, and_5_out, and_6_out, and_7_out, and_8_out, and_9_out,
       and_10_out, and_11_out, and_12_out, and_13_out, and_14_out, and_15_out, and_16_out, and_17_out,
       and_18_out, and_19_out, and_20_out, and_21_out, and_22_out, and_23_out, and_24_out, and_25_out,
       not_1_out, not_2_out, not_3_out, not_4_out, not_5_out, not_6_out, not_7_out, not_8_out, not_9_out,
       not_10_out, not_11_out, not_12_out, not_13_out, not_14_out, not_15_out, not_16_out, not_17_out,
       not_18_out, not_19_out, not_20_out, not_21_out, not_22_out, not_23_out, not_24_out, not_25_out,
       not_26_out, not_27_out, not_28_out, not_29_out, not_30_out, not_31_out, not_32_out, not_33_out,
       not_34_out, not_35_out, not_36_out, not_37_out, not_38_out, not_39_out, not_40_out, not_41_out,
       not_42_out, not_43_out, not_44_out, not_45_out, not_46_out, not_47_out, not_48_out, not_49_out,
       not_50_out, not_51_out, not_52_out, not_53_out, not_54_out, not_55_out, not_56_out, not_57_out,
       not_58_out, not_59_out, not_60_out, not_61_out, not_62_out, not_63_out, not_64_out, not_65_out,
       not_66_out, not_67_out, not_68_out, not_69_out, not_70_out, not_71_out, not_72_out, not_73_out,
       not_74_out, not_75_out, not_76_out, not_77_out, not_78_out, not_79_out, not_80_out, not_81_out,
       not_82_out, not_83_out, not_84_out, not_85_out, not_86_out, not_87_out, not_88_out, not_89_out,
       not_90_out, not_91_out, not_92_out, not_93_out, not_94_out, not_95_out, not_96_out, not_97_out,
       not_98_out, not_99_out, not_100_out, not_101_out, not_102_out, not_103_out, not_104_out, not_105_out,
       not_106_out, not_107_out, not_108_out, not_109_out, not_110_out, not_111_out, not_112_out,
       not_113_out, not_114_out, not_115_out, not_116_out, not_117_out, not_118_out, not_119_out,
       not_120_out, not_121_out, not_122_out, not_123_out, not_124_out, not_125_out, not_126_out,
       not_127_out, not_128_out, not_129_out, not_130_out, not_131_out, not_132_out, not_133_out,
       not_134_out, not_135_out, not_136_out, not_137_out, not_138_out, not_139_out;

  not not_1 (not_1_out, OP2);
  not not_2 (not_2_out, OP3);
  not not_3 (not_3_out, OP5);
  not not_4 (not_4_out, OP6);
  not not_5 (not_5_out, F12);
  not not_6 (not_6_out, F13);
  not not_7 (not_7_out, OP2);
  not not_8 (not_8_out, OP3);
  not not_9 (not_9_out, OP5);
  not not_10 (not_10_out, OP6);
  not not_11 (not_11_out, F12);
  not not_12 (not_12_out, F14);
  not not_13 (not_13_out, OP2);
  not not_14 (not_14_out, OP3);
  not not_15 (not_15_out, OP6);
  not not_16 (not_16_out, F12);
  not not_17 (not_17_out, F13);
  not not_18 (not_18_out, F25);
  not not_19 (not_19_out, F30);
  not not_20 (not_20_out, OP2);
  not not_21 (not_21_out, OP3);
  not not_22 (not_22_out, OP6);
  not not_23 (not_23_out, F12);
  not not_24 (not_24_out, F14);
  not not_25 (not_25_out, F25);
  not not_26 (not_26_out, F30);
  not not_27 (not_27_out, OP2);
  not not_28 (not_28_out, OP3);
  not not_29 (not_29_out, OP5);
  not not_30 (not_30_out, OP6);
  not not_31 (not_31_out, F13);
  not not_32 (not_32_out, F25);
  not not_33 (not_33_out, OP2);
  not not_34 (not_34_out, OP3);
  not not_35 (not_35_out, OP5);
  not not_36 (not_36_out, OP6);
  not not_37 (not_37_out, OP2);
  not not_38 (not_38_out, OP3);
  not not_39 (not_39_out, OP6);
  not not_40 (not_40_out, F25);
  not not_41 (not_41_out, F30);
  not not_42 (not_42_out, OP2);
  not not_43 (not_43_out, OP3);
  not not_44 (not_44_out, OP4);
  not not_45 (not_45_out, F13);
  not not_46 (not_46_out, F14);
  not not_47 (not_47_out, OP2);
  not not_48 (not_48_out, OP3);
  not not_49 (not_49_out, OP4);
  not not_50 (not_50_out, F13);
  not not_51 (not_51_out, OP2);
  not not_52 (not_52_out, OP3);
  not not_53 (not_53_out, OP5);
  not not_54 (not_54_out, OP6);
  not not_55 (not_55_out, F12);
  not not_56 (not_56_out, F14);
  not not_57 (not_57_out, OP2);
  not not_58 (not_58_out, OP3);
  not not_59 (not_59_out, OP6);
  not not_60 (not_60_out, F12);
  not not_61 (not_61_out, F14);
  not not_62 (not_62_out, F25);
  not not_63 (not_63_out, F30);
  not not_64 (not_64_out, OP2);
  not not_65 (not_65_out, OP3);
  not not_66 (not_66_out, OP5);
  not not_67 (not_67_out, OP6);
  not not_68 (not_68_out, F25);
  not not_69 (not_69_out, F30);
  not not_70 (not_70_out, OP2);
  not not_71 (not_71_out, OP3);
  not not_72 (not_72_out, OP5);
  not not_73 (not_73_out, OP6);
  not not_74 (not_74_out, OP2);
  not not_75 (not_75_out, OP3);
  not not_76 (not_76_out, OP6);
  not not_77 (not_77_out, F25);
  not not_78 (not_78_out, F30);
  not not_79 (not_79_out, OP2);
  not not_80 (not_80_out, OP3);
  not not_81 (not_81_out, OP6);
  not not_82 (not_82_out, F12);
  not not_83 (not_83_out, F13);
  not not_84 (not_84_out, F14);
  not not_85 (not_85_out, F25);
  not not_86 (not_86_out, OP2);
  not not_87 (not_87_out, OP3);
  not not_88 (not_88_out, OP4);
  not not_89 (not_89_out, F13);
  not not_90 (not_90_out, F14);
  not not_91 (not_91_out, OP2);
  not not_92 (not_92_out, OP3);
  not not_93 (not_93_out, OP4);
  not not_94 (not_94_out, F13);
  not not_95 (not_95_out, OP2);
  not not_96 (not_96_out, OP3);
  not not_97 (not_97_out, OP5);
  not not_98 (not_98_out, OP6);
  not not_99 (not_99_out, F12);
  not not_100 (not_100_out, F13);
  not not_101 (not_101_out, F14);
  not not_102 (not_102_out, OP2);
  not not_103 (not_103_out, OP3);
  not not_104 (not_104_out, OP6);
  not not_105 (not_105_out, F12);
  not not_106 (not_106_out, F13);
  not not_107 (not_107_out, F14);
  not not_108 (not_108_out, F25);
  not not_109 (not_109_out, OP2);
  not not_110 (not_110_out, OP3);
  not not_111 (not_111_out, OP5);
  not not_112 (not_112_out, OP6);
  not not_113 (not_113_out, OP2);
  not not_114 (not_114_out, OP3);
  not not_115 (not_115_out, OP6);
  not not_116 (not_116_out, F25);
  not not_117 (not_117_out, F30);
  not not_118 (not_118_out, OP2);
  not not_119 (not_119_out, OP3);
  not not_120 (not_120_out, OP5);
  not not_121 (not_121_out, OP6);
  not not_122 (not_122_out, F12);
  not not_123 (not_123_out, OP2);
  not not_124 (not_124_out, OP3);
  not not_125 (not_125_out, OP6);
  not not_126 (not_126_out, F12);
  not not_127 (not_127_out, F25);
  not not_128 (not_128_out, F30);
  not not_129 (not_129_out, OP2);
  not not_130 (not_130_out, OP3);
  not not_131 (not_131_out, OP5);
  not not_132 (not_132_out, OP6);
  not not_133 (not_133_out, F12);
  not not_134 (not_134_out, OP2);
  not not_135 (not_135_out, OP3);
  not not_136 (not_136_out, OP6);
  not not_137 (not_137_out, F14);
  not not_138 (not_138_out, F25);
  not not_139 (not_139_out, F30);
  and and_1 (and_1_out, not_1_out, not_2_out, OP4, not_3_out, not_4_out, not_5_out, not_6_out);
  and and_2 (and_2_out, not_7_out, not_8_out, OP4, not_9_out, not_10_out, not_11_out, not_12_out);
  and and_3 (and_3_out, not_13_out, not_14_out, OP4, not_15_out, not_16_out, not_17_out, not_18_out, not_19_out);
  and and_4 (and_4_out, not_20_out, not_21_out, OP4, not_22_out, not_23_out, not_24_out, not_25_out, not_26_out);
  and and_5 (and_5_out, not_27_out, not_28_out, OP4, not_29_out, not_30_out, not_31_out, F14, not_32_out, F30);
  and and_6 (and_6_out, not_33_out, not_34_out, OP4, not_35_out, not_36_out, F12, F13, F14);
  and and_7 (and_7_out, not_37_out, not_38_out, OP4, not_39_out, F12, F13, F14, not_40_out, not_41_out);
  and and_8 (and_8_out, not_42_out, not_43_out, not_44_out, OP5, OP6, not_45_out, not_46_out);
  and and_9 (and_9_out, not_47_out, not_48_out, not_49_out, OP5, OP6, F12, not_50_out);
  and and_10 (and_10_out, not_51_out, not_52_out, OP4, not_53_out, not_54_out, not_55_out, F13, not_56_out);
  and and_11 (and_11_out, not_57_out, not_58_out, OP4, not_59_out, not_60_out, F13, not_61_out, not_62_out, not_63_out);
  and and_12 (and_12_out, not_64_out, not_65_out, OP4, not_66_out, not_67_out, F12, F14, not_68_out, not_69_out);
  and and_13 (and_13_out, not_70_out, not_71_out, OP4, not_72_out, not_73_out, F12, F13, F14);
  and and_14 (and_14_out, not_74_out, not_75_out, OP4, not_76_out, F12, F13, F14, not_77_out, not_78_out);
  and and_15 (and_15_out, not_79_out, not_80_out, OP4, OP5, not_81_out, not_82_out, not_83_out, not_84_out, not_85_out, F30);
  and and_16 (and_16_out, not_86_out, not_87_out, not_88_out, OP5, OP6, not_89_out, not_90_out);
  and and_17 (and_17_out, not_91_out, not_92_out, not_93_out, OP5, OP6, F12, not_94_out);
  and and_18 (and_18_out, not_95_out, not_96_out, OP4, not_97_out, not_98_out, not_99_out, not_100_out, not_101_out);
  and and_19 (and_19_out, not_102_out, not_103_out, OP4, not_104_out, not_105_out, not_106_out, not_107_out, not_108_out);
  and and_20 (and_20_out, not_109_out, not_110_out, OP4, not_111_out, not_112_out, F12, F13, F14);
  and and_21 (and_21_out, not_113_out, not_114_out, OP4, OP5, not_115_out, F12, F13, not_116_out, not_117_out);
  and and_22 (and_22_out, not_118_out, not_119_out, OP4, not_120_out, not_121_out, not_122_out, F14);
  and and_23 (and_23_out, not_123_out, not_124_out, OP4, not_125_out, not_126_out, F14, not_127_out, not_128_out);
  and and_24 (and_24_out, not_129_out, not_130_out, OP4, not_131_out, not_132_out, not_133_out, F13);
  and and_25 (and_25_out, not_134_out, not_135_out, OP4, OP5, not_136_out, F13, not_137_out, not_138_out, not_139_out);
  or or_1 (S0, and_1_out, and_2_out, and_3_out, and_4_out, and_5_out, and_6_out, and_7_out);
  or or_2 (S2, and_16_out, and_17_out, and_18_out, and_19_out, and_20_out, and_21_out);
  or or_3 (S3, and_22_out, and_23_out, and_24_out, and_25_out);
  or or_4 (S1, and_8_out, and_9_out, and_10_out, and_11_out, and_12_out, and_13_out, and_14_out, and_15_out);
endmodule

// 控制信号生成
module \控制信号自动生成  (
  input  OP2,
  input  OP3,
  input  OP4,
  input  OP5,
  input  OP6,
  input  F12,
  input  F13,
  input  F14,
  input  F25,
  input  F30,
  output MemToReg,
  output MemWrite,
  output ALU_SRC,
  output Xor,
  output Bge,
  output Lh,
  output Auipc,
  output RegWrite,
  output ecall,
  output S_Type,
  output BEQ,
  output BNE,
  output JALR,
  output JAL,
  output RsUsed,
  output RtUsed
);

  wire and_1_out, and_2_out, and_4_out, and_5_out, and_6_out, and_7_out, and_8_out, and_9_out, and_10_out,
       and_15_out, and_16_out, and_17_out, and_18_out, and_19_out, and_20_out, and_21_out, and_22_out,
       and_23_out, and_24_out, and_25_out, and_26_out, and_33_out, and_34_out, and_35_out, and_36_out,
       and_37_out, and_38_out, and_39_out, and_40_out, and_41_out, and_42_out, and_43_out, and_44_out,
       and_45_out, and_46_out, and_47_out, and_48_out, and_49_out, and_50_out, and_51_out, and_52_out,
       and_53_out, and_54_out, and_55_out, and_56_out, and_57_out, and_58_out, and_59_out, and_60_out,
       and_61_out, and_62_out, and_63_out, and_64_out, and_65_out, not_1_out, not_2_out, not_3_out,
       not_4_out, not_5_out, not_6_out, not_7_out, not_8_out, not_9_out, not_10_out, not_11_out, not_12_out,
       not_13_out, not_14_out, not_15_out, not_16_out, not_17_out, not_18_out, not_19_out, not_20_out,
       not_21_out, not_22_out, not_23_out, not_24_out, not_25_out, not_26_out, not_27_out, not_28_out,
       not_29_out, not_30_out, not_31_out, not_32_out, not_33_out, not_34_out, not_35_out, not_36_out,
       not_37_out, not_38_out, not_39_out, not_40_out, not_41_out, not_42_out, not_43_out, not_44_out,
       not_45_out, not_46_out, not_47_out, not_48_out, not_49_out, not_50_out, not_51_out, not_52_out,
       not_53_out, not_54_out, not_55_out, not_56_out, not_57_out, not_58_out, not_59_out, not_60_out,
       not_61_out, not_62_out, not_63_out, not_64_out, not_65_out, not_66_out, not_67_out, not_68_out,
       not_69_out, not_70_out, not_71_out, not_72_out, not_73_out, not_74_out, not_75_out, not_76_out,
       not_77_out, not_78_out, not_79_out, not_80_out, not_81_out, not_82_out, not_83_out, not_84_out,
       not_85_out, not_86_out, not_87_out, not_88_out, not_89_out, not_90_out, not_91_out, not_92_out,
       not_93_out, not_94_out, not_95_out, not_96_out, not_97_out, not_98_out, not_99_out, not_100_out,
       not_101_out, not_102_out, not_103_out, not_104_out, not_105_out, not_106_out, not_107_out,
       not_108_out, not_109_out, not_110_out, not_111_out, not_112_out, not_113_out, not_114_out,
       not_115_out, not_116_out, not_117_out, not_118_out, not_119_out, not_120_out, not_121_out,
       not_122_out, not_123_out, not_124_out, not_125_out, not_126_out, not_127_out, not_128_out,
       not_129_out, not_130_out, not_131_out, not_132_out, not_133_out, not_134_out, not_135_out,
       not_136_out, not_137_out, not_138_out, not_139_out, not_140_out, not_141_out, not_142_out,
       not_143_out, not_144_out, not_145_out, not_146_out, not_147_out, not_148_out, not_149_out,
       not_150_out, not_151_out, not_152_out, not_153_out, not_154_out, not_155_out, not_156_out,
       not_157_out, not_158_out, not_159_out, not_160_out, not_161_out, not_162_out, not_163_out,
       not_164_out, not_165_out, not_166_out, not_167_out, not_168_out, not_169_out, not_170_out,
       not_171_out, not_172_out, not_173_out, not_174_out, not_175_out, not_176_out, not_177_out,
       not_178_out, not_179_out, not_180_out, not_181_out, not_182_out, not_183_out, not_184_out,
       not_185_out, not_186_out, not_187_out, not_188_out, not_189_out, not_190_out, not_191_out,
       not_192_out, not_193_out, not_194_out, not_195_out, not_196_out, not_197_out, not_198_out,
       not_199_out, not_200_out, not_201_out, not_202_out, not_203_out, not_204_out, not_205_out,
       not_206_out, not_207_out, not_208_out, not_209_out, not_210_out, not_211_out, not_212_out,
       not_213_out, not_214_out, not_215_out, not_216_out, not_217_out, not_218_out, not_219_out,
       not_220_out, not_221_out, not_222_out, not_223_out, not_224_out, not_225_out, not_226_out,
       not_227_out, not_228_out, not_229_out, not_230_out, not_231_out, not_232_out, not_233_out,
       not_234_out, not_235_out, not_236_out, not_237_out, not_238_out, not_239_out, not_240_out,
       not_241_out, not_242_out, not_243_out, not_244_out, not_245_out, not_246_out, not_247_out,
       not_248_out, not_249_out, not_250_out, not_251_out, not_252_out, not_253_out, not_254_out,
       not_255_out, not_256_out, not_257_out, not_258_out, not_259_out, not_260_out, not_261_out,
       not_262_out, not_263_out, not_264_out, not_265_out, not_266_out, not_267_out, not_268_out,
       not_269_out, not_270_out, not_271_out, not_272_out, not_273_out, not_274_out, not_275_out,
       not_276_out, not_277_out, not_278_out, not_279_out, not_280_out, not_281_out, not_282_out,
       not_283_out, not_284_out, not_285_out, not_286_out, not_287_out, not_288_out, not_289_out,
       not_290_out, not_291_out, not_292_out, not_293_out, not_294_out, not_295_out, not_296_out,
       not_297_out, not_298_out, not_299_out, not_300_out, not_301_out, not_302_out, not_303_out,
       not_304_out, not_305_out, not_306_out, not_307_out, not_308_out, not_309_out, not_310_out,
       not_311_out, not_312_out, not_313_out, not_314_out, not_315_out, not_316_out, not_317_out,
       not_318_out, not_319_out, not_320_out, not_321_out, not_322_out, not_323_out, not_324_out,
       not_325_out, not_326_out, not_327_out, not_328_out, not_329_out, not_330_out, not_331_out,
       not_332_out, not_333_out, not_334_out, not_335_out, not_336_out, not_337_out, not_338_out,
       not_339_out, not_340_out, not_341_out, not_342_out, not_343_out, not_344_out, not_345_out,
       not_346_out, not_347_out, not_348_out, not_349_out, not_350_out, not_351_out, not_352_out,
       not_353_out, not_354_out, not_355_out, not_356_out, not_357_out, not_358_out, not_359_out,
       not_360_out, not_361_out, not_362_out, not_363_out, not_364_out, not_365_out, not_366_out,
       not_367_out, not_368_out, not_369_out, not_370_out, not_371_out, not_372_out, not_373_out,
       not_374_out, not_375_out, not_376_out, not_377_out, not_378_out, not_379_out, not_380_out,
       not_381_out, not_382_out, not_383_out;

  not not_1 (not_1_out, OP2);
  not not_2 (not_2_out, OP3);
  not not_3 (not_3_out, OP4);
  not not_4 (not_4_out, OP5);
  not not_5 (not_5_out, OP6);
  not not_6 (not_6_out, F12);
  not not_7 (not_7_out, F14);
  not not_8 (not_8_out, OP2);
  not not_9 (not_9_out, OP3);
  not not_10 (not_10_out, OP4);
  not not_11 (not_11_out, OP5);
  not not_12 (not_12_out, OP6);
  not not_13 (not_13_out, F13);
  not not_14 (not_14_out, F14);
  not not_15 (not_15_out, OP2);
  not not_16 (not_16_out, OP3);
  not not_17 (not_17_out, OP4);
  not not_18 (not_18_out, OP6);
  not not_19 (not_19_out, F12);
  not not_20 (not_20_out, F14);
  not not_21 (not_21_out, OP2);
  not not_22 (not_22_out, OP3);
  not not_23 (not_23_out, OP4);
  not not_24 (not_24_out, OP6);
  not not_25 (not_25_out, F12);
  not not_26 (not_26_out, F14);
  not not_27 (not_27_out, OP2);
  not not_28 (not_28_out, OP3);
  not not_29 (not_29_out, OP4);
  not not_30 (not_30_out, OP5);
  not not_31 (not_31_out, OP6);
  not not_32 (not_32_out, F13);
  not not_33 (not_33_out, F14);
  not not_34 (not_34_out, OP2);
  not not_35 (not_35_out, OP3);
  not not_36 (not_36_out, OP5);
  not not_37 (not_37_out, OP6);
  not not_38 (not_38_out, F12);
  not not_39 (not_39_out, OP2);
  not not_40 (not_40_out, OP3);
  not not_41 (not_41_out, OP5);
  not not_42 (not_42_out, OP6);
  not not_43 (not_43_out, F13);
  not not_44 (not_44_out, F25);
  not not_45 (not_45_out, F30);
  not not_46 (not_46_out, OP2);
  not not_47 (not_47_out, OP3);
  not not_48 (not_48_out, OP5);
  not not_49 (not_49_out, OP6);
  not not_50 (not_50_out, F25);
  not not_51 (not_51_out, OP2);
  not not_52 (not_52_out, OP3);
  not not_53 (not_53_out, OP5);
  not not_54 (not_54_out, OP6);
  not not_55 (not_55_out, OP3);
  not not_56 (not_56_out, OP4);
  not not_57 (not_57_out, F12);
  not not_58 (not_58_out, F13);
  not not_59 (not_59_out, F14);
  not not_60 (not_60_out, OP2);
  not not_61 (not_61_out, OP3);
  not not_62 (not_62_out, OP6);
  not not_63 (not_63_out, F12);
  not not_64 (not_64_out, F13);
  not not_65 (not_65_out, F25);
  not not_66 (not_66_out, F30);
  not not_67 (not_67_out, OP2);
  not not_68 (not_68_out, OP3);
  not not_69 (not_69_out, OP4);
  not not_70 (not_70_out, F13);
  not not_71 (not_71_out, OP2);
  not not_72 (not_72_out, OP3);
  not not_73 (not_73_out, OP4);
  not not_74 (not_74_out, OP5);
  not not_75 (not_75_out, OP6);
  not not_76 (not_76_out, F13);
  not not_77 (not_77_out, F14);
  not not_78 (not_78_out, OP3);
  not not_79 (not_79_out, OP5);
  not not_80 (not_80_out, OP6);
  not not_81 (not_81_out, OP2);
  not not_82 (not_82_out, OP3);
  not not_83 (not_83_out, OP5);
  not not_84 (not_84_out, OP6);
  not not_85 (not_85_out, F12);
  not not_86 (not_86_out, F14);
  not not_87 (not_87_out, OP2);
  not not_88 (not_88_out, OP3);
  not not_89 (not_89_out, OP4);
  not not_90 (not_90_out, OP5);
  not not_91 (not_91_out, OP6);
  not not_92 (not_92_out, F13);
  not not_93 (not_93_out, F14);
  not not_94 (not_94_out, OP2);
  not not_95 (not_95_out, OP3);
  not not_96 (not_96_out, OP6);
  not not_97 (not_97_out, F12);
  not not_98 (not_98_out, F13);
  not not_99 (not_99_out, F14);
  not not_100 (not_100_out, F25);
  not not_101 (not_101_out, OP2);
  not not_102 (not_102_out, OP3);
  not not_103 (not_103_out, OP6);
  not not_104 (not_104_out, F12);
  not not_105 (not_105_out, F25);
  not not_106 (not_106_out, F30);
  not not_107 (not_107_out, OP3);
  not not_108 (not_108_out, OP5);
  not not_109 (not_109_out, OP6);
  not not_110 (not_110_out, F12);
  not not_111 (not_111_out, OP3);
  not not_112 (not_112_out, OP5);
  not not_113 (not_113_out, OP6);
  not not_114 (not_114_out, F13);
  not not_115 (not_115_out, F25);
  not not_116 (not_116_out, F30);
  not not_117 (not_117_out, OP3);
  not not_118 (not_118_out, OP5);
  not not_119 (not_119_out, OP6);
  not not_120 (not_120_out, F25);
  not not_121 (not_121_out, OP3);
  not not_122 (not_122_out, OP5);
  not not_123 (not_123_out, OP6);
  not not_124 (not_124_out, OP2);
  not not_125 (not_125_out, OP3);
  not not_126 (not_126_out, OP6);
  not not_127 (not_127_out, F25);
  not not_128 (not_128_out, F30);
  not not_129 (not_129_out, OP4);
  not not_130 (not_130_out, F12);
  not not_131 (not_131_out, F13);
  not not_132 (not_132_out, F14);
  not not_133 (not_133_out, OP3);
  not not_134 (not_134_out, OP5);
  not not_135 (not_135_out, OP6);
  not not_136 (not_136_out, OP4);
  not not_137 (not_137_out, OP2);
  not not_138 (not_138_out, OP3);
  not not_139 (not_139_out, F12);
  not not_140 (not_140_out, F13);
  not not_141 (not_141_out, F14);
  not not_142 (not_142_out, F25);
  not not_143 (not_143_out, F30);
  not not_144 (not_144_out, OP2);
  not not_145 (not_145_out, OP3);
  not not_146 (not_146_out, OP4);
  not not_147 (not_147_out, OP6);
  not not_148 (not_148_out, F12);
  not not_149 (not_149_out, F14);
  not not_150 (not_150_out, OP2);
  not not_151 (not_151_out, OP3);
  not not_152 (not_152_out, OP4);
  not not_153 (not_153_out, F12);
  not not_154 (not_154_out, F13);
  not not_155 (not_155_out, F14);
  not not_156 (not_156_out, OP2);
  not not_157 (not_157_out, OP3);
  not not_158 (not_158_out, OP4);
  not not_159 (not_159_out, F13);
  not not_160 (not_160_out, F14);
  not not_161 (not_161_out, OP3);
  not not_162 (not_162_out, OP4);
  not not_163 (not_163_out, F12);
  not not_164 (not_164_out, F13);
  not not_165 (not_165_out, F14);
  not not_166 (not_166_out, OP4);
  not not_167 (not_167_out, F30);
  not not_168 (not_168_out, F25);
  not not_169 (not_169_out, F14);
  not not_170 (not_170_out, F13);
  not not_171 (not_171_out, F12);
  not not_172 (not_172_out, OP6);
  not not_173 (not_173_out, OP3);
  not not_174 (not_174_out, OP2);
  not not_175 (not_175_out, F25);
  not not_176 (not_176_out, F14);
  not not_177 (not_177_out, F13);
  not not_178 (not_178_out, F12);
  not not_179 (not_179_out, OP6);
  not not_180 (not_180_out, OP3);
  not not_181 (not_181_out, OP2);
  not not_182 (not_182_out, F30);
  not not_183 (not_183_out, F25);
  not not_184 (not_184_out, OP6);
  not not_185 (not_185_out, OP3);
  not not_186 (not_186_out, OP2);
  not not_187 (not_187_out, F30);
  not not_188 (not_188_out, F25);
  not not_189 (not_189_out, F12);
  not not_190 (not_190_out, OP6);
  not not_191 (not_191_out, OP3);
  not not_192 (not_192_out, OP2);
  not not_193 (not_193_out, F30);
  not not_194 (not_194_out, F25);
  not not_195 (not_195_out, F14);
  not not_196 (not_196_out, F12);
  not not_197 (not_197_out, OP6);
  not not_198 (not_198_out, OP3);
  not not_199 (not_199_out, OP2);
  not not_200 (not_200_out, F30);
  not not_201 (not_201_out, F25);
  not not_202 (not_202_out, F14);
  not not_203 (not_203_out, OP6);
  not not_204 (not_204_out, OP3);
  not not_205 (not_205_out, OP2);
  not not_206 (not_206_out, F14);
  not not_207 (not_207_out, F13);
  not not_208 (not_208_out, F12);
  not not_209 (not_209_out, OP6);
  not not_210 (not_210_out, OP5);
  not not_211 (not_211_out, OP3);
  not not_212 (not_212_out, OP2);
  not not_213 (not_213_out, OP6);
  not not_214 (not_214_out, OP5);
  not not_215 (not_215_out, OP3);
  not not_216 (not_216_out, OP2);
  not not_217 (not_217_out, F12);
  not not_218 (not_218_out, OP6);
  not not_219 (not_219_out, OP5);
  not not_220 (not_220_out, OP3);
  not not_221 (not_221_out, OP2);
  not not_222 (not_222_out, F13);
  not not_223 (not_223_out, F12);
  not not_224 (not_224_out, OP6);
  not not_225 (not_225_out, OP5);
  not not_226 (not_226_out, OP3);
  not not_227 (not_227_out, OP2);
  not not_228 (not_228_out, F14);
  not not_229 (not_229_out, F12);
  not not_230 (not_230_out, OP6);
  not not_231 (not_231_out, OP5);
  not not_232 (not_232_out, OP3);
  not not_233 (not_233_out, OP2);
  not not_234 (not_234_out, F30);
  not not_235 (not_235_out, F25);
  not not_236 (not_236_out, F14);
  not not_237 (not_237_out, F13);
  not not_238 (not_238_out, OP6);
  not not_239 (not_239_out, OP5);
  not not_240 (not_240_out, OP3);
  not not_241 (not_241_out, OP2);
  not not_242 (not_242_out, F30);
  not not_243 (not_243_out, F25);
  not not_244 (not_244_out, F13);
  not not_245 (not_245_out, OP6);
  not not_246 (not_246_out, OP5);
  not not_247 (not_247_out, OP3);
  not not_248 (not_248_out, OP2);
  not not_249 (not_249_out, F25);
  not not_250 (not_250_out, F13);
  not not_251 (not_251_out, OP6);
  not not_252 (not_252_out, OP5);
  not not_253 (not_253_out, OP3);
  not not_254 (not_254_out, OP2);
  not not_255 (not_255_out, F14);
  not not_256 (not_256_out, F12);
  not not_257 (not_257_out, OP6);
  not not_258 (not_258_out, OP5);
  not not_259 (not_259_out, OP4);
  not not_260 (not_260_out, OP3);
  not not_261 (not_261_out, OP2);
  not not_262 (not_262_out, F14);
  not not_263 (not_263_out, F12);
  not not_264 (not_264_out, OP6);
  not not_265 (not_265_out, OP4);
  not not_266 (not_266_out, OP3);
  not not_267 (not_267_out, OP2);
  not not_268 (not_268_out, F14);
  not not_269 (not_269_out, F13);
  not not_270 (not_270_out, F12);
  not not_271 (not_271_out, OP4);
  not not_272 (not_272_out, OP3);
  not not_273 (not_273_out, OP2);
  not not_274 (not_274_out, F14);
  not not_275 (not_275_out, F13);
  not not_276 (not_276_out, OP4);
  not not_277 (not_277_out, OP3);
  not not_278 (not_278_out, OP2);
  not not_279 (not_279_out, F14);
  not not_280 (not_280_out, F13);
  not not_281 (not_281_out, F12);
  not not_282 (not_282_out, OP4);
  not not_283 (not_283_out, OP3);
  not not_284 (not_284_out, F30);
  not not_285 (not_285_out, F25);
  not not_286 (not_286_out, F13);
  not not_287 (not_287_out, F12);
  not not_288 (not_288_out, OP6);
  not not_289 (not_289_out, OP3);
  not not_290 (not_290_out, OP2);
  not not_291 (not_291_out, F30);
  not not_292 (not_292_out, F25);
  not not_293 (not_293_out, F14);
  not not_294 (not_294_out, F13);
  not not_295 (not_295_out, F12);
  not not_296 (not_296_out, OP6);
  not not_297 (not_297_out, OP5);
  not not_298 (not_298_out, OP4);
  not not_299 (not_299_out, OP3);
  not not_300 (not_300_out, OP2);
  not not_301 (not_301_out, F30);
  not not_302 (not_302_out, F25);
  not not_303 (not_303_out, F14);
  not not_304 (not_304_out, F13);
  not not_305 (not_305_out, F12);
  not not_306 (not_306_out, OP6);
  not not_307 (not_307_out, OP5);
  not not_308 (not_308_out, OP4);
  not not_309 (not_309_out, OP3);
  not not_310 (not_310_out, OP2);
  not not_311 (not_311_out, F30);
  not not_312 (not_312_out, F25);
  not not_313 (not_313_out, F14);
  not not_314 (not_314_out, F13);
  not not_315 (not_315_out, F12);
  not not_316 (not_316_out, OP6);
  not not_317 (not_317_out, OP3);
  not not_318 (not_318_out, OP2);
  not not_319 (not_319_out, F25);
  not not_320 (not_320_out, F14);
  not not_321 (not_321_out, F13);
  not not_322 (not_322_out, F12);
  not not_323 (not_323_out, OP6);
  not not_324 (not_324_out, OP3);
  not not_325 (not_325_out, OP2);
  not not_326 (not_326_out, F30);
  not not_327 (not_327_out, F25);
  not not_328 (not_328_out, OP6);
  not not_329 (not_329_out, OP3);
  not not_330 (not_330_out, OP2);
  not not_331 (not_331_out, F30);
  not not_332 (not_332_out, F25);
  not not_333 (not_333_out, F12);
  not not_334 (not_334_out, OP6);
  not not_335 (not_335_out, OP3);
  not not_336 (not_336_out, OP2);
  not not_337 (not_337_out, F30);
  not not_338 (not_338_out, F25);
  not not_339 (not_339_out, F14);
  not not_340 (not_340_out, F12);
  not not_341 (not_341_out, OP6);
  not not_342 (not_342_out, OP3);
  not not_343 (not_343_out, OP2);
  not not_344 (not_344_out, F30);
  not not_345 (not_345_out, F25);
  not not_346 (not_346_out, F14);
  not not_347 (not_347_out, OP6);
  not not_348 (not_348_out, OP3);
  not not_349 (not_349_out, OP2);
  not not_350 (not_350_out, F14);
  not not_351 (not_351_out, F12);
  not not_352 (not_352_out, OP6);
  not not_353 (not_353_out, OP4);
  not not_354 (not_354_out, OP3);
  not not_355 (not_355_out, OP2);
  not not_356 (not_356_out, F14);
  not not_357 (not_357_out, F13);
  not not_358 (not_358_out, F12);
  not not_359 (not_359_out, OP4);
  not not_360 (not_360_out, OP3);
  not not_361 (not_361_out, OP2);
  not not_362 (not_362_out, F14);
  not not_363 (not_363_out, F13);
  not not_364 (not_364_out, OP4);
  not not_365 (not_365_out, OP3);
  not not_366 (not_366_out, OP2);
  not not_367 (not_367_out, F30);
  not not_368 (not_368_out, F25);
  not not_369 (not_369_out, F13);
  not not_370 (not_370_out, F12);
  not not_371 (not_371_out, OP6);
  not not_372 (not_372_out, OP3);
  not not_373 (not_373_out, OP2);
  not not_374 (not_374_out, F30);
  not not_375 (not_375_out, F25);
  not not_376 (not_376_out, F14);
  not not_377 (not_377_out, F13);
  not not_378 (not_378_out, F12);
  not not_379 (not_379_out, OP6);
  not not_380 (not_380_out, OP5);
  not not_381 (not_381_out, OP4);
  not not_382 (not_382_out, OP3);
  not not_383 (not_383_out, OP2);
  and and_1 (and_1_out, not_1_out, not_2_out, not_3_out, not_4_out, not_5_out, not_6_out, F13, not_7_out);
  and and_2 (and_2_out, not_8_out, not_9_out, not_10_out, not_11_out, not_12_out, F12, not_13_out, not_14_out);
  and and_3 (MemWrite, not_15_out, not_16_out, not_17_out, OP5, not_18_out, not_19_out, F13, not_20_out);
  and and_4 (and_4_out, not_21_out, not_22_out, not_23_out, not_24_out, not_25_out, F13, not_26_out);
  and and_5 (and_5_out, not_27_out, not_28_out, not_29_out, not_30_out, not_31_out, F12, not_32_out, not_33_out);
  and and_6 (and_6_out, not_34_out, not_35_out, OP4, not_36_out, not_37_out, not_38_out);
  and and_7 (and_7_out, not_39_out, not_40_out, OP4, not_41_out, not_42_out, not_43_out, not_44_out, not_45_out);
  and and_8 (and_8_out, not_46_out, not_47_out, OP4, not_48_out, not_49_out, F14, not_50_out);
  and and_9 (and_9_out, not_51_out, not_52_out, OP4, not_53_out, not_54_out, F13, F14);
  and and_10 (and_10_out, OP2, not_55_out, not_56_out, OP5, OP6, not_57_out, not_58_out, not_59_out);
  and and_11 (Xor, not_60_out, not_61_out, OP4, OP5, not_62_out, not_63_out, not_64_out, F14, not_65_out, not_66_out);
  and and_12 (Bge, not_67_out, not_68_out, not_69_out, OP5, OP6, F12, not_70_out, F14);
  and and_13 (Lh, not_71_out, not_72_out, not_73_out, not_74_out, not_75_out, F12, not_76_out, not_77_out);
  and and_14 (Auipc, OP2, not_78_out, OP4, not_79_out, not_80_out);
  and and_15 (and_15_out, not_81_out, not_82_out, not_83_out, not_84_out, not_85_out, F13, not_86_out);
  and and_16 (and_16_out, not_87_out, not_88_out, not_89_out, not_90_out, not_91_out, F12, not_92_out, not_93_out);
  and and_17 (and_17_out, not_94_out, not_95_out, OP4, not_96_out, not_97_out, not_98_out, not_99_out, not_100_out);
  and and_18 (and_18_out, not_101_out, not_102_out, OP4, not_103_out, not_104_out, not_105_out, not_106_out);
  and and_19 (and_19_out, not_107_out, OP4, not_108_out, not_109_out, not_110_out);
  and and_20 (and_20_out, not_111_out, OP4, not_112_out, not_113_out, not_114_out, not_115_out, not_116_out);
  and and_21 (and_21_out, not_117_out, OP4, not_118_out, not_119_out, F14, not_120_out);
  and and_22 (and_22_out, not_121_out, OP4, not_122_out, not_123_out, F13, F14);
  and and_23 (and_23_out, not_124_out, not_125_out, OP4, OP5, not_126_out, F13, not_127_out, not_128_out);
  and and_24 (and_24_out, OP2, not_129_out, OP5, OP6, not_130_out, not_131_out, not_132_out);
  and and_25 (and_25_out, OP2, not_133_out, OP4, not_134_out, not_135_out);
  and and_26 (and_26_out, OP2, OP3, not_136_out, OP5, OP6);
  and and_27 (ecall, not_137_out, not_138_out, OP4, OP5, OP6, not_139_out, not_140_out, not_141_out, not_142_out, not_143_out);
  and and_28 (S_Type, not_144_out, not_145_out, not_146_out, OP5, not_147_out, not_148_out, F13, not_149_out);
  and and_29 (BEQ, not_150_out, not_151_out, not_152_out, OP5, OP6, not_153_out, not_154_out, not_155_out);
  and and_30 (BNE, not_156_out, not_157_out, not_158_out, OP5, OP6, F12, not_159_out, not_160_out);
  and and_31 (JALR, OP2, not_161_out, not_162_out, OP5, OP6, not_163_out, not_164_out, not_165_out);
  and and_32 (JAL, OP2, OP3, not_166_out, OP5, OP6);
  and and_33 (and_33_out, not_167_out, not_168_out, not_169_out, not_170_out, not_171_out, not_172_out, OP5, OP4, not_173_out, not_174_out);
  and and_34 (and_34_out, F30, not_175_out, not_176_out, not_177_out, not_178_out, not_179_out, OP5, OP4, not_180_out, not_181_out);
  and and_35 (and_35_out, not_182_out, not_183_out, F14, F13, F12, not_184_out, OP5, OP4, not_185_out, not_186_out);
  and and_36 (and_36_out, not_187_out, not_188_out, F14, F13, not_189_out, not_190_out, OP5, OP4, not_191_out, not_192_out);
  and and_37 (and_37_out, not_193_out, not_194_out, not_195_out, F13, not_196_out, not_197_out, OP5, OP4, not_198_out, not_199_out);
  and and_38 (and_38_out, not_200_out, not_201_out, not_202_out, F13, F12, not_203_out, OP5, OP4, not_204_out, not_205_out);
  and and_39 (and_39_out, not_206_out, not_207_out, not_208_out, not_209_out, not_210_out, OP4, not_211_out, not_212_out);
  and and_40 (and_40_out, F14, F13, F12, not_213_out, not_214_out, OP4, not_215_out, not_216_out);
  and and_41 (and_41_out, F14, F13, not_217_out, not_218_out, not_219_out, OP4, not_220_out, not_221_out);
  and and_42 (and_42_out, F14, not_222_out, not_223_out, not_224_out, not_225_out, OP4, not_226_out, not_227_out);
  and and_43 (and_43_out, not_228_out, F13, not_229_out, not_230_out, not_231_out, OP4, not_232_out, not_233_out);
  and and_44 (and_44_out, not_234_out, not_235_out, not_236_out, not_237_out, F12, not_238_out, not_239_out, OP4, not_240_out, not_241_out);
  and and_45 (and_45_out, not_242_out, not_243_out, F14, not_244_out, F12, not_245_out, not_246_out, OP4, not_247_out, not_248_out);
  and and_46 (and_46_out, F30, not_249_out, F14, not_250_out, F12, not_251_out, not_252_out, OP4, not_253_out, not_254_out);
  and and_47 (and_47_out, not_255_out, F13, not_256_out, not_257_out, not_258_out, not_259_out, not_260_out, not_261_out);
  and and_48 (and_48_out, not_262_out, F13, not_263_out, not_264_out, OP5, not_265_out, not_266_out, not_267_out);
  and and_49 (and_49_out, not_268_out, not_269_out, not_270_out, OP6, OP5, not_271_out, not_272_out, not_273_out);
  and and_50 (and_50_out, not_274_out, not_275_out, F12, OP6, OP5, not_276_out, not_277_out, not_278_out);
  and and_51 (and_51_out, not_279_out, not_280_out, not_281_out, OP6, OP5, not_282_out, not_283_out, OP2);
  and and_52 (and_52_out, not_284_out, not_285_out, F14, not_286_out, not_287_out, not_288_out, OP5, OP4, not_289_out, not_290_out);
  and and_53 (and_53_out, not_291_out, not_292_out, not_293_out, not_294_out, not_295_out, not_296_out, not_297_out, not_298_out, not_299_out, not_300_out);
  and and_54 (and_54_out, not_301_out, not_302_out, not_303_out, not_304_out, not_305_out, not_306_out, not_307_out, not_308_out, not_309_out, not_310_out);
  and and_55 (and_55_out, not_311_out, not_312_out, not_313_out, not_314_out, not_315_out, not_316_out, OP5, OP4, not_317_out, not_318_out);
  and and_56 (and_56_out, F30, not_319_out, not_320_out, not_321_out, not_322_out, not_323_out, OP5, OP4, not_324_out, not_325_out);
  and and_57 (and_57_out, not_326_out, not_327_out, F14, F13, F12, not_328_out, OP5, OP4, not_329_out, not_330_out);
  and and_58 (and_58_out, not_331_out, not_332_out, F14, F13, not_333_out, not_334_out, OP5, OP4, not_335_out, not_336_out);
  and and_59 (and_59_out, not_337_out, not_338_out, not_339_out, F13, not_340_out, not_341_out, OP5, OP4, not_342_out, not_343_out);
  and and_60 (and_60_out, not_344_out, not_345_out, not_346_out, F13, F12, not_347_out, OP5, OP4, not_348_out, not_349_out);
  and and_61 (and_61_out, not_350_out, F13, not_351_out, not_352_out, OP5, not_353_out, not_354_out, not_355_out);
  and and_62 (and_62_out, not_356_out, not_357_out, not_358_out, OP6, OP5, not_359_out, not_360_out, not_361_out);
  and and_63 (and_63_out, not_362_out, not_363_out, F12, OP6, OP5, not_364_out, not_365_out, not_366_out);
  and and_64 (and_64_out, not_367_out, not_368_out, F14, not_369_out, not_370_out, not_371_out, OP5, OP4, not_372_out, not_373_out);
  and and_65 (and_65_out, not_374_out, not_375_out, not_376_out, not_377_out, not_378_out, not_379_out, not_380_out, not_381_out, not_382_out, not_383_out);
  or or_1 (MemToReg, and_1_out, and_2_out);
  or or_2 (ALU_SRC, and_4_out, and_5_out, and_6_out, and_7_out, and_8_out, and_9_out, and_10_out);
  or or_3 (RegWrite, and_15_out, and_16_out, and_17_out, and_18_out, and_19_out, and_20_out, and_21_out, and_22_out, and_23_out, and_24_out, and_25_out, and_26_out);
  or or_4 (RtUsed, and_55_out, and_56_out, and_57_out, and_58_out, and_59_out, and_60_out, and_61_out, and_62_out, and_63_out, and_64_out, and_65_out);
  or or_5 (RsUsed, and_33_out, and_34_out, and_35_out, and_36_out, and_37_out, and_38_out, and_39_out, and_40_out, and_41_out, and_42_out, and_43_out, and_44_out, and_45_out, and_46_out, and_47_out, and_48_out, and_49_out, and_50_out, and_51_out, and_52_out, and_53_out, and_54_out);
endmodule

// ALU
module ALU (
  input  [31:0] X,
  input  [31:0] Y,
  input  [3:0] AluOP,
  output out_4,
  output Equal,
  output out_6,
  output [31:0] Result,
  output [31:0] Result_2
);

  wire [0:0] comparator_1_lt, comparator_2_lt;
  wire [31:0] adder_1_out, AND_out, divider_1_out, divider_1_rem, multiplier_1_cout, multiplier_1_out,
       NOR_out, OR_out, shifter_1_out, shifter_2_out, shifter_3_out, subtractor_1_out, XOR_out;

  assign AND_out = X & Y;  // AND_Gate AND, 32 bits wide
  assign OR_out = X | Y;  // OR_Gate OR, 32 bits wide
  Shifter #(.width(32), .shift("ll")) shifter_1 (.in(X), .\dist (Y[4:0]), .out(shifter_1_out));
  Shifter #(.width(32), .shift("ar")) shifter_2 (.in(X), .\dist (Y[4:0]), .out(shifter_2_out));
  Shifter #(.width(32), .shift("lr")) shifter_3 (.in(X), .\dist (Y[4:0]), .out(shifter_3_out));
  Multiplier #(.width(32)) multiplier_1 (.a(X), .b(Y), .out(multiplier_1_out), .cout(multiplier_1_cout));  // open: cin
  Divider #(.width(32)) divider_1 (.a(X), .b(Y), .out(divider_1_out), .rem(divider_1_rem));  // open: upper
  Adder #(.width(32)) adder_1 (.a(X), .b(Y), .out(adder_1_out));  // open: cin, cout
  Subtractor #(.width(32)) subtractor_1 (.a(X), .b(Y), .out(subtractor_1_out));  // open: bin, bout
  assign XOR_out = X ^ Y;  // XOR_Gate XOR, 32 bits wide
  assign NOR_out = ~(X | Y);  // NOR_Gate NOR, 32 bits wide
  Comparator #(.width(32), .mode("twosComplement")) comparator_1 (
    .a(X), .b(Y), .eq(Equal), .lt(comparator_1_lt[0]));  // open: gt
  Comparator #(.width(32), .mode("unsigned")) comparator_2 (.a(X), .b(Y), .lt(comparator_2_lt[0]));  // open: gt, eq
  Multiplexer #(.select(4), .width(32), .disabled("Z"), .enable("false")) multiplexer_1 (
    .in0(shifter_1_out), .in1(shifter_2_out), .in2(shifter_3_out), .in3(multiplier_1_out),
    .in4(divider_1_out), .in5(adder_1_out), .in6(subtractor_1_out), .in7(AND_out), .in8(OR_out),
    .in9(XOR_out), .in10(NOR_out), .in11({{31{1'b0}}, comparator_1_lt[0]}),
    .in12({{31{1'b0}}, comparator_2_lt[0]}), .in13({32{1'b0}}), .in14({32{1'b0}}), .in15({32{1'b0}}),
    .out(Result), .sel(AluOP));
  Multiplexer #(.select(4), .width(32), .disabled("Z"), .enable("false")) multiplexer_2 (
    .in0({32{1'b0}}), .in1({32{1'b0}}), .in2({32{1'b0}}), .in3(multiplier_1_cout), .in4(divider_1_rem),
    .in5({32{1'b0}}), .in6({32{1'b0}}), .in7({32{1'b0}}), .in8({32{1'b0}}), .in9({32{1'b0}}),
    .in10({32{1'b0}}), .in11({32{1'b0}}), .in12({32{1'b0}}), .in13({32{1'b0}}), .in14({32{1'b0}}),
    .in15({32{1'b0}}), .out(Result_2), .sel(AluOP));
  Multiplexer #(.select(4), .width(1), .disabled("Z"), .enable("false")) multiplexer_3 (
    .in0(1'b0), .in1(1'b0), .in2(1'b0), .in3(1'b0), .in4(1'b0), .in5(1'b0), .in6(1'b0), .in7(1'b0),
    .in8(1'b0), .in9(1'b0), .in10(1'b0), .in11(comparator_1_lt[0]), .in12(comparator_2_lt[0]), .in13(1'b0),
    .in14(1'b0), .in15(1'b0), .out(out_6), .sel(AluOP));
  not not_1 (out_4, out_6);

  // Other names for the same wires on the sheet: Result2[31:0] = Result_2; S[3:0] = AluOP; tunnel = out_6;
  //   tunnel_t = out_4

  // Notes on the sheet:
  //   不要改变此引脚区域内容，也不要改变ALU封装形式
  //   输入引脚
  //   输出引脚
endmodule

module Regifile (
  input  [31:0] Din,
  input  Clk,
  input  WE,
  input  [4:0] R1_num,
  input  [4:0] W_num,
  input  [4:0] R2_num,
  output [31:0] R1,
  output [31:0] R2
);

  // RegisterFile registerfile_1: pin names not known; wires that end beside it: Din, Clk, WE, W_num, R1_num, R2_num, R1, R2
endmodule

module \理想流水线  (
);


  // Notes on the sheet:
  //   本文件仅包含动态预测电路
  //   请见cpu21-riscv-2(理想流水线).circ的“理想流水线”
endmodule

module \气泡流水线  (
);


  // Notes on the sheet:
  //   本文件仅包含动态预测电路
  //   请见cpu21-riscv-3(气泡流水线).circ的“气泡流水线”
endmodule

module \重定向流水线  (
);


  // Notes on the sheet:
  //   本文件仅包含动态预测电路
  //   请见cpu21-riscv-4(重定向流水线).circ的“重定向流水线”
endmodule

module \中断按键参考电路  (
  input  \同步清零信号 ,
  output \与中断屏蔽位与 
);

  wire \_1号中断_out , and_1_out, clock_1_out, d_ff_1_q, or_1_out, or_2_out;

  Clock #(.highDuration(1), .lowDuration(1)) clock_1 (.out(clock_1_out));
  Button \_1号中断  (.out(\_1号中断_out ));
  LED #(.active("true")) \_1号中断等待指示灯  (.in(or_1_out));
  or or_1 (or_1_out, \与中断屏蔽位与 , d_ff_1_q);
  D_Flip_Flop #(.trigger("rising"), .Pre_Clr_Positions("LEGACY"), .NegatePresetClear("false"), .enable("true"), .NewFFLayout("false")) d_ff_1 (
    .clk(\_1号中断_out ), .D(1'b1), .Q(d_ff_1_q), .reset(\与中断屏蔽位与 ));  // open: Qn, preset, en
  or or_2 (or_2_out, d_ff_1_q, \与中断屏蔽位与 );
  and and_1 (and_1_out, or_2_out, ~\同步清零信号 );  // AND_Gate
  D_Flip_Flop #(.trigger("rising"), .Pre_Clr_Positions("LEGACY"), .NegatePresetClear("false"), .enable("true"), .NewFFLayout("false")) IR1 (
    .clk(clock_1_out), .D(and_1_out), .Q(\与中断屏蔽位与 ));  // open: Qn, preset, en, reset

  // Notes on the sheet:
  //   中断信号采样参考电路
  //   Reset 
endmodule

module \单周期_单级中断  (
);


  // Notes on the sheet:
  //   本文件仅包含动态预测电路
  //   请见cpu21-riscv-5(单级中断).circ的“单周期+单级中断”
endmodule

module \单周期_多级中断  (
);


  // Notes on the sheet:
  //   本文件仅包含动态预测电路
  //   请见cpu21-riscv-6(多级中断).circ的“单周期+多级中断”
endmodule

module \封装正确性测试  (
);

  \单周期RISC_V  \u_单周期risc_v_1  ();
  \气泡流水线  \u_气泡流水线_1  ();
  \单周期_单级中断  \u_单周期_单级中断_1  ();
  \理想流水线  \u_理想流水线_1  ();
  \重定向流水线  \u_重定向流水线_1  ();
  \单周期_多级中断  \u_单周期_多级中断_1  ();

  // Notes on the sheet:
  //   单周期封装测试
  //   气泡流水封装测试
  //   单周期+单级中断封装测试
  //   请检查上面封装有无位宽不匹配，引脚标签是否和连接的标签相对应，否则无法在educoder平台上正确测试
  //   理想流水封装测试
  //   重定向流水封装测试
  //   单周期+多级中断封装测试
endmodule

module IF_ID (
  input  IF_PredictJump,
  input  [31:0] RD,
  input  [31:0] IF_PC,
  input  reset,
  input  en,
  input  clk,
  output ID_PredictJump,
  output [31:0] RD_2,
  output [31:0] ID_PC
);

  wire multiplexer_1_out;
  wire [31:0] multiplexer_2_out, multiplexer_3_out;

  Multiplexer #(.select(1), .width(1), .disabled("Z"), .enable("false")) multiplexer_1 (
    .in0(IF_PredictJump), .in1(1'b0), .out(multiplexer_1_out), .sel(reset));
  Multiplexer #(.select(1), .width(32), .disabled("Z"), .enable("false")) multiplexer_2 (
    .in0(RD), .in1({32{1'b0}}), .out(multiplexer_2_out), .sel(reset));
  Multiplexer #(.select(1), .width(32), .disabled("Z"), .enable("false")) multiplexer_3 (
    .in0(IF_PC), .in1({32{1'b0}}), .out(multiplexer_3_out), .sel(reset));
  Register #(.width(1), .trigger("rising"), .Select("low")) register_1 (
    .D(multiplexer_1_out), .en(en), .Q(ID_PredictJump), .clk(clk));  // open: clr
  Register #(.width(32), .trigger("rising"), .Select("low")) register_2 (
    .D(multiplexer_2_out), .en(en), .Q(RD_2), .clk(clk));  // open: clr
  Register #(.width(32), .trigger("rising"), .Select("low")) register_3 (
    .D(multiplexer_3_out), .en(en), .Q(ID_PC), .clk(clk));  // open: clr
endmodule

module ID_EX (
  input  ID_PredictJump,
  input  RegWrite,
  input  MemToReg,
  input  MemWrite,
  input  [1:0] RsForward,
  input  AluSrc,
  input  JAL,
  input  JALR,
  input  Bge,
  input  Beq,
  input  Bne,
  input  Lh,
  input  Auipc,
  input  [1:0] RtForward,
  input  [3:0] AluOp,
  input  [4:0] W_num,
  input  [31:0] RS,
  input  [31:0] RT,
  input  [31:0] SImm,
  input  [31:0] BImm,
  input  [31:0] JImm,
  input  [31:0] AImm,
  input  [31:0] ID_PC,
  input  [31:0] ID_IR,
  input  ID_ecall,
  input  reset,
  input  en,
  input  clk,
  output EX_PredictJump,
  output RegWrite_2,
  output MemToReg_2,
  output MemWrite_2,
  output [1:0] RsForward_2,
  output AluSrc_2,
  output JAL_2,
  output JALR_2,
  output Bge_2,
  output Beq_2,
  output Bne_2,
  output Lh_2,
  output Auipc_2,
  output [1:0] RtForward_2,
  output [3:0] AluOp_2,
  output [4:0] W_num_2,
  output [31:0] RS_2,
  output [31:0] RT_2,
  output [31:0] SImm_2,
  output [31:0] BImm_2,
  output [31:0] JImm_2,
  output [31:0] AImm_2,
  output [31:0] EX_PC,
  output [31:0] EX_IR,
  output EX_ecall
);

  wire multiplexer_1_out, multiplexer_2_out, multiplexer_3_out, multiplexer_4_out, multiplexer_6_out,
       multiplexer_7_out, multiplexer_8_out, multiplexer_9_out, multiplexer_10_out, multiplexer_11_out,
       multiplexer_12_out, multiplexer_13_out, multiplexer_25_out;
  wire [1:0] multiplexer_5_out, multiplexer_14_out;
  wire [3:0] multiplexer_15_out;
  wire [4:0] multiplexer_16_out;
  wire [31:0] multiplexer_17_out, multiplexer_18_out, multiplexer_19_out, multiplexer_20_out,
       multiplexer_21_out, multiplexer_22_out, multiplexer_23_out, multiplexer_24_out;

  Multiplexer #(.select(1), .width(1), .disabled("Z"), .enable("false")) multiplexer_1 (
    .in0(ID_PredictJump), .in1(1'b0), .out(multiplexer_1_out), .sel(reset));
  Multiplexer #(.select(1), .width(1), .disabled("Z"), .enable("false")) multiplexer_2 (
    .in0(RegWrite), .in1(1'b0), .out(multiplexer_2_out), .sel(reset));
  Multiplexer #(.select(1), .width(1), .disabled("Z"), .enable("false")) multiplexer_3 (
    .in0(MemToReg), .in1(1'b0), .out(multiplexer_3_out), .sel(reset));
  Multiplexer #(.select(1), .width(1), .disabled("Z"), .enable("false")) multiplexer_4 (
    .in0(MemWrite), .in1(1'b0), .out(multiplexer_4_out), .sel(reset));
  Multiplexer #(.select(1), .width(2), .disabled("Z"), .enable("false")) multiplexer_5 (
    .in0(RsForward), .in1(2'b00), .out(multiplexer_5_out), .sel(reset));
  Multiplexer #(.select(1), .width(1), .disabled("Z"), .enable("false")) multiplexer_6 (
    .in0(AluSrc), .in1(1'b0), .out(multiplexer_6_out), .sel(reset));
  Multiplexer #(.select(1), .width(1), .disabled("Z"), .enable("false")) multiplexer_7 (
    .in0(JAL), .in1(1'b0), .out(multiplexer_7_out), .sel(reset));
  Multiplexer #(.select(1), .width(1), .disabled("Z"), .enable("false")) multiplexer_8 (
    .in0(JALR), .in1(1'b0), .out(multiplexer_8_out), .sel(reset));
  Multiplexer #(.select(1), .width(1), .disabled("Z"), .enable("false")) multiplexer_9 (
    .in0(Bge), .in1(1'b0), .out(multiplexer_9_out), .sel(reset));
  Multiplexer #(.select(1), .width(1), .disabled("Z"), .enable("false")) multiplexer_10 (
    .in0(Beq), .in1(1'b0), .out(multiplexer_10_out), .sel(reset));
  Multiplexer #(.select(1), .width(1), .disabled("Z"), .enable("false")) multiplexer_11 (
    .in0(Bne), .in1(1'b0), .out(multiplexer_11_out), .sel(reset));
  Multiplexer #(.select(1), .width(1), .disabled("Z"), .enable("false")) multiplexer_12 (
    .in0(Lh), .in1(1'b0), .out(multiplexer_12_out), .sel(reset));
  Multiplexer #(.select(1), .width(1), .disabled("Z"), .enable("false")) multiplexer_13 (
    .in0(Auipc), .in1(1'b0), .out(multiplexer_13_out), .sel(reset));
  Multiplexer #(.select(1), .width(2), .disabled("Z"), .enable("false")) multiplexer_14 (
    .in0(RtForward), .in1(2'b00), .out(multiplexer_14_out), .sel(reset));
  Multiplexer #(.select(1), .width(4), .disabled("Z"), .enable("false")) multiplexer_15 (
    .in0(AluOp), .in1(4'b0000), .out(multiplexer_15_out), .sel(reset));
  Multiplexer #(.select(1), .width(5), .disabled("Z"), .enable("false")) multiplexer_16 (
    .in0(W_num), .in1({5{1'b0}}), .out(multiplexer_16_out), .sel(reset));
  Multiplexer #(.select(1), .width(32), .disabled("Z"), .enable("false")) multiplexer_17 (
    .in0(RS), .in1({32{1'b0}}), .out(multiplexer_17_out), .sel(reset));
  Multiplexer #(.select(1), .width(32), .disabled("Z"), .enable("false")) multiplexer_18 (
    .in0(RT), .in1({32{1'b0}}), .out(multiplexer_18_out), .sel(reset));
  Multiplexer #(.select(1), .width(32), .disabled("Z"), .enable("false")) multiplexer_19 (
    .in0(SImm), .in1({32{1'b0}}), .out(multiplexer_19_out), .sel(reset));
  Multiplexer #(.select(1), .width(32), .disabled("Z"), .enable("false")) multiplexer_20 (
    .in0(BImm), .in1({32{1'b0}}), .out(multiplexer_20_out), .sel(reset));
  Multiplexer #(.select(1), .width(32), .disabled("Z"), .enable("false")) multiplexer_21 (
    .in0(JImm), .in1({32{1'b0}}), .out(multiplexer_21_out), .sel(reset));
  Multiplexer #(.select(1), .width(32), .disabled("Z"), .enable("false")) multiplexer_22 (
    .in0(AImm), .in1({32{1'b0}}), .out(multiplexer_22_out), .sel(reset));
  Multiplexer #(.select(1), .width(32), .disabled("Z"), .enable("false")) multiplexer_23 (
    .in0(ID_PC), .in1({32{1'b0}}), .out(multiplexer_23_out), .sel(reset));
  Multiplexer #(.select(1), .width(32), .disabled("Z"), .enable("false")) multiplexer_24 (
    .in0(ID_IR), .in1({32{1'b0}}), .out(multiplexer_24_out), .sel(reset));
  Multiplexer #(.select(1), .width(1), .disabled("Z"), .enable("false")) multiplexer_25 (
    .in0(ID_ecall), .in1(1'b0), .out(multiplexer_25_out), .sel(reset));
  Register #(.width(1), .trigger("rising"), .Select("low")) register_1 (
    .D(multiplexer_1_out), .en(en), .Q(EX_PredictJump), .clk(clk));  // open: clr
  Register #(.width(1), .trigger("rising"), .Select("low")) register_2 (
    .D(multiplexer_2_out), .en(en), .Q(RegWrite_2), .clk(clk));  // open: clr
  Register #(.width(1), .trigger("rising"), .Select("low")) register_3 (
    .D(multiplexer_3_out), .en(en), .Q(MemToReg_2), .clk(clk));  // open: clr
  Register #(.width(1), .trigger("rising"), .Select("low")) register_4 (
    .D(multiplexer_4_out), .en(en), .Q(MemWrite_2), .clk(clk));  // open: clr
  Register #(.width(2), .trigger("rising"), .Select("low")) register_5 (
    .D(multiplexer_5_out), .en(en), .Q(RsForward_2), .clk(clk));  // open: clr
  Register #(.width(1), .trigger("rising"), .Select("low")) register_6 (
    .D(multiplexer_6_out), .en(en), .Q(AluSrc_2), .clk(clk));  // open: clr
  Register #(.width(1), .trigger("rising"), .Select("low")) register_7 (
    .D(multiplexer_7_out), .en(en), .Q(JAL_2), .clk(clk));  // open: clr
  Register #(.width(1), .trigger("rising"), .Select("low")) register_8 (
    .D(multiplexer_8_out), .en(en), .Q(JALR_2), .clk(clk));  // open: clr
  Register #(.width(1), .trigger("rising"), .Select("low")) register_9 (
    .D(multiplexer_9_out), .en(en), .Q(Bge_2), .clk(clk));  // open: clr
  Register #(.width(1), .trigger("rising"), .Select("low")) register_10 (
    .D(multiplexer_10_out), .en(en), .Q(Beq_2), .clk(clk));  // open: clr
  Register #(.width(1), .trigger("rising"), .Select("low")) register_11 (
    .D(multiplexer_11_out), .en(en), .Q(Bne_2), .clk(clk));  // open: clr
  Register #(.width(1), .trigger("rising"), .Select("low")) register_12 (
    .D(multiplexer_12_out), .en(en), .Q(Lh_2), .clk(clk));  // open: clr
  Register #(.width(1), .trigger("rising"), .Select("low")) register_13 (
    .D(multiplexer_13_out), .en(en), .Q(Auipc_2), .clk(clk));  // open: clr
  Register #(.width(2), .trigger("rising"), .Select("low")) register_14 (
    .D(multiplexer_14_out), .en(en), .Q(RtForward_2), .clk(clk));  // open: clr
  Register #(.width(4), .trigger("rising"), .Select("low")) register_15 (
    .D(multiplexer_15_out), .en(en), .Q(AluOp_2), .clk(clk));  // open: clr
  Register #(.width(5), .trigger("rising"), .Select("low")) register_16 (
    .D(multiplexer_16_out), .en(en), .Q(W_num_2), .clk(clk));  // open: clr
  Register #(.width(32), .trigger("rising"), .Select("low")) register_17 (
    .D(multiplexer_17_out), .en(en), .Q(RS_2), .clk(clk));  // open: clr
  Register #(.width(32), .trigger("rising"), .Select("low")) register_18 (
    .D(multiplexer_18_out), .en(en), .Q(RT_2), .clk(clk));  // open: clr
  Register #(.width(32), .trigger("rising"), .Select("low")) register_19 (
    .D(multiplexer_19_out), .en(en), .Q(SImm_2), .clk(clk));  // open: clr
  Register #(.width(32), .trigger("rising"), .Select("low")) register_20 (
    .D(multiplexer_20_out), .en(en), .Q(BImm_2), .clk(clk));  // open: clr
  Register #(.width(32), .trigger("rising"), .Select("low")) register_21 (
    .D(multiplexer_21_out), .en(en), .Q(JImm_2), .clk(clk));  // open: clr
  Register #(.width(32), .trigger("rising"), .Select("low")) register_22 (
    .D(multiplexer_22_out), .en(en), .Q(AImm_2), .clk(clk));  // open: clr
  Register #(.width(32), .trigger("rising"), .Select("low")) register_23 (
    .D(multiplexer_23_out), .en(en), .Q(EX_PC), .clk(clk));  // open: clr
  Register #(.width(32), .trigger("rising"), .Select("low")) register_24 (
    .D(multiplexer_24_out), .en(en), .Q(EX_IR), .clk(clk));  // open: clr
  Register #(.width(1), .trigger("rising"), .Select("low")) register_25 (
    .D(multiplexer_25_out), .en(en), .Q(EX_ecall), .clk(clk));  // open: clr
endmodule

module EX_MEM (
  input  RegWrite,
  input  EX_ecall,
  input  Equal,
  input  MemToReg,
  input  MemWrite,
  input  JAL,
  input  JALR,
  input  Lh,
  input  Auipc,
  input  [4:0] W_num,
  input  [31:0] AluResult,
  input  [31:0] RT,
  input  [31:0] AuipcResult,
  input  [31:0] EX_PC,
  input  [31:0] EX_IR,
  input  reset,
  input  en,
  input  clk,
  output RegWrite_2,
  output MEM_ecall,
  output Equal_2,
  output MemToReg_2,
  output MemWrite_2,
  output JAL_2,
  output JALR_2,
  output Lh_2,
  output Auipc_2,
  output [4:0] W_num_2,
  output [31:0] AluResult_2,
  output [31:0] RT_2,
  output [31:0] AuipcResult_2,
  output [31:0] MEM_PC,
  output [31:0] MEM_IR
);

  wire multiplexer_1_out, multiplexer_2_out, multiplexer_3_out, multiplexer_4_out, multiplexer_5_out,
       multiplexer_6_out, multiplexer_7_out, multiplexer_8_out, multiplexer_9_out;
  wire [4:0] multiplexer_10_out;
  wire [31:0] multiplexer_11_out, multiplexer_12_out, multiplexer_13_out, multiplexer_14_out,
       multiplexer_15_out;

  Multiplexer #(.select(1), .width(1), .disabled("Z"), .enable("false")) multiplexer_1 (
    .in0(RegWrite), .in1(1'b0), .out(multiplexer_1_out), .sel(reset));
  Multiplexer #(.select(1), .width(1), .disabled("Z"), .enable("false")) multiplexer_2 (
    .in0(EX_ecall), .in1(1'b0), .out(multiplexer_2_out), .sel(reset));
  Multiplexer #(.select(1), .width(1), .disabled("Z"), .enable("false")) multiplexer_3 (
    .in0(Equal), .in1(1'b0), .out(multiplexer_3_out), .sel(reset));
  Multiplexer #(.select(1), .width(1), .disabled("Z"), .enable("false")) multiplexer_4 (
    .in0(MemToReg), .in1(1'b0), .out(multiplexer_4_out), .sel(reset));
  Multiplexer #(.select(1), .width(1), .disabled("Z"), .enable("false")) multiplexer_5 (
    .in0(MemWrite), .in1(1'b0), .out(multiplexer_5_out), .sel(reset));
  Multiplexer #(.select(1), .width(1), .disabled("Z"), .enable("false")) multiplexer_6 (
    .in0(JAL), .in1(1'b0), .out(multiplexer_6_out), .sel(reset));
  Multiplexer #(.select(1), .width(1), .disabled("Z"), .enable("false")) multiplexer_7 (
    .in0(JALR), .in1(1'b0), .out(multiplexer_7_out), .sel(reset));
  Multiplexer #(.select(1), .width(1), .disabled("Z"), .enable("false")) multiplexer_8 (
    .in0(Lh), .in1(1'b0), .out(multiplexer_8_out), .sel(reset));
  Multiplexer #(.select(1), .width(1), .disabled("Z"), .enable("false")) multiplexer_9 (
    .in0(Auipc), .in1(1'b0), .out(multiplexer_9_out), .sel(reset));
  Multiplexer #(.select(1), .width(5), .disabled("Z"), .enable("false")) multiplexer_10 (
    .in0(W_num), .in1({5{1'b0}}), .out(multiplexer_10_out), .sel(reset));
  Multiplexer #(.select(1), .width(32), .disabled("Z"), .enable("false")) multiplexer_11 (
    .in0(AluResult), .in1({32{1'b0}}), .out(multiplexer_11_out), .sel(reset));
  Multiplexer #(.select(1), .width(32), .disabled("Z"), .enable("false")) multiplexer_12 (
    .in0(RT), .in1({32{1'b0}}), .out(multiplexer_12_out), .sel(reset));
  Multiplexer #(.select(1), .width(32), .disabled("Z"), .enable("false")) multiplexer_13 (
    .in0(AuipcResult), .in1({32{1'b0}}), .out(multiplexer_13_out), .sel(reset));
  Multiplexer #(.select(1), .width(32), .disabled("Z"), .enable("false")) multiplexer_14 (
    .in0(EX_PC), .in1({32{1'b0}}), .out(multiplexer_14_out), .sel(reset));
  Multiplexer #(.select(1), .width(32), .disabled("Z"), .enable("false")) multiplexer_15 (
    .in0(EX_IR), .in1({32{1'b0}}), .out(multiplexer_15_out), .sel(reset));
  Register #(.width(1), .trigger("rising"), .Select("low")) register_1 (
    .D(multiplexer_1_out), .en(en), .Q(RegWrite_2), .clk(clk));  // open: clr
  Register #(.width(1), .trigger("rising"), .Select("low")) register_2 (
    .D(multiplexer_2_out), .en(en), .Q(MEM_ecall), .clk(clk));  // open: clr
  Register #(.width(1), .trigger("rising"), .Select("low")) register_3 (
    .D(multiplexer_3_out), .en(en), .Q(Equal_2), .clk(clk));  // open: clr
  Register #(.width(1), .trigger("rising"), .Select("low")) register_4 (
    .D(multiplexer_4_out), .en(en), .Q(MemToReg_2), .clk(clk));  // open: clr
  Register #(.width(1), .trigger("rising"), .Select("low")) register_5 (
    .D(multiplexer_5_out), .en(en), .Q(MemWrite_2), .clk(clk));  // open: clr
  Register #(.width(1), .trigger("rising"), .Select("low")) register_6 (
    .D(multiplexer_6_out), .en(en), .Q(JAL_2), .clk(clk));  // open: clr
  Register #(.width(1), .trigger("rising"), .Select("low")) register_7 (
    .D(multiplexer_7_out), .en(en), .Q(JALR_2), .clk(clk));  // open: clr
  Register #(.width(1), .trigger("rising"), .Select("low")) register_8 (
    .D(multiplexer_8_out), .en(en), .Q(Lh_2), .clk(clk));  // open: clr
  Register #(.width(1), .trigger("rising"), .Select("low")) register_9 (
    .D(multiplexer_9_out), .en(en), .Q(Auipc_2), .clk(clk));  // open: clr
  Register #(.width(5), .trigger("rising"), .Select("low")) register_10 (
    .D(multiplexer_10_out), .en(en), .Q(W_num_2), .clk(clk));  // open: clr
  Register #(.width(32), .trigger("rising"), .Select("low")) register_11 (
    .D(multiplexer_11_out), .en(en), .Q(AluResult_2), .clk(clk));  // open: clr
  Register #(.width(32), .trigger("rising"), .Select("low")) register_12 (
    .D(multiplexer_12_out), .en(en), .Q(RT_2), .clk(clk));  // open: clr
  Register #(.width(32), .trigger("rising"), .Select("low")) register_13 (
    .D(multiplexer_13_out), .en(en), .Q(AuipcResult_2), .clk(clk));  // open: clr
  Register #(.width(32), .trigger("rising"), .Select("low")) register_14 (
    .D(multiplexer_14_out), .en(en), .Q(MEM_PC), .clk(clk));  // open: clr
  Register #(.width(32), .trigger("rising"), .Select("low")) register_15 (
    .D(multiplexer_15_out), .en(en), .Q(MEM_IR), .clk(clk));  // open: clr
endmodule

module MEM_WB (
  input  MEM_ecall,
  input  Equal,
  input  RegWrite,
  input  MemToReg,
  input  JAL,
  input  JALR,
  input  Lh,
  input  Auipc,
  input  [4:0] W_num,
  input  [31:0] AluResult,
  input  [31:0] Data,
  input  [31:0] AuipcResult,
  input  [31:0] MEM_PC,
  input  [31:0] MEM_IR,
  input  [31:0] RT,
  input  reset,
  input  en,
  input  clk,
  output WB_ecall,
  output Equal_2,
  output RegWrite_2,
  output MemToReg_2,
  output JAL_2,
  output JALR_2,
  output Lh_2,
  output Auipc_2,
  output [4:0] W_num_2,
  output [31:0] AluResult_2,
  output [31:0] Data_2,
  output [31:0] AuipcResult_2,
  output [31:0] WB_PC,
  output [31:0] WB_IR,
  output [31:0] RT_2
);

  wire multiplexer_1_out, multiplexer_2_out, multiplexer_3_out, multiplexer_4_out, multiplexer_5_out,
       multiplexer_6_out, multiplexer_7_out, multiplexer_8_out;
  wire [4:0] multiplexer_9_out;
  wire [31:0] multiplexer_10_out, multiplexer_11_out, multiplexer_12_out, multiplexer_13_out,
       multiplexer_14_out, multiplexer_15_out;

  Multiplexer #(.select(1), .width(1), .disabled("Z"), .enable("false")) multiplexer_1 (
    .in0(MEM_ecall), .in1(1'b0), .out(multiplexer_1_out), .sel(reset));
  Multiplexer #(.select(1), .width(1), .disabled("Z"), .enable("false")) multiplexer_2 (
    .in0(Equal), .in1(1'b0), .out(multiplexer_2_out), .sel(reset));
  Multiplexer #(.select(1), .width(1), .disabled("Z"), .enable("false")) multiplexer_3 (
    .in0(RegWrite), .in1(1'b0), .out(multiplexer_3_out), .sel(reset));
  Multiplexer #(.select(1), .width(1), .disabled("Z"), .enable("false")) multiplexer_4 (
    .in0(MemToReg), .in1(1'b0), .out(multiplexer_4_out), .sel(reset));
  Multiplexer #(.select(1), .width(1), .disabled("Z"), .enable("false")) multiplexer_5 (
    .in0(JAL), .in1(1'b0), .out(multiplexer_5_out), .sel(reset));
  Multiplexer #(.select(1), .width(1), .disabled("Z"), .enable("false")) multiplexer_6 (
    .in0(JALR), .in1(1'b0), .out(multiplexer_6_out), .sel(reset));
  Multiplexer #(.select(1), .width(1), .disabled("Z"), .enable("false")) multiplexer_7 (
    .in0(Lh), .in1(1'b0), .out(multiplexer_7_out), .sel(reset));
  Multiplexer #(.select(1), .width(1), .disabled("Z"), .enable("false")) multiplexer_8 (
    .in0(Auipc), .in1(1'b0), .out(multiplexer_8_out), .sel(reset));
  Multiplexer #(.select(1), .width(5), .disabled("Z"), .enable("false")) multiplexer_9 (
    .in0(W_num), .in1({5{1'b0}}), .out(multiplexer_9_out), .sel(reset));
  Multiplexer #(.select(1), .width(32), .disabled("Z"), .enable("false")) multiplexer_10 (
    .in0(AluResult), .in1({32{1'b0}}), .out(multiplexer_10_out), .sel(reset));
  Multiplexer #(.select(1), .width(32), .disabled("Z"), .enable("false")) multiplexer_11 (
    .in0(Data), .in1({32{1'b0}}), .out(multiplexer_11_out), .sel(reset));
  Multiplexer #(.select(1), .width(32), .disabled("Z"), .enable("false")) multiplexer_12 (
    .in0(AuipcResult), .in1({32{1'b0}}), .out(multiplexer_12_out), .sel(reset));
  Multiplexer #(.select(1), .width(32), .disabled("Z"), .enable("false")) multiplexer_13 (
    .in0(MEM_PC), .in1({32{1'b0}}), .out(multiplexer_13_out), .sel(reset));
  Multiplexer #(.select(1), .width(32), .disabled("Z"), .enable("false")) multiplexer_14 (
    .in0(MEM_IR), .in1({32{1'b0}}), .out(multiplexer_14_out), .sel(reset));
  Multiplexer #(.select(1), .width(32), .disabled("Z"), .enable("false")) multiplexer_15 (
    .in0(RT), .in1({32{1'b0}}), .out(multiplexer_15_out), .sel(reset));
  Register #(.width(1), .trigger("rising"), .Select("low")) register_1 (
    .D(multiplexer_1_out), .en(en), .Q(WB_ecall), .clk(clk));  // open: clr
  Register #(.width(1), .trigger("rising"), .Select("low")) register_2 (
    .D(multiplexer_2_out), .en(en), .Q(Equal_2), .clk(clk));  // open: clr
  Register #(.width(1), .trigger("rising"), .Select("low")) register_3 (
    .D(multiplexer_3_out), .en(en), .Q(RegWrite_2), .clk(clk));  // open: clr
  Register #(.width(1), .trigger("rising"), .Select("low")) register_4 (
    .D(multiplexer_4_out), .en(en), .Q(MemToReg_2), .clk(clk));  // open: clr
  Register #(.width(1), .trigger("rising"), .Select("low")) register_5 (
    .D(multiplexer_5_out), .en(en), .Q(JAL_2), .clk(clk));  // open: clr
  Register #(.width(1), .trigger("rising"), .Select("low")) register_6 (
    .D(multiplexer_6_out), .en(en), .Q(JALR_2), .clk(clk));  // open: clr
  Register #(.width(1), .trigger("rising"), .Select("low")) register_7 (
    .D(multiplexer_7_out), .en(en), .Q(Lh_2), .clk(clk));  // open: clr
  Register #(.width(1), .trigger("rising"), .Select("low")) register_8 (
    .D(multiplexer_8_out), .en(en), .Q(Auipc_2), .clk(clk));  // open: clr
  Register #(.width(5), .trigger("rising"), .Select("low")) register_9 (
    .D(multiplexer_9_out), .en(en), .Q(W_num_2), .clk(clk));  // open: clr
  Register #(.width(32), .trigger("rising"), .Select("low")) register_10 (
    .D(multiplexer_10_out), .en(en), .Q(AluResult_2), .clk(clk));  // open: clr
  Register #(.width(32), .trigger("rising"), .Select("low")) register_11 (
    .D(multiplexer_11_out), .en(en), .Q(Data_2), .clk(clk));  // open: clr
  Register #(.width(32), .trigger("rising"), .Select("low")) register_12 (
    .D(multiplexer_12_out), .en(en), .Q(AuipcResult_2), .clk(clk));  // open: clr
  Register #(.width(32), .trigger("rising"), .Select("low")) register_13 (
    .D(multiplexer_13_out), .en(en), .Q(WB_PC), .clk(clk));  // open: clr
  Register #(.width(32), .trigger("rising"), .Select("low")) register_14 (
    .D(multiplexer_14_out), .en(en), .Q(WB_IR), .clk(clk));  // open: clr
  Register #(.width(32), .trigger("rising"), .Select("low")) register_15 (
    .D(multiplexer_15_out), .en(en), .Q(RT_2), .clk(clk));  // open: clr
endmodule

module \气泡  (
  input  ecall,
  input  RsUsed,
  input  RtUsed,
  input  EX_RegWrite,
  input  MEM_RegWrite,
  input  BranchTaken,
  input  [4:0] rs,
  input  [4:0] EX_W_num,
  input  [4:0] rt,
  input  [4:0] MEM_W_num,
  output Stall,
  output Flush
);

  wire and_1_out, and_2_out, and_3_out, and_4_out, and_5_out, and_6_out, and_7_out, and_8_out,
       comparator_1_eq, comparator_2_eq, comparator_3_eq, comparator_4_eq, comparator_5_eq, comparator_6_eq,
       comparator_7_eq, comparator_8_eq, comparator_9_eq, comparator_10_eq, not_1_out, not_2_out, or_1_out,
       or_2_out;

  Comparator #(.width(5), .mode("twosComplement")) comparator_1 (
    .a(5'b10001), .b(EX_W_num), .eq(comparator_1_eq));  // open: gt, lt
  Comparator #(.width(5), .mode("twosComplement")) comparator_2 (
    .a(EX_W_num), .b(5'b01010), .eq(comparator_2_eq));  // open: gt, lt
  Comparator #(.width(5), .mode("twosComplement")) comparator_3 (
    .a(5'b10001), .b(MEM_W_num), .eq(comparator_3_eq));  // open: gt, lt
  Comparator #(.width(5), .mode("twosComplement")) comparator_4 (
    .a(MEM_W_num), .b(5'b01010), .eq(comparator_4_eq));  // open: gt, lt
  and and_1 (and_1_out, EX_RegWrite, ecall);
  or or_1 (or_1_out, comparator_1_eq, comparator_2_eq);
  and and_2 (and_2_out, ecall, MEM_RegWrite);
  or or_2 (or_2_out, comparator_3_eq, comparator_4_eq);
  not not_1 (not_1_out, comparator_5_eq);
  Comparator #(.width(5), .mode("twosComplement")) comparator_5 (
    .a(rt), .b({5{1'b0}}), .eq(comparator_5_eq));  // open: gt, lt
  Comparator #(.width(5), .mode("twosComplement")) comparator_6 (
    .a(rs), .b({5{1'b0}}), .eq(comparator_6_eq));  // open: gt, lt
  not not_2 (not_2_out, comparator_6_eq);
  Comparator #(.width(5), .mode("twosComplement")) comparator_7 (
    .a(rs), .b(EX_W_num), .eq(comparator_7_eq));  // open: gt, lt
  Comparator #(.width(5), .mode("twosComplement")) comparator_8 (
    .a(rt), .b(EX_W_num), .eq(comparator_8_eq));  // open: gt, lt
  Comparator #(.width(5), .mode("twosComplement")) comparator_9 (
    .a(rs), .b(MEM_W_num), .eq(comparator_9_eq));  // open: gt, lt
  Comparator #(.width(5), .mode("twosComplement")) comparator_10 (
    .a(rt), .b(MEM_W_num), .eq(comparator_10_eq));  // open: gt, lt
  and and_3 (and_3_out, and_1_out, or_1_out);
  and and_4 (and_4_out, and_2_out, or_2_out);
  and and_5 (and_5_out, RsUsed, not_2_out, EX_RegWrite, comparator_7_eq);
  and and_6 (and_6_out, RtUsed, not_1_out, EX_RegWrite, comparator_8_eq);
  and and_7 (and_7_out, MEM_RegWrite, RsUsed, not_2_out, comparator_9_eq);
  and and_8 (and_8_out, RtUsed, not_1_out, MEM_RegWrite, comparator_10_eq);
  or or_3 (Stall, and_3_out, and_4_out, and_5_out, and_6_out, and_7_out, and_8_out);
  or or_4 (Flush, Stall, BranchTaken);

  // Notes on the sheet:
  //   rt
  //   rs
  //   rs
  //   rt
  //   rs
  //   rt
endmodule

module \重定向  (
  input  LH,
  input  RsUsed,
  input  [4:0] EX_W_num,
  input  EX_RegWrite,
  input  [4:0] rs,
  input  ecall,
  input  RtUsed,
  input  [4:0] MEM_W_num,
  input  MEM_RegWrite,
  input  [4:0] rt,
  input  EX_MemToReg,
  input  BranchTaken,
  output [1:0] RsFoward,
  output Flush,
  output [1:0] RtFoward,
  output Stall
);

  wire and_1_out, and_2_out, and_3_out, and_4_out, and_5_out, and_6_out, and_7_out, and_8_out, and_9_out,
       and_10_out, and_11_out, and_12_out, comparator_1_eq, comparator_2_eq, comparator_3_eq,
       comparator_4_eq, comparator_5_eq, comparator_6_eq, comparator_7_eq, comparator_8_eq, comparator_9_eq,
       comparator_10_eq, ecall1, ecall2, ecall3, ecall4, not_1_out, not_2_out, not_3_out, not_4_out,
       or_1_out, or_2_out, or_6_out;

  Comparator #(.width(5), .mode("twosComplement")) comparator_1 (
    .a({5{1'b0}}), .b(rs), .eq(comparator_1_eq));  // open: gt, lt
  not not_1 (not_1_out, comparator_1_eq);
  Comparator #(.width(5), .mode("twosComplement")) comparator_2 (
    .a(rs), .b(EX_W_num), .eq(comparator_2_eq));  // open: gt, lt
  not not_2 (not_2_out, comparator_3_eq);
  Comparator #(.width(5), .mode("twosComplement")) comparator_3 (
    .a({5{1'b0}}), .b(rt), .eq(comparator_3_eq));  // open: gt, lt
  Comparator #(.width(5), .mode("twosComplement")) comparator_4 (
    .a(rt), .b(EX_W_num), .eq(comparator_4_eq));  // open: gt, lt
  and and_1 (and_1_out, EX_RegWrite, ecall);
  and and_2 (and_2_out, EX_RegWrite, ecall);
  and and_3 (and_3_out, MEM_RegWrite, ecall);
  and and_4 (and_4_out, MEM_RegWrite, ecall);
  Comparator #(.width(5), .mode("twosComplement")) comparator_5 (
    .a(MEM_W_num), .b(rs), .eq(comparator_5_eq));  // open: gt, lt
  Comparator #(.width(5), .mode("twosComplement")) comparator_6 (
    .a(MEM_W_num), .b(rt), .eq(comparator_6_eq));  // open: gt, lt
  and and_5 (and_5_out, not_1_out, or_1_out);
  or or_1 (or_1_out, LH, RsUsed);
  and and_6 (and_6_out, RsUsed, not_1_out, comparator_2_eq, EX_MemToReg);
  and and_7 (and_7_out, EX_MemToReg, RtUsed, not_2_out, comparator_4_eq);
  and and_8 (and_8_out, RtUsed, not_2_out);
  Comparator #(.width(5), .mode("twosComplement")) comparator_7 (
    .a(EX_W_num), .b(5'b10001), .eq(comparator_7_eq));  // open: gt, lt
  Comparator #(.width(5), .mode("twosComplement")) comparator_8 (
    .a(EX_W_num), .b(5'b01010), .eq(comparator_8_eq));  // open: gt, lt
  Comparator #(.width(5), .mode("twosComplement")) comparator_9 (
    .a(MEM_W_num), .b(5'b10001), .eq(comparator_9_eq));  // open: gt, lt
  Comparator #(.width(5), .mode("twosComplement")) comparator_10 (
    .a(MEM_W_num), .b(5'b01010), .eq(comparator_10_eq));  // open: gt, lt
  and and_9 (and_9_out, comparator_5_eq, MEM_RegWrite, and_5_out);
  and and_10 (and_10_out, EX_RegWrite, comparator_2_eq, and_5_out);
  and and_11 (and_11_out, and_8_out, comparator_4_eq, EX_RegWrite);
  and and_12 (and_12_out, and_8_out, MEM_RegWrite, comparator_6_eq);
  and and_13 (ecall1, and_1_out, comparator_7_eq);
  and and_14 (ecall3, and_2_out, comparator_8_eq);
  and and_15 (ecall2, and_3_out, comparator_9_eq);
  and and_16 (ecall4, and_4_out, comparator_10_eq);
  or or_2 (or_2_out, ecall2, and_9_out);
  or or_3 (RsFoward[1], ecall1, and_10_out);
  or or_4 (Stall, and_6_out, and_7_out);
  or or_5 (RtFoward[1], ecall3, and_11_out);
  or or_6 (or_6_out, ecall4, and_12_out);
  and and_17 (RsFoward[0], or_2_out, not_3_out);
  not not_3 (not_3_out, RsFoward[1]);
  or or_7 (Flush, BranchTaken, Stall);
  not not_4 (not_4_out, RtFoward[1]);
  and and_18 (RtFoward[0], not_4_out, or_6_out);

  // Notes on the sheet:
  //   输入
  //   输出
endmodule

module \重定向动态预测  (
  output RegWrite,
  output MemWrite,
  output [31:0] IF_PC,
  output [31:0] ID_PC,
  output [31:0] EX_PC,
  output [31:0] M_PC,
  output [31:0] WB_PC,
  output [31:0] RDin,
  output [31:0] MDin,
  output [31:0] LedData
);

  wire AluSrcB, and_1_out, and_2_out, and_3_out, and_4_out, and_5_out, and_6_out, and_7_out, and_8_out,
       and_9_out, Auipc, Beq, Bge, Bne, BranchTaken, button_1_out, CLK, clock_1_out, clock_2_out,
       comparator_1_eq, comparator_1_lt, comparator_2_eq, comparator_3_eq, d_ff_1_q, Equal, EX_Branch,
       EX_ecall, EX_JAL, EX_JALR, ex_mem_1_auipc_2, ex_mem_1_equal_2, ex_mem_1_jal_2, ex_mem_1_jalr_2,
       ex_mem_1_lh_2, ex_mem_1_mem_ecall, ex_mem_1_memtoreg_2, ex_mem_1_regwrite_2, EX_PredictJump, Flush,
       Gequal, Go, halt, ID_ecall, id_ex_1_alusrc_2, id_ex_1_auipc_2, id_ex_1_beq_2, id_ex_1_bge_2,
       id_ex_1_bne_2, id_ex_1_lh_2, id_ex_1_memtoreg_2, id_ex_1_memwrite_2, id_ex_1_regwrite_2,
       if_id_1_id_predictjump, IF_PredictJump, IR1, IR2, IR3, JAL, JALR, Lh, mem_wb_1_auipc_2,
       mem_wb_1_equal_2, mem_wb_1_jal_2, mem_wb_1_jalr_2, mem_wb_1_lh_2, mem_wb_1_memtoreg_2,
       mem_wb_1_wb_ecall, nand_1_out, not_1_out, not_2_out, not_3_out, not_4_out, not_5_out, not_6_out,
       not_7_out, not_8_out, not_10_out, not_11_out, or_2_out, or_3_out, or_7_out, Predicterror, RST, S_type,
       stall, URET, W1, W2, W3, \单周期硬布线控制器_1_memtoreg , \单周期硬布线控制器_1_memwrite , \单周期硬布线控制器_1_regwrite ,
       \单周期硬布线控制器_1_rsused , \单周期硬布线控制器_1_rtused , \无条件分支 , \有条件分支 ;
  wire [1:0] id_ex_1_rsforward_2, id_ex_1_rtforward_2, priority_encoder_1_out, RsForwad, RtForwad;
  wire [2:0] priority_encoder_2_out;
  wire [3:0] AluOP, id_ex_1_aluop_2;
  wire [4:0] ex_mem_1_w_num_2, id_ex_1_w_num_2, multiplexer_5_out, multiplexer_6_out, WBW_num;
  wire [11:0] multiplexer_7_out;
  wire [12:0] CNT_num;
  wire [15:0] \LoadUse次数 , multiplexer_11_out, \总周期数 , \插入气泡数 , \无条件分支数 , \条件分支成功数 ;
  wire [31:0] adder_5_out, adder_6_out, bit_extender_1_out, bit_extender_2_out, bit_extender_3_out,
       bit_extender_4_out, bit_extender_5_out, btb_1_btb_jumpaddr, EX_BranchAddr, EX_IR,
       ex_mem_1_auipcresult_2, EX_PC_4, id_ex_1_aimm_2, id_ex_1_bimm_2, id_ex_1_jimm_2, id_ex_1_rs_2,
       id_ex_1_rt_2, id_ex_1_simm_2, ID_IR, IF_IR, IF_PC_4, JALAddr, MEM_AluResult, MEM_IR,
       mem_wb_1_aluresult_2, mem_wb_1_auipcresult_2, mem_wb_1_data_2, mem_wb_1_rt_2, multiplexer_1_out,
       multiplexer_2_out, multiplexer_8_out, multiplexer_9_out, multiplexer_10_out, PredictAddr, ram_1_data,
       regifile_1_r1, regifile_1_r2, Result, shifter_1_out, shifter_2_out, shifter_3_out, WB_IR, \条件Addr ;

  Button \u_总复位  (.out(RST));
  Button _1 (.out(IR1));
  Button _2 (.out(IR2));
  Button _3 (.out(IR3));
  // Probe on \总周期数 
  // Probe on \总周期数 
  Button \u_继续运行  (.out(Go));
  LED #(.active("true")) led_1 (.in(W1));
  LED #(.active("true")) led_2 (.in(W2));
  LED #(.active("true")) led_3 (.in(W3));
  Hex_Digit_Display hex_digit_display_1 (.value(LedData[31:28]));  // open: dp
  // Probe on IF_PC[19:0]
  // RiscV_Probe riscv_probe_1: pin names not known; wires that end beside it: IF_IR
  Priority_Encoder #(.select(2), .disabled("Z")) priority_encoder_1 (
    .in0(1'b1), .in1(\有条件分支 ), .in2(EX_JAL), .in3(EX_JALR), .out(priority_encoder_1_out));  // open: gs, en_out, en_in
  Multiplexer #(.select(2), .width(32), .disabled("Z"), .enable("false")) multiplexer_1 (
    .in0(EX_PC_4), .in1(\条件Addr ), .in2(JALAddr), .in3(Result), .out(multiplexer_1_out),
    .sel(priority_encoder_1_out));
  Hex_Digit_Display hex_digit_display_2 (.value(LedData[27:24]));  // open: dp
  Hex_Digit_Display hex_digit_display_3 (.value(LedData[23:20]));  // open: dp
  // Probe on ID_PC[19:0]
  // RiscV_Probe riscv_probe_2: pin names not known; wires that end beside it: ID_IR
  or or_1 (\无条件分支 , EX_JAL, EX_JALR);
  Multiplexer #(.select(1), .width(32), .disabled("Z"), .enable("false")) multiplexer_2 (
    .in0(PredictAddr), .in1(multiplexer_1_out), .out(multiplexer_2_out), .sel(Predicterror));
  and and_1 (and_1_out, not_1_out, not_2_out);
  not not_1 (not_1_out, halt);
  not not_2 (not_2_out, stall);
  Multiplexer #(.select(3), .width(32), .disabled("Z"), .enable("false")) multiplexer_3 (
    .in0(IF_PC), .in1(JALAddr), .in2(Result), .in4(\条件Addr ), .out(EX_BranchAddr),
    .sel({\有条件分支 , EX_JALR, EX_JAL}));  // open: in3, in5, in6, in7
  Hex_Digit_Display hex_digit_display_4 (.value(LedData[19:16]));  // open: dp
  Hex_Digit_Display hex_digit_display_5 (.value(LedData[15:12]));  // open: dp
  Register #(.width(32), .trigger("rising"), .Select("low")) PC (
    .D(multiplexer_2_out), .en(and_1_out), .Q(IF_PC), .clk(CLK), .clr(RST));
  not not_3 (not_3_out, halt);
  Counter #(.width(16), .max('hffff), .ongoal("wrap"), .trigger("rising"), .behavior("new")) counter_1 (
    .count(not_3_out), .Q(\总周期数 ), .clk(CLK));  // open: load, D, carry, clr, preset, down
  Hex_Digit_Display hex_digit_display_6 (.value(LedData[7:4]));  // open: dp
  Hex_Digit_Display hex_digit_display_7 (.value(LedData[11:8]));  // open: dp
  Clock #(.highDuration(1), .lowDuration(1)) clock_1 (.out(clock_1_out));
  // Probe on EX_PC[19:0]
  // RiscV_Probe riscv_probe_3: pin names not known; wires that end beside it: clock_1_out, EX_IR, CLK
  // Probe on IF_PC
  Adder #(.width(32)) adder_1 (.a(IF_PC), .b(32'h4), .out(IF_PC_4));  // open: cin, cout
  Hex_Digit_Display hex_digit_display_8 (.value(LedData[3:0]));  // open: dp
  not not_4 (not_4_out, halt);
  and and_2 (and_2_out, \无条件分支 , not_4_out);
  Counter #(.width(16), .max('hffff), .ongoal("wrap"), .trigger("rising"), .behavior("new")) counter_2 (
    .count(and_2_out), .Q(\无条件分支数 ), .clk(CLK));  // open: load, D, carry, clr, preset, down
  // Probe on \总周期数 
  // Probe on M_PC[19:0]
  // RiscV_Probe riscv_probe_4: pin names not known; wires that end beside it: MEM_IR
  ROM #(.addrWidth(10), .dataWidth(32), .Select("high")) rom_1 (.addr(IF_PC[11:2]), .data(IF_IR));
  BTB btb_1 (
    .PC(IF_PC), .EX_PC(EX_PC), .EX_BranchAddr(EX_BranchAddr), .EX_Branch(EX_Branch),
    .EX_Branched(BranchTaken), .in_6(CLK), .ID_PredictJump(IF_PredictJump), .BTB_JumpAddr(btb_1_btb_jumpaddr));
  // Probe on \总周期数 
  // Probe on \无条件分支数 
  // Probe on \条件分支成功数 
  // Probe on \插入气泡数 
  // Probe on \LoadUse次数 
  or or_2 (or_2_out, Predicterror, RST);
  not not_5 (not_5_out, stall);
  // Probe on IF_PC[11:0]
  // Probe on WB_PC[19:0]
  // RiscV_Probe riscv_probe_5: pin names not known; wires that end beside it: WB_IR
  IF_ID if_id_1 (
    .RD(IF_IR), .IF_PC(IF_PC), .RD_2(ID_IR), .ID_PC(ID_PC), .reset(or_2_out), .en(not_5_out), .clk(CLK),
    .IF_PredictJump(IF_PredictJump), .ID_PredictJump(if_id_1_id_predictjump));
  Multiplexer #(.select(1), .width(32), .disabled("Z"), .enable("false")) multiplexer_4 (
    .in0(IF_PC_4), .in1(btb_1_btb_jumpaddr), .out(PredictAddr), .sel(IF_PredictJump));
  not not_6 (not_6_out, halt);
  and and_3 (and_3_out, \有条件分支 , not_6_out);
  Counter #(.width(16), .max('hffff), .ongoal("wrap"), .trigger("rising"), .behavior("new")) counter_3 (
    .count(and_3_out), .Q(\条件分支成功数 ), .clk(CLK));  // open: load, D, carry, clr, preset, down
  // Probe on ID_PC[11:0]
  // Probe on EX_PC[11:0]
  // RiscV_Probe riscv_probe_6: pin names not known; wires that end beside it: ID_IR
  // Probe on M_PC[11:0]
  D_Flip_Flop #(.trigger("high"), .Pre_Clr_Positions("LEGACY"), .NegatePresetClear("false"), .enable("true"), .NewFFLayout("false")) d_ff_1 (.Q(d_ff_1_q));  // open: clk, D, Qn, preset, en, reset
  // Probe on 13'hc
  not not_7 (not_7_out, halt);
  and and_4 (and_4_out, Flush, not_7_out);
  Counter #(.width(16), .max('hffff), .ongoal("wrap"), .trigger("rising"), .behavior("new")) counter_4 (
    .count(and_4_out), .Q(\插入气泡数 ), .clk(CLK));  // open: load, D, carry, clr, preset, down
  // Probe on WB_PC[11:0]
  Comparator #(.width(13), .mode("twosComplement")) comparator_1 (
    .a(CNT_num), .b(13'hc), .eq(comparator_1_eq), .lt(comparator_1_lt));  // open: gt
  Clock #(.highDuration(1), .lowDuration(1)) clock_2 (.out(clock_2_out));
  nand nand_1 (nand_1_out, d_ff_1_q, comparator_1_eq);
  Counter #(.width(13), .max('h1fff), .ongoal("stay"), .trigger("rising"), .behavior("old")) counter_5 (
    .count(comparator_1_lt), .Q(CNT_num), .clk(clock_2_out));  // open: load, D, carry, clr, preset
  \单周期硬布线控制器  \u_单周期硬布线控制器_1  (
    .Funct({ID_IR[30], ID_IR[25], ID_IR[14:12]}), .OP(ID_IR[6:2]), .ALU_OP(AluOP),
    .MemToReg(\单周期硬布线控制器_1_memtoreg ), .MemWrite(\单周期硬布线控制器_1_memwrite ), .ALU_SRC(AluSrcB),
    .ecall(ID_ecall), .S_type(S_type), .Jalr(JALR), .Beq(Beq), .JAL(JAL), .Bne(Bne), .in_3(ID_IR[21]),
    .uret(URET), .RegWrite(\单周期硬布线控制器_1_regwrite ), .Bge(Bge), .Lh(Lh), .Auipc(Auipc),
    .RsUsed(\单周期硬布线控制器_1_rsused ), .RtUsed(\单周期硬布线控制器_1_rtused ));  // open: xor
  Multiplexer #(.select(1), .width(5), .disabled("Z"), .enable("false")) multiplexer_5 (
    .in0(ID_IR[19:15]), .in1(5'b10001), .out(multiplexer_5_out), .sel(ID_ecall));
  Multiplexer #(.select(1), .width(5), .disabled("Z"), .enable("false")) multiplexer_6 (
    .in0(ID_IR[24:20]), .in1(5'b01010), .out(multiplexer_6_out), .sel(ID_ecall));
  Multiplexer #(.select(1), .width(12), .disabled("Z"), .enable("false")) multiplexer_7 (
    .in0(ID_IR[31:20]), .in1({ID_IR[31:25], ID_IR[11:7]}), .out(multiplexer_7_out), .sel(S_type));
  assign bit_extender_1_out = {{20{ID_IR[31]}}, {ID_IR[31], ID_IR[7], ID_IR[30:25], ID_IR[11:8]}};  // Bit_Extender bit_extender_1
  assign bit_extender_2_out = {{12{ID_IR[31]}}, {ID_IR[31], ID_IR[19:12], ID_IR[20], ID_IR[30:21]}};  // Bit_Extender bit_extender_2
  assign bit_extender_3_out = {{12{ID_IR[31]}}, ID_IR[31:12]};  // Bit_Extender bit_extender_3
  Comparator #(.width(1), .mode("twosComplement")) comparator_2 (
    .a(BranchTaken), .b(EX_PredictJump), .eq(comparator_2_eq));  // open: gt, lt
  Adder #(.width(32)) adder_2 (.a(EX_PC), .b(32'h4), .out(EX_PC_4));  // open: cin, cout
  not not_8 (not_8_out, halt);
  and and_5 (and_5_out, stall, not_8_out);
  assign CLK = nand_1_out ? clock_2_out : 1'bz;  // Controlled_Buffer controlled_buffer_1
  \重定向  \u_重定向_1  (
    .LH(Lh), .RsFoward(RsForwad), .Flush(Flush), .RsUsed(\单周期硬布线控制器_1_rsused ), .EX_W_num(id_ex_1_w_num_2),
    .EX_RegWrite(id_ex_1_regwrite_2), .rs(ID_IR[19:15]), .ecall(ID_ecall), .RtUsed(\单周期硬布线控制器_1_rtused ),
    .MEM_W_num(ex_mem_1_w_num_2), .MEM_RegWrite(ex_mem_1_regwrite_2), .rt(ID_IR[24:20]),
    .EX_MemToReg(id_ex_1_memtoreg_2), .RtFoward(RtForwad), .Stall(stall), .BranchTaken(Predicterror));
  assign bit_extender_4_out = {{20{multiplexer_7_out[11]}}, multiplexer_7_out};  // Bit_Extender bit_extender_4
  not not_9 (Predicterror, comparator_2_eq);
  Counter #(.width(16), .max('hffff), .ongoal("wrap"), .trigger("rising"), .behavior("new")) counter_6 (
    .count(and_5_out), .Q(\LoadUse次数 ), .clk(CLK));  // open: load, D, carry, clr, preset, down
  Pull_Resistor #(.pull(1)) pull_resistor_1 (.node(CLK));
  Regifile regifile_1 (
    .Din(RDin), .Clk(CLK), .R1(regifile_1_r1), .R2(regifile_1_r2), .WE(RegWrite), .W_num(WBW_num),
    .R1_num(multiplexer_5_out), .R2_num(multiplexer_6_out));
  or or_3 (or_3_out, Flush, RST);
  ID_EX id_ex_1 (
    .RegWrite(\单周期硬布线控制器_1_regwrite ), .MemToReg(\单周期硬布线控制器_1_memtoreg ), .MemWrite(\单周期硬布线控制器_1_memwrite ),
    .RsForward(RsForwad), .AluSrc(AluSrcB), .JAL(JAL), .JALR(JALR), .Bge(Bge), .Beq(Beq), .Bne(Bne), .Lh(Lh),
    .Auipc(Auipc), .RtForward(RtForwad), .AluOp(AluOP), .W_num(ID_IR[11:7]), .RS(regifile_1_r1),
    .RT(regifile_1_r2), .SImm(bit_extender_4_out), .BImm(bit_extender_1_out), .JImm(bit_extender_2_out),
    .AImm(bit_extender_3_out), .ID_PC(ID_PC), .RegWrite_2(id_ex_1_regwrite_2),
    .MemToReg_2(id_ex_1_memtoreg_2), .MemWrite_2(id_ex_1_memwrite_2), .RsForward_2(id_ex_1_rsforward_2),
    .AluSrc_2(id_ex_1_alusrc_2), .JAL_2(EX_JAL), .JALR_2(EX_JALR), .Bge_2(id_ex_1_bge_2),
    .Beq_2(id_ex_1_beq_2), .Bne_2(id_ex_1_bne_2), .Lh_2(id_ex_1_lh_2), .Auipc_2(id_ex_1_auipc_2),
    .RtForward_2(id_ex_1_rtforward_2), .AluOp_2(id_ex_1_aluop_2), .W_num_2(id_ex_1_w_num_2),
    .RS_2(id_ex_1_rs_2), .RT_2(id_ex_1_rt_2), .SImm_2(id_ex_1_simm_2), .BImm_2(id_ex_1_bimm_2),
    .JImm_2(id_ex_1_jimm_2), .AImm_2(id_ex_1_aimm_2), .EX_PC(EX_PC), .reset(or_3_out), .en(1'b1), .clk(CLK),
    .ID_IR(ID_IR), .EX_IR(EX_IR), .EX_ecall(EX_ecall), .ID_ecall(ID_ecall),
    .ID_PredictJump(if_id_1_id_predictjump), .EX_PredictJump(EX_PredictJump));
  Multiplexer #(.select(2), .width(32), .disabled("Z"), .enable("false")) multiplexer_8 (
    .in0(id_ex_1_rs_2), .in1(RDin), .in2(MEM_AluResult), .out(multiplexer_8_out), .sel(id_ex_1_rsforward_2));  // open: in3
  Multiplexer #(.select(2), .width(32), .disabled("Z"), .enable("false")) multiplexer_9 (
    .in0(id_ex_1_rt_2), .in1(RDin), .in2(MEM_AluResult), .out(multiplexer_9_out), .sel(id_ex_1_rtforward_2));  // open: in3
  Shifter #(.width(32), .shift("ll")) shifter_1 (.in(id_ex_1_bimm_2), .\dist (5'b00001), .out(shifter_1_out));
  Shifter #(.width(32), .shift("ll")) shifter_2 (.in(id_ex_1_jimm_2), .\dist (5'b00001), .out(shifter_2_out));
  Shifter #(.width(32), .shift("ll")) shifter_3 (.in(id_ex_1_aimm_2), .\dist (5'b01100), .out(shifter_3_out));
  Multiplexer #(.select(1), .width(32), .disabled("Z"), .enable("false")) multiplexer_10 (
    .in0(multiplexer_9_out), .in1(id_ex_1_simm_2), .out(multiplexer_10_out), .sel(id_ex_1_alusrc_2));
  or or_4 (BranchTaken, EX_JAL, EX_JALR, \有条件分支 );
  and and_6 (and_6_out, id_ex_1_beq_2, Equal);
  Comparator #(.width(32), .mode("twosComplement")) comparator_3 (
    .a(multiplexer_8_out), .b(32'ha), .eq(comparator_3_eq));  // open: gt, lt
  Adder #(.width(32)) adder_3 (.a(shifter_1_out), .b(EX_PC), .out(\条件Addr ));  // open: cin, cout
  Adder #(.width(32)) adder_4 (.a(shifter_2_out), .b(EX_PC), .out(JALAddr));  // open: cin, cout
  Adder #(.width(32)) adder_5 (.a(shifter_3_out), .b(EX_PC), .out(adder_5_out));  // open: cin, cout
  or or_5 (\有条件分支 , and_6_out, and_8_out, and_7_out);
  and and_7 (and_7_out, id_ex_1_bge_2, Gequal);
  and and_8 (and_8_out, not_10_out, id_ex_1_bne_2);
  not not_10 (not_10_out, Equal);
  ALU alu_1 (
    .X(multiplexer_8_out), .Y(multiplexer_10_out), .AluOP(id_ex_1_aluop_2), .Equal(Equal), .Result(Result),
    .out_4(Gequal));  // open: Result_2, out_6
  or or_6 (EX_Branch, EX_JAL, EX_JALR, id_ex_1_bge_2, id_ex_1_beq_2, id_ex_1_bne_2);
  EX_MEM ex_mem_1 (
    .RegWrite(id_ex_1_regwrite_2), .MemToReg(id_ex_1_memtoreg_2), .MemWrite(id_ex_1_memwrite_2),
    .JAL(EX_JAL), .JALR(EX_JALR), .Lh(id_ex_1_lh_2), .Auipc(id_ex_1_auipc_2), .W_num(id_ex_1_w_num_2),
    .AluResult(Result), .RT(multiplexer_9_out), .EX_PC(EX_PC), .RegWrite_2(ex_mem_1_regwrite_2),
    .MemToReg_2(ex_mem_1_memtoreg_2), .MemWrite_2(MemWrite), .JAL_2(ex_mem_1_jal_2),
    .JALR_2(ex_mem_1_jalr_2), .Lh_2(ex_mem_1_lh_2), .Auipc_2(ex_mem_1_auipc_2), .W_num_2(ex_mem_1_w_num_2),
    .AluResult_2(MEM_AluResult), .RT_2(MDin), .MEM_PC(M_PC), .reset(RST), .en(1'b1), .clk(CLK),
    .AuipcResult(adder_5_out), .AuipcResult_2(ex_mem_1_auipcresult_2), .EX_IR(EX_IR), .MEM_IR(MEM_IR),
    .Equal(comparator_3_eq), .Equal_2(ex_mem_1_equal_2), .EX_ecall(EX_ecall), .MEM_ecall(ex_mem_1_mem_ecall));
  Button button_1 (.out(button_1_out));
  // Probe on MEM_AluResult
  RAM #(.addrWidth(10), .dataWidth(32), .bus("separate"), .Select("high")) ram_1 (
    .addr(MEM_AluResult[11:2]), .din(MDin), .data(ram_1_data), .str(MemWrite), .sel(1'b1), .clk(CLK),
    .ld(1'b1), .clr(button_1_out));
  MEM_WB mem_wb_1 (
    .RegWrite(ex_mem_1_regwrite_2), .MemToReg(ex_mem_1_memtoreg_2), .JAL(ex_mem_1_jal_2),
    .JALR(ex_mem_1_jalr_2), .Lh(ex_mem_1_lh_2), .Auipc(ex_mem_1_auipc_2), .W_num(ex_mem_1_w_num_2),
    .AluResult(MEM_AluResult), .Data(ram_1_data), .AuipcResult(ex_mem_1_auipcresult_2), .MEM_PC(M_PC),
    .RegWrite_2(RegWrite), .MemToReg_2(mem_wb_1_memtoreg_2), .JAL_2(mem_wb_1_jal_2),
    .JALR_2(mem_wb_1_jalr_2), .Lh_2(mem_wb_1_lh_2), .Auipc_2(mem_wb_1_auipc_2), .W_num_2(WBW_num),
    .AluResult_2(mem_wb_1_aluresult_2), .Data_2(mem_wb_1_data_2), .AuipcResult_2(mem_wb_1_auipcresult_2),
    .WB_PC(WB_PC), .reset(RST), .en(1'b1), .clk(CLK), .WB_IR(WB_IR), .MEM_IR(MEM_IR),
    .Equal(ex_mem_1_equal_2), .Equal_2(mem_wb_1_equal_2), .MEM_ecall(ex_mem_1_mem_ecall),
    .WB_ecall(mem_wb_1_wb_ecall), .RT(MDin), .RT_2(mem_wb_1_rt_2));
  assign bit_extender_5_out = {{16{multiplexer_11_out[15]}}, multiplexer_11_out};  // Bit_Extender bit_extender_5
  Multiplexer #(.select(1), .width(16), .disabled("Z"), .enable("false")) multiplexer_11 (
    .in0(mem_wb_1_data_2[15:0]), .in1(mem_wb_1_data_2[31:16]), .out(multiplexer_11_out),
    .sel(mem_wb_1_aluresult_2[1]));
  and and_9 (and_9_out, mem_wb_1_wb_ecall, not_11_out);
  not not_11 (not_11_out, mem_wb_1_equal_2);
  D_Flip_Flop #(.trigger("rising"), .Pre_Clr_Positions("LEGACY"), .NegatePresetClear("false"), .enable("true"), .NewFFLayout("false")) d_ff_2 (
    .clk(mem_wb_1_equal_2), .D(1'b1), .Q(halt), .en(mem_wb_1_wb_ecall), .reset(Go));  // open: Qn, preset
  // Probe on mem_wb_1_aluresult_2
  // Probe on mem_wb_1_data_2
  Register #(.width(32), .trigger("rising"), .Select("low")) register_1 (
    .D(mem_wb_1_rt_2), .en(and_9_out), .Q(LedData), .clk(CLK));  // open: clr
  Adder #(.width(32)) adder_6 (.a(WB_PC), .b(32'h4), .out(adder_6_out));  // open: cin, cout
  or or_7 (or_7_out, mem_wb_1_jalr_2, mem_wb_1_jal_2);
  Priority_Encoder #(.select(3), .disabled("Z")) priority_encoder_2 (
    .in0(1'b1), .in1(mem_wb_1_memtoreg_2), .in2(or_7_out), .in3(mem_wb_1_auipc_2), .in4(mem_wb_1_lh_2),
    .out(priority_encoder_2_out));  // open: in5, in6, in7, gs, en_out, en_in
  Multiplexer #(.select(3), .width(32), .disabled("Z"), .enable("false")) multiplexer_12 (
    .in0(mem_wb_1_aluresult_2), .in1(mem_wb_1_data_2), .in2(adder_6_out), .in3(mem_wb_1_auipcresult_2),
    .in4(bit_extender_5_out), .out(RDin), .sel(priority_encoder_2_out));  // open: in5, in6, in7

  // Other names for the same wires on the sheet: W_num[4:0] = ID_IR[11:7]; rt[4:0] = ID_IR[24:20];
  //   rs[4:0] = ID_IR[19:15]; MEM_PC[31:0] = M_PC

  // Notes on the sheet:
  //   中断源
  //   时空图监测，可删除
  //   中断等待指示
  //   分支信号类型及对应跳转地址
  //   数码管输出
  //   指令存储器
  //   contents of rom_1 (hex, n*v repeats v):
  //   100493 100006f 100493 200913 300993 100006f 100493 200913 300993 100006f 100493 200913 300993
  //   100006f 100493 200913 300993 29c000ef 100413 100493 1f49493 900533 2200893 73 24d493 48463 fedff06f
  //   900533 2200893 73 100493 249493 900533 2200893 73 48463 fedff06f 100493 1f49493 900533 2200893 73
  //   4034d493 900533 2200893 73 4044d493 900533 2200893 73 4044d493 900533 2200893 73 4044d493 900533
  //   2200893 73 4044d493 900533 2200893 73 4044d493 900533 2200893 73 4044d493 900533 2200893 73 4044d493
  //   900533 2200893 73 100413 1f41993 41f9d993 433 c00913 300b13 140413 f47413 800293 100313 499993
  //   89e9b3 1300533 2200893 73 406282b3 fe0294e3 140413 f00f93 1f47433 1c41413 800293 100313 49d993
  //   89e9b3 1300533 2200893 73 406282b3 fe0294e3 1c45413 406b0b33 b0463 f95ff06f 2b3 fff2c293 829293
  //   ff2e293 500533 2200893 73 fff00413 493 84a023 140413 448493 84a023 140413 448493 84a023 140413
  //   448493 84a023 140413 448493 84a023 140413 448493 84a023 140413 448493 84a023 140413 448493 84a023
  //   140413 448493 84a023 140413 448493 84a023 140413 448493 84a023 140413 448493 84a023 140413 448493
  //   84a023 140413 448493 84a023 140413 448493 84a023 140413 448493 84a023 140413 448493 140413 433
  //   3c00493 42983 4aa03 149a2b3 28663 134a023 1442023 ffc48493 fe9412e3 800533 2200893 73 440413 3c00493
  //   fc9416e3 a00893 73 413 140413 800533 2200893 73 240413 800533 2200893 73 340413 800533 2200893 73
  //   440413 800533 2200893 73 540413 800533 2200893 73 640413 800533 2200893 73 740413 800533 2200893 73
  //   840413 800533 2200893 2200893 73 8067
  //   BTB表构建
  //   控制位
  //   指令探针
  //   流水调试日志用
  //   暂停节拍，不能为0
  //   rs1
  //   rs2
  //   指令字
  //   rd
  //   I
  //   s
  //   b
  //   j
  //   auipc
  //   戳工具置1进入计数暂停模式，ctrl+k时钟自动运行到对应节拍暂停
  //   ctrl+k关闭时钟连续运行，将控制位置零，进入单步调试模式调试
  //   RtUsed
  //   RsUsed
  //   Bne
  //   MemToReg
  //   MemWrite
  //   AluOP
  //   AluSrcB
  //   Xor
  //   S_type
  //   预测结果对比
  //   可计数暂停的时钟源
  //   为方便自动评测，需要输出流水线各段保存的PC值，注意是PC不是PC+4，另外ID段寄存器写入信息，Mem段内存写入信息也要输出
  //   数据存储器
endmodule
module BTB (
  input  [31:0] PC,
  input  [31:0] EX_PC,
  input  [31:0] EX_BranchAddr,
  input  EX_Branch,
  input  EX_Branched,
  input  in_6,
  output ID_PredictJump,
  output [31:0] BTB_JumpAddr
);

  wire and_17_out, and_26_out, and_27_out, and_28_out, and_29_out, and_30_out, and_31_out, and_32_out,
       and_33_out, comparator_1_eq, comparator_2_eq, comparator_3_eq, comparator_4_eq, comparator_5_eq,
       comparator_6_eq, comparator_7_eq, comparator_8_eq, comparator_9_eq, comparator_10_eq,
       comparator_11_eq, comparator_12_eq, comparator_13_eq, comparator_14_eq, comparator_15_eq,
       comparator_16_eq, d_ff_1_q, d_ff_2_q, d_ff_3_q, d_ff_4_q, d_ff_5_q, d_ff_6_q, d_ff_7_q, d_ff_8_q,
       decoder_1_out0, decoder_1_out1, decoder_1_out2, decoder_1_out3, decoder_1_out4, decoder_1_out5,
       decoder_1_out6, decoder_1_out7, decoder_2_out0, decoder_2_out1, decoder_2_out2, decoder_2_out3,
       decoder_2_out4, decoder_2_out5, decoder_2_out6, decoder_2_out7, EX_Hit, EX_Miss, L0, L1, L2, L3, L4,
       L5, L6, L7, M0, M1, M2, M3, M4, M5, M6, M7, not_1_out, not_2_out, not_3_out, not_4_out, not_5_out,
       not_6_out, not_7_out, not_8_out, or_1_out, or_2_out, or_3_out, or_4_out, or_5_out, or_6_out, or_7_out,
       or_8_out, or_11_out, or_12_out, or_13_out, or_14_out, or_15_out, or_16_out, or_17_out, or_18_out,
       original, priority_encoder_1_gs, v0, v1, v2, v3, v4, v5, v6, v7, write0, write1, write2, write3,
       write4, write5, write6, write7;
  wire [0:0] controlled_buffer_9_out, controlled_buffer_10_out, controlled_buffer_11_out,
       controlled_buffer_12_out, controlled_buffer_13_out, controlled_buffer_14_out,
       controlled_buffer_15_out, controlled_buffer_16_out;
  wire [1:0] fsm_1_nextlow, fsm_2_nextlow, fsm_3_nextlow, fsm_4_nextlow, fsm_5_nextlow, fsm_6_nextlow,
       fsm_7_nextlow, fsm_8_nextlow, multiplexer_1_out, multiplexer_2_out, multiplexer_3_out,
       multiplexer_4_out, multiplexer_5_out, multiplexer_6_out, multiplexer_7_out, multiplexer_8_out,
       predict0, predict1, predict2, predict3, predict4, predict5, predict6, predict7;
  wire [2:0] max_1_max_num, max_2_max_num, max_3_max_num, max_4_max_num, max_5_max_num, max_6_max_num,
       max_7_max_num, priority_encoder_1_out;
  wire [15:0] c0, c1, c2, c3, c4, c5, c6, c7, max_1_max, max_2_max, max_3_max, max_4_max, max_5_max,
       max_6_max;
  wire [31:0] register_17_q, register_18_q, register_19_q, register_20_q, register_21_q, register_22_q,
       register_23_q, register_24_q, tag0, tag1, tag2, tag3, tag4, tag5, tag6, tag7;

  LED #(.active("true")) led_1 (.in(v0));
  Register #(.width(1), .trigger("rising"), .Select("low")) register_1 (
    .D(1'b1), .en(write0), .Q(v0), .clk(in_6));  // open: clr
  LED #(.active("true")) led_2 (.in(v1));
  Register #(.width(1), .trigger("rising"), .Select("low")) register_2 (
    .D(1'b1), .en(write1), .Q(v1), .clk(in_6));  // open: clr
  LED #(.active("true")) led_3 (.in(v2));
  Register #(.width(1), .trigger("rising"), .Select("low")) register_3 (
    .D(1'b1), .en(write2), .Q(v2), .clk(in_6));  // open: clr
  LED #(.active("true")) led_4 (.in(v3));
  Register #(.width(1), .trigger("rising"), .Select("low")) register_4 (
    .D(1'b1), .en(write3), .Q(v3), .clk(in_6));  // open: clr
  LED #(.active("true")) led_5 (.in(v4));
  Register #(.width(1), .trigger("rising"), .Select("low")) register_5 (
    .D(1'b1), .en(write4), .Q(v4), .clk(in_6));  // open: clr
  LED #(.active("true")) led_6 (.in(v5));
  Register #(.width(1), .trigger("rising"), .Select("low")) register_6 (
    .D(1'b1), .en(write5), .Q(v5), .clk(in_6));  // open: clr
  LED #(.active("true")) led_7 (.in(v6));
  Register #(.width(1), .trigger("rising"), .Select("low")) register_7 (
    .D(1'b1), .en(write6), .Q(v6), .clk(in_6));  // open: clr
  Register #(.width(1), .trigger("rising"), .Select("low")) register_8 (
    .D(1'b1), .en(write7), .Q(v7), .clk(in_6));  // open: clr
  LED #(.active("true")) led_8 (.in(v7));
  // Probe on tag0
  Register #(.width(32), .trigger("rising"), .Select("low")) register_9 (
    .D(EX_PC), .en(write0), .Q(tag0), .clk(in_6));  // open: clr
  // Probe on tag1
  Register #(.width(32), .trigger("rising"), .Select("low")) register_10 (
    .D(EX_PC), .en(write1), .Q(tag1), .clk(in_6));  // open: clr
  // Probe on tag2
  Register #(.width(32), .trigger("rising"), .Select("low")) register_11 (
    .D(EX_PC), .en(write2), .Q(tag2), .clk(in_6));  // open: clr
  // Probe on tag3
  Register #(.width(32), .trigger("rising"), .Select("low")) register_12 (
    .D(EX_PC), .en(write3), .Q(tag3), .clk(in_6));  // open: clr
  // Probe on tag4
  Register #(.width(32), .trigger("rising"), .Select("low")) register_13 (
    .D(EX_PC), .en(write4), .Q(tag4), .clk(in_6));  // open: clr
  // Probe on tag5
  Register #(.width(32), .trigger("rising"), .Select("low")) register_14 (
    .D(EX_PC), .en(write5), .Q(tag5), .clk(in_6));  // open: clr
  Register #(.width(32), .trigger("rising"), .Select("low")) register_15 (
    .D(EX_PC), .en(write6), .Q(tag6), .clk(in_6));  // open: clr
  // Probe on tag7
  Register #(.width(32), .trigger("rising"), .Select("low")) register_16 (
    .D(EX_PC), .en(write7), .Q(tag7), .clk(in_6));  // open: clr
  // Probe on tag6
  Counter #(.width(16), .max('hffff), .ongoal("wrap"), .trigger("rising"), .behavior("new")) counter_1 (
    .Q(c0), .clk(in_6), .clr(d_ff_3_q));  // open: load, D, count, carry, preset, down
  or or_1 (or_1_out, write0, L0);
  Counter #(.width(16), .max('hffff), .ongoal("wrap"), .trigger("rising"), .behavior("new")) counter_2 (
    .Q(c1), .clk(in_6), .clr(d_ff_4_q));  // open: load, D, count, carry, preset, down
  or or_2 (or_2_out, write1, L1);
  Counter #(.width(16), .max('hffff), .ongoal("wrap"), .trigger("rising"), .behavior("new")) counter_3 (
    .Q(c2), .clk(in_6), .clr(d_ff_5_q));  // open: load, D, count, carry, preset, down
  or or_3 (or_3_out, write2, L2);
  Counter #(.width(16), .max('hffff), .ongoal("wrap"), .trigger("rising"), .behavior("new")) counter_4 (
    .Q(c3), .clk(in_6), .clr(d_ff_6_q));  // open: load, D, count, carry, preset, down
  or or_4 (or_4_out, write3, L3);
  Counter #(.width(16), .max('hffff), .ongoal("wrap"), .trigger("rising"), .behavior("new")) counter_5 (
    .Q(c4), .clk(in_6), .clr(d_ff_1_q));  // open: load, D, count, carry, preset, down
  D_Flip_Flop #(.trigger("rising"), .Pre_Clr_Positions("ABOVE_BELOW"), .NegatePresetClear("false"), .enable("false"), .NewFFLayout("false")) d_ff_1 (
    .clk(in_6), .D(or_5_out), .Q(d_ff_1_q));  // open: Qn, preset, reset
  or or_5 (or_5_out, write4, L4);
  Counter #(.width(16), .max('hffff), .ongoal("wrap"), .trigger("rising"), .behavior("new")) counter_6 (
    .Q(c5), .clk(in_6), .clr(d_ff_7_q));  // open: load, D, count, carry, preset, down
  or or_6 (or_6_out, write5, L5);
  Counter #(.width(16), .max('hffff), .ongoal("wrap"), .trigger("rising"), .behavior("new")) counter_7 (
    .Q(c6), .clk(in_6), .clr(d_ff_8_q));  // open: load, D, count, carry, preset, down
  or or_7 (or_7_out, write6, L6);
  Counter #(.width(16), .max('hffff), .ongoal("wrap"), .trigger("rising"), .behavior("new")) counter_8 (
    .Q(c7), .clk(in_6), .clr(d_ff_2_q));  // open: load, D, count, carry, preset, down
  D_Flip_Flop #(.trigger("rising"), .Pre_Clr_Positions("LEGACY"), .NegatePresetClear("false"), .enable("true"), .NewFFLayout("false")) d_ff_2 (
    .clk(in_6), .D(or_8_out), .Q(d_ff_2_q));  // open: Qn, preset, en, reset
  or or_8 (or_8_out, write7, L7);
  D_Flip_Flop #(.trigger("rising"), .Pre_Clr_Positions("ABOVE_BELOW"), .NegatePresetClear("false"), .enable("false"), .NewFFLayout("false")) d_ff_3 (
    .clk(in_6), .D(or_1_out), .Q(d_ff_3_q));  // open: Qn, preset, reset
  D_Flip_Flop #(.trigger("rising"), .Pre_Clr_Positions("ABOVE_BELOW"), .NegatePresetClear("false"), .enable("false"), .NewFFLayout("false")) d_ff_4 (
    .clk(in_6), .D(or_2_out), .Q(d_ff_4_q));  // open: Qn, preset, reset
  D_Flip_Flop #(.trigger("rising"), .Pre_Clr_Positions("ABOVE_BELOW"), .NegatePresetClear("false"), .enable("false"), .NewFFLayout("false")) d_ff_5 (
    .clk(in_6), .D(or_3_out), .Q(d_ff_5_q));  // open: Qn, preset, reset
  D_Flip_Flop #(.trigger("rising"), .Pre_Clr_Positions("ABOVE_BELOW"), .NegatePresetClear("false"), .enable("false"), .NewFFLayout("false")) d_ff_6 (
    .clk(in_6), .D(or_4_out), .Q(d_ff_6_q));  // open: Qn, preset, reset
  D_Flip_Flop #(.trigger("rising"), .Pre_Clr_Positions("ABOVE_BELOW"), .NegatePresetClear("false"), .enable("false"), .NewFFLayout("false")) d_ff_7 (
    .clk(in_6), .D(or_6_out), .Q(d_ff_7_q));  // open: Qn, preset, reset
  D_Flip_Flop #(.trigger("rising"), .Pre_Clr_Positions("LEGACY"), .NegatePresetClear("false"), .enable("true"), .NewFFLayout("false")) d_ff_8 (
    .clk(in_6), .D(or_7_out), .Q(d_ff_8_q));  // open: Qn, preset, en, reset
  Register #(.width(32), .trigger("rising"), .Select("low")) register_17 (
    .D(EX_BranchAddr), .en(write0), .Q(register_17_q), .clk(in_6));  // open: clr
  Register #(.width(32), .trigger("rising"), .Select("low")) register_18 (
    .D(EX_BranchAddr), .en(write1), .Q(register_18_q), .clk(in_6));  // open: clr
  Register #(.width(32), .trigger("rising"), .Select("low")) register_19 (
    .D(EX_BranchAddr), .en(write2), .Q(register_19_q), .clk(in_6));  // open: clr
  Register #(.width(32), .trigger("rising"), .Select("low")) register_20 (
    .D(EX_BranchAddr), .en(write3), .Q(register_20_q), .clk(in_6));  // open: clr
  Register #(.width(32), .trigger("rising"), .Select("low")) register_21 (
    .D(EX_BranchAddr), .en(write4), .Q(register_21_q), .clk(in_6));  // open: clr
  Register #(.width(32), .trigger("rising"), .Select("low")) register_22 (
    .D(EX_BranchAddr), .en(write5), .Q(register_22_q), .clk(in_6));  // open: clr
  Register #(.width(32), .trigger("rising"), .Select("low")) register_23 (
    .D(EX_BranchAddr), .en(write6), .Q(register_23_q), .clk(in_6));  // open: clr
  Register #(.width(32), .trigger("rising"), .Select("low")) register_24 (
    .D(EX_BranchAddr), .en(write7), .Q(register_24_q), .clk(in_6));  // open: clr
  assign BTB_JumpAddr = L0 ? register_17_q : 32'bz;  // Controlled_Buffer controlled_buffer_1
  assign BTB_JumpAddr = L1 ? register_18_q : 32'bz;  // Controlled_Buffer controlled_buffer_2
  assign BTB_JumpAddr = L2 ? register_19_q : 32'bz;  // Controlled_Buffer controlled_buffer_3
  assign BTB_JumpAddr = L3 ? register_20_q : 32'bz;  // Controlled_Buffer controlled_buffer_4
  assign BTB_JumpAddr = L4 ? register_21_q : 32'bz;  // Controlled_Buffer controlled_buffer_5
  assign BTB_JumpAddr = L5 ? register_22_q : 32'bz;  // Controlled_Buffer controlled_buffer_6
  assign BTB_JumpAddr = L6 ? register_23_q : 32'bz;  // Controlled_Buffer controlled_buffer_7
  assign BTB_JumpAddr = L7 ? register_24_q : 32'bz;  // Controlled_Buffer controlled_buffer_8
  Comparator #(.width(32), .mode("twosComplement")) comparator_1 (
    .a(tag0), .b(PC), .eq(comparator_1_eq));  // open: gt, lt
  Comparator #(.width(32), .mode("twosComplement")) comparator_2 (
    .a(tag1), .b(PC), .eq(comparator_2_eq));  // open: gt, lt
  Comparator #(.width(32), .mode("twosComplement")) comparator_3 (
    .a(tag2), .b(PC), .eq(comparator_3_eq));  // open: gt, lt
  Comparator #(.width(32), .mode("twosComplement")) comparator_4 (
    .a(tag3), .b(PC), .eq(comparator_4_eq));  // open: gt, lt
  Comparator #(.width(32), .mode("twosComplement")) comparator_5 (
    .a(tag4), .b(PC), .eq(comparator_5_eq));  // open: gt, lt
  Comparator #(.width(32), .mode("twosComplement")) comparator_6 (
    .a(tag5), .b(PC), .eq(comparator_6_eq));  // open: gt, lt
  Comparator #(.width(32), .mode("twosComplement")) comparator_7 (
    .a(tag6), .b(PC), .eq(comparator_7_eq));  // open: gt, lt
  Comparator #(.width(32), .mode("twosComplement")) comparator_8 (
    .a(tag7), .b(PC), .eq(comparator_8_eq));  // open: gt, lt
  and and_1 (L0, v0, comparator_1_eq);
  and and_2 (L1, v1, comparator_2_eq);
  and and_3 (L2, v2, comparator_3_eq);
  and and_4 (L3, v3, comparator_4_eq);
  and and_5 (L4, v4, comparator_5_eq);
  and and_6 (L5, v5, comparator_6_eq);
  and and_7 (L6, v6, comparator_7_eq);
  and and_8 (L7, v7, comparator_8_eq);
  Comparator #(.width(32), .mode("twosComplement")) comparator_9 (
    .a(tag0), .b(EX_PC), .eq(comparator_9_eq));  // open: gt, lt
  Comparator #(.width(32), .mode("twosComplement")) comparator_10 (
    .a(tag1), .b(EX_PC), .eq(comparator_10_eq));  // open: gt, lt
  Comparator #(.width(32), .mode("twosComplement")) comparator_11 (
    .a(tag2), .b(EX_PC), .eq(comparator_11_eq));  // open: gt, lt
  Comparator #(.width(32), .mode("twosComplement")) comparator_12 (
    .a(tag3), .b(EX_PC), .eq(comparator_12_eq));  // open: gt, lt
  Comparator #(.width(32), .mode("twosComplement")) comparator_13 (
    .a(tag4), .b(EX_PC), .eq(comparator_13_eq));  // open: gt, lt
  Comparator #(.width(32), .mode("twosComplement")) comparator_14 (
    .a(tag5), .b(EX_PC), .eq(comparator_14_eq));  // open: gt, lt
  Comparator #(.width(32), .mode("twosComplement")) comparator_15 (
    .a(tag6), .b(EX_PC), .eq(comparator_15_eq));  // open: gt, lt
  Comparator #(.width(32), .mode("twosComplement")) comparator_16 (
    .a(tag7), .b(EX_PC), .eq(comparator_16_eq));  // open: gt, lt
  and and_9 (M0, v0, comparator_9_eq);
  and and_10 (M1, v1, comparator_10_eq);
  and and_11 (M2, v2, comparator_11_eq);
  and and_12 (M3, v3, comparator_12_eq);
  and and_13 (M4, v4, comparator_13_eq);
  and and_14 (M5, v5, comparator_14_eq);
  and and_15 (M6, v6, comparator_15_eq);
  and and_16 (M7, v7, comparator_16_eq);
  not not_1 (not_1_out, v0);
  not not_2 (not_2_out, v1);
  not not_3 (not_3_out, v2);
  not not_4 (not_4_out, v3);
  not not_5 (not_5_out, v4);
  not not_6 (not_6_out, v5);
  not not_7 (not_7_out, v6);
  not not_8 (not_8_out, v7);
  MAX max_1 (.Y(c1), .X(c0), .Y_num(3'b001), .X_num(3'b000), .MAX(max_1_max), .Max_num(max_1_max_num));
  MAX max_2 (.Y(c3), .X(c2), .Y_num(3'b011), .X_num(3'b010), .MAX(max_2_max), .Max_num(max_2_max_num));
  MAX max_3 (.Y(c5), .X(c4), .Y_num(3'b101), .X_num(3'b100), .MAX(max_3_max), .Max_num(max_3_max_num));
  MAX max_4 (.Y(c7), .X(c6), .Y_num(3'b111), .X_num(3'b110), .MAX(max_4_max), .Max_num(max_4_max_num));
  or or_9 (EX_Hit, M0, M1, M2, M3, M4, M5, M6, M7);
  not not_9 (EX_Miss, EX_Hit);
  Priority_Encoder #(.select(3), .disabled("Z")) priority_encoder_1 (
    .in0(not_1_out), .in1(not_2_out), .in2(not_3_out), .in3(not_4_out), .in4(not_5_out), .in5(not_6_out),
    .in6(not_7_out), .in7(not_8_out), .out(priority_encoder_1_out), .gs(priority_encoder_1_gs));  // open: en_out, en_in
  MAX max_5 (
    .Y(max_2_max), .X(max_1_max), .Y_num(max_2_max_num), .X_num(max_1_max_num), .MAX(max_5_max),
    .Max_num(max_5_max_num));
  MAX max_6 (
    .Y(max_4_max), .X(max_3_max), .Y_num(max_4_max_num), .X_num(max_3_max_num), .MAX(max_6_max),
    .Max_num(max_6_max_num));
  and and_17 (and_17_out, v0, v1, v2, v3, v4, v5, v6, v7);
  Decoder #(.select(3), .tristate("false"), .disabled(0), .enable("true")) decoder_1 (
    .out0(decoder_1_out0), .out1(decoder_1_out1), .out2(decoder_1_out2), .out3(decoder_1_out3),
    .out4(decoder_1_out4), .out5(decoder_1_out5), .out6(decoder_1_out6), .out7(decoder_1_out7),
    .sel(priority_encoder_1_out), .en(priority_encoder_1_gs));
  Decoder #(.select(3), .tristate("false"), .disabled(0), .enable("true")) decoder_2 (
    .out0(decoder_2_out0), .out1(decoder_2_out1), .out2(decoder_2_out2), .out3(decoder_2_out3),
    .out4(decoder_2_out4), .out5(decoder_2_out5), .out6(decoder_2_out6), .out7(decoder_2_out7),
    .sel(max_7_max_num), .en(and_17_out));
  MAX max_7 (
    .Y(max_6_max), .X(max_5_max), .Y_num(max_6_max_num), .X_num(max_5_max_num), .Max_num(max_7_max_num));  // open: MAX
  or or_10 (original, v0, v1, v2, v3, v4, v5, v6, v7);
  or or_11 (or_11_out, decoder_1_out0, decoder_2_out0);
  or or_12 (or_12_out, decoder_1_out1, decoder_2_out1);
  or or_13 (or_13_out, decoder_1_out2, decoder_2_out2);
  or or_14 (or_14_out, decoder_1_out3, decoder_2_out3);
  or or_15 (or_15_out, decoder_1_out4, decoder_2_out4);
  or or_16 (or_16_out, decoder_1_out5, decoder_2_out5);
  or or_17 (or_17_out, decoder_1_out6, decoder_2_out6);
  or or_18 (or_18_out, decoder_1_out7, decoder_2_out7);
  and and_18 (write0, or_11_out, EX_Miss, EX_Branch);
  and and_19 (write1, or_12_out, EX_Miss, EX_Branch);
  and and_20 (write2, or_13_out, EX_Miss, EX_Branch);
  and and_21 (write3, or_14_out, EX_Miss, EX_Branch);
  and and_22 (write4, or_15_out, EX_Miss, EX_Branch);
  and and_23 (write5, or_16_out, EX_Miss, EX_Branch);
  and and_24 (write6, or_17_out, EX_Miss, EX_Branch);
  and and_25 (write7, or_18_out, EX_Miss, EX_Branch);
  assign {ID_PredictJump, controlled_buffer_9_out[0]} = L0 ? predict0 : 2'bz;  // Controlled_Buffer controlled_buffer_9
  assign {ID_PredictJump, controlled_buffer_10_out[0]} = L1 ? predict1 : 2'bz;  // Controlled_Buffer controlled_buffer_10
  assign {ID_PredictJump, controlled_buffer_11_out[0]} = L2 ? predict2 : 2'bz;  // Controlled_Buffer controlled_buffer_11
  assign {ID_PredictJump, controlled_buffer_12_out[0]} = L3 ? predict3 : 2'bz;  // Controlled_Buffer controlled_buffer_12
  assign {ID_PredictJump, controlled_buffer_13_out[0]} = L4 ? predict4 : 2'bz;  // Controlled_Buffer controlled_buffer_13
  assign {ID_PredictJump, controlled_buffer_14_out[0]} = L5 ? predict5 : 2'bz;  // Controlled_Buffer controlled_buffer_14
  assign {ID_PredictJump, controlled_buffer_15_out[0]} = L6 ? predict6 : 2'bz;  // Controlled_Buffer controlled_buffer_15
  assign {ID_PredictJump, controlled_buffer_16_out[0]} = L7 ? predict7 : 2'bz;  // Controlled_Buffer controlled_buffer_16
  Pull_Resistor #(.pull(0)) pull_resistor_1 (.node(ID_PredictJump));
  and and_26 (and_26_out, EX_Branch, M0);
  FSM fsm_1 (
    .high(multiplexer_1_out[1]), .low(multiplexer_1_out[0]), .jump(EX_Branched), .NextHigh(fsm_1_nextlow[1]),
    .NextLow(fsm_1_nextlow[0]));
  and and_27 (and_27_out, EX_Branch, M1);
  FSM fsm_2 (
    .high(multiplexer_2_out[1]), .low(multiplexer_2_out[0]), .jump(EX_Branched), .NextHigh(fsm_2_nextlow[1]),
    .NextLow(fsm_2_nextlow[0]));
  and and_28 (and_28_out, EX_Branch, M2);
  FSM fsm_3 (
    .high(multiplexer_3_out[1]), .low(multiplexer_3_out[0]), .jump(EX_Branched), .NextHigh(fsm_3_nextlow[1]),
    .NextLow(fsm_3_nextlow[0]));
  and and_29 (and_29_out, EX_Branch, M3);
  FSM fsm_4 (
    .high(multiplexer_4_out[1]), .low(multiplexer_4_out[0]), .jump(EX_Branched), .NextHigh(fsm_4_nextlow[1]),
    .NextLow(fsm_4_nextlow[0]));
  and and_30 (and_30_out, EX_Branch, M4);
  FSM fsm_5 (
    .high(multiplexer_5_out[1]), .low(multiplexer_5_out[0]), .jump(EX_Branched), .NextHigh(fsm_5_nextlow[1]),
    .NextLow(fsm_5_nextlow[0]));
  and and_31 (and_31_out, EX_Branch, M5);
  FSM fsm_6 (
    .high(multiplexer_6_out[1]), .low(multiplexer_6_out[0]), .jump(EX_Branched), .NextHigh(fsm_6_nextlow[1]),
    .NextLow(fsm_6_nextlow[0]));
  and and_32 (and_32_out, EX_Branch, M6);
  FSM fsm_7 (
    .high(multiplexer_7_out[1]), .low(multiplexer_7_out[0]), .jump(EX_Branched), .NextHigh(fsm_7_nextlow[1]),
    .NextLow(fsm_7_nextlow[0]));
  and and_33 (and_33_out, EX_Branch, M7);
  FSM fsm_8 (
    .high(multiplexer_8_out[1]), .low(multiplexer_8_out[0]), .jump(EX_Branched), .NextHigh(fsm_8_nextlow[1]),
    .NextLow(fsm_8_nextlow[0]));
  Multiplexer #(.select(1), .width(2), .disabled("Z"), .enable("false")) multiplexer_1 (
    .in0(2'b01), .in1(predict0), .out(multiplexer_1_out), .sel(original));
  Register #(.width(2), .trigger("rising"), .Select("low")) register_25 (
    .D(fsm_1_nextlow), .en(and_26_out), .Q(predict0), .clk(in_6));  // open: clr
  Multiplexer #(.select(1), .width(2), .disabled("Z"), .enable("false")) multiplexer_2 (
    .in0(2'b01), .in1(predict1), .out(multiplexer_2_out), .sel(original));
  Register #(.width(2), .trigger("rising"), .Select("low")) register_26 (
    .D(fsm_2_nextlow), .en(and_27_out), .Q(predict1), .clk(in_6));  // open: clr
  Multiplexer #(.select(1), .width(2), .disabled("Z"), .enable("false")) multiplexer_3 (
    .in0(2'b01), .in1(predict2), .out(multiplexer_3_out), .sel(original));
  Register #(.width(2), .trigger("rising"), .Select("low")) register_27 (
    .D(fsm_3_nextlow), .en(and_28_out), .Q(predict2), .clk(in_6));  // open: clr
  Multiplexer #(.select(1), .width(2), .disabled("Z"), .enable("false")) multiplexer_4 (
    .in0(2'b01), .in1(predict3), .out(multiplexer_4_out), .sel(original));
  Register #(.width(2), .trigger("rising"), .Select("low")) register_28 (
    .D(fsm_4_nextlow), .en(and_29_out), .Q(predict3), .clk(in_6));  // open: clr
  Multiplexer #(.select(1), .width(2), .disabled("Z"), .enable("false")) multiplexer_5 (
    .in0(2'b01), .in1(predict4), .out(multiplexer_5_out), .sel(original));
  Register #(.width(2), .trigger("rising"), .Select("low")) register_29 (
    .D(fsm_5_nextlow), .en(and_30_out), .Q(predict4), .clk(in_6));  // open: clr
  Multiplexer #(.select(1), .width(2), .disabled("Z"), .enable("false")) multiplexer_6 (
    .in0(2'b01), .in1(predict5), .out(multiplexer_6_out), .sel(original));
  Register #(.width(2), .trigger("rising"), .Select("low")) register_30 (
    .D(fsm_6_nextlow), .en(and_31_out), .Q(predict5), .clk(in_6));  // open: clr
  Multiplexer #(.select(1), .width(2), .disabled("Z"), .enable("false")) multiplexer_7 (
    .in0(2'b01), .in1(predict6), .out(multiplexer_7_out), .sel(original));
  Register #(.width(2), .trigger("rising"), .Select("low")) register_31 (
    .D(fsm_7_nextlow), .en(and_32_out), .Q(predict6), .clk(in_6));  // open: clr
  Multiplexer #(.select(1), .width(2), .disabled("Z"), .enable("false")) multiplexer_8 (
    .in0(2'b01), .in1(predict7), .out(multiplexer_8_out), .sel(original));
  Register #(.width(2), .trigger("rising"), .Select("low")) register_32 (
    .D(fsm_8_nextlow), .en(and_33_out), .Q(predict7), .clk(in_6));  // open: clr

  // Other names for the same wires on the sheet: CLK = in_6; Tag[31:0] = EX_PC

  // Notes on the sheet:
  //   EX写入逻辑
  //   历史预测位
  //   与PC比较数据命中  选择L而不是M
  //   EX.PC如果数据命中，需要根据EX.Branched的值依据预测位状态机更新分支预测历史位的值
endmodule

module MAX (
  input  [15:0] Y,
  input  [15:0] X,
  input  [2:0] Y_num,
  input  [2:0] X_num,
  output [15:0] MAX,
  output [2:0] Max_num
);

  wire comparator_1_eq, comparator_1_gt, or_1_out;

  Comparator #(.width(16), .mode("unsigned")) comparator_1 (
    .a(X), .b(Y), .gt(comparator_1_gt), .eq(comparator_1_eq));  // open: lt
  Multiplexer #(.select(1), .width(16), .disabled("Z"), .enable("false")) multiplexer_1 (
    .in0(Y), .in1(X), .out(MAX), .sel(or_1_out));
  or or_1 (or_1_out, comparator_1_gt, comparator_1_eq);
  Multiplexer #(.select(1), .width(3), .disabled("Z"), .enable("false")) multiplexer_2 (
    .in0(Y_num), .in1(X_num), .out(Max_num), .sel(or_1_out));

  // Notes on the sheet:
  //   输出两个输入中的较大值，并输出较大值的3位编号
endmodule

module FSM (
  input  high,
  input  low,
  input  jump,
  output NextHigh,
  output NextLow
);

  wire and_1_out, and_2_out, and_3_out, and_4_out, not_1_out, not_2_out, not_3_out, not_4_out, not_5_out;

  not not_1 (not_1_out, low);
  not not_2 (not_2_out, high);
  not not_3 (not_3_out, low);
  not not_4 (not_4_out, low);
  not not_5 (not_5_out, jump);
  and and_1 (and_1_out, low, jump);
  and and_2 (and_2_out, high, not_1_out);
  and and_3 (and_3_out, not_2_out, not_3_out, jump);
  and and_4 (and_4_out, high, not_4_out, not_5_out);
  or or_1 (NextHigh, and_1_out, and_2_out);
  or or_2 (NextLow, and_3_out, and_4_out);
endmodule
